// Logisim project cpu21-riscv_pipeline_interru.circ as structural Verilog: 26 circuits, main circuit ◇单周期RISC-V
module \单周期RISC_V  (
  input  IR1,
  input  IR2,
  input  IR3,
  output RegWrite,
  output MemWrite,
  output [31:0] PC,
  output [31:0] IR,
  output [31:0] RDin,
  output [31:0] MDin,
  output [31:0] LedData
);

  wire AluSrcB, and_2_out, and_3_out, and_4_out, and_5_out, and_7_out, B_Src, Beq, BGEU, Bne, Byte, CLK,
       clock_1_out, comparator_1_eq, comparator_1_lt, comparator_2_eq, d_ff_1_q, ecall, ecallFB, Equ, Go,
       GreEqu, halt, IR1_t, IR2_t, IR3_t, IRA, IRB, IRC, JAL, JALR, MemToReg, nand_1_out, not_1_out,
       not_2_out, not_3_out, not_4_out, not_5_out, or_1_out, or_6_out, RST, S_type, U_type, URET, W1, W2, W3,
       \单周期硬布线控制器_1_ecall ;
  wire [3:0] AluOP;
  wire [4:0] multiplexer_4_out, multiplexer_5_out;
  wire [7:0] Mem_byte;
  wire [12:0] CNT_num;
  wire [15:0] counter_2_q, \总周期数 ;
  wire [31:0] bit_extender_1_out, bit_extender_2_out, bit_extender_3_out, bit_extender_4_out,
       bit_extender_5_out, bit_extender_6_out, imm_U, Mem, multiplexer_1_out, multiplexer_2_out,
       multiplexer_3_out, multiplexer_6_out, multiplexer_7_out, multiplexer_8_out, multiplexer_9_out,
       multiplexer_10_out, multiplexer_12_out, PC_4, PC_B, PC_J, R1, Result, shifter_1_out, shifter_2_out;

  Button \u_继续运行  (.out(Go));
  Button _1 (.out(IRA));
  Button _2 (.out(IRB));
  Button _3 (.out(IRC));
  LED #(.active("true")) led_1 (.in(W1));
  LED #(.active("true")) led_2 (.in(W2));
  LED #(.active("true")) led_3 (.in(W3));
  Button button_1 (.out(RST));
  Multiplexer #(.select(1), .width(32), .disabled("Z"), .enable("false")) multiplexer_1 (
    .in0(PC_4), .in1(Result), .out(multiplexer_1_out), .sel(JALR));
  Hex_Digit_Display hex_digit_display_1 (.value(LedData[31:28]));  // open: dp
  Multiplexer #(.select(1), .width(32), .disabled("Z"), .enable("false")) multiplexer_2 (
    .in0(multiplexer_1_out), .in1(PC_J), .out(multiplexer_2_out), .sel(JAL));
  not not_1 (not_1_out, halt);
  or or_1 (or_1_out, U_type, Byte, BGEU);
  Hex_Digit_Display hex_digit_display_2 (.value(LedData[27:24]));  // open: dp
  Hex_Digit_Display hex_digit_display_3 (.value(LedData[23:20]));  // open: dp
  not not_2 (not_2_out, halt);
  Counter #(.width(16), .max('hffff), .ongoal("wrap"), .trigger("rising"), .behavior("new")) counter_1 (
    .count(not_2_out), .Q(\总周期数 ), .clk(CLK), .clr(RST));  // open: load, D, carry, preset, down
  Multiplexer #(.select(1), .width(32), .disabled("Z"), .enable("false")) multiplexer_3 (
    .in0(multiplexer_2_out), .in1(PC_B), .out(multiplexer_3_out), .sel(B_Src));
  not not_3 (not_3_out, halt);
  Counter #(.width(16), .max('hffff), .ongoal("wrap"), .trigger("rising"), .behavior("new")) counter_2 (
    .count(not_1_out), .Q(counter_2_q), .clk(or_1_out), .clr(RST));  // open: load, D, carry, preset, down
  // Probe on counter_2_q
  Hex_Digit_Display hex_digit_display_4 (.value(LedData[15:12]));  // open: dp
  Hex_Digit_Display hex_digit_display_5 (.value(LedData[19:16]));  // open: dp
  Register #(.width(32), .trigger("rising"), .Select("low")) u_PC (
    .D(multiplexer_3_out), .en(not_3_out), .Q(PC), .clk(CLK), .clr(RST));
  Hex_Digit_Display hex_digit_display_6 (.value(LedData[11:8]));  // open: dp
  Hex_Digit_Display hex_digit_display_7 (.value(LedData[7:4]));  // open: dp
  // Probe on \总周期数 
  Adder #(.width(32)) adder_1 (.a(PC), .b(32'h4), .out(PC_4), .cin(1'b0));  // open: cout
  Hex_Digit_Display hex_digit_display_8 (.value(LedData[3:0]));  // open: dp
  // RiscV_Probe riscv_probe_1: pin names not known; wires that end beside it: IR
  ROM #(.addrWidth(10), .dataWidth(32), .Select("high")) rom_1 (.addr(PC[11:2]), .data(IR));
  or or_2 (IR1_t, IR1, IRA);
  and and_1 (ecall, ~ecallFB, \单周期硬布线控制器_1_ecall );  // AND_Gate
  assign bit_extender_1_out = {{20{IR[31]}}, {IR[31:25], IR[11:7]}};  // Bit_Extender bit_extender_1
  or or_3 (IR2_t, IR2, IRB);
  \单周期硬布线控制器  \u_单周期硬布线控制器_1  (
    .Funct({IR[30], IR[25], IR[14:12]}), .OP(IR[6:2]), .ALU_OP(AluOP), .MemToReg(MemToReg),
    .MemWrite(MemWrite), .ALU_SRC(AluSrcB), .RegWrite(RegWrite), .ecall(\单周期硬布线控制器_1_ecall ),
    .S_type(S_type), .Jalr(JALR), .Beq(Beq), .JAL(JAL), .Bne(Bne), .in_3(IR[21]), .uret(URET),
    .U_ype(U_type), .Byte(Byte), .BGEU(BGEU));
  assign bit_extender_2_out = {{20{IR[31]}}, IR[31:20]};  // Bit_Extender bit_extender_2
  assign bit_extender_3_out = {{20{IR[31]}}, {IR[31], IR[7], IR[30:25], IR[11:8]}};  // Bit_Extender bit_extender_3
  assign bit_extender_4_out = {{12{IR[31]}}, {IR[31], IR[19:12], IR[20], IR[30:21]}};  // Bit_Extender bit_extender_4
  assign bit_extender_5_out = {{12{IR[31]}}, IR[31:12]};  // Bit_Extender bit_extender_5
  Multiplexer #(.select(1), .width(5), .disabled("Z"), .enable("false")) multiplexer_4 (
    .in0(IR[19:15]), .in1(5'b10001), .out(multiplexer_4_out), .sel(ecall));
  Multiplexer #(.select(1), .width(5), .disabled("Z"), .enable("false")) multiplexer_5 (
    .in0(IR[24:20]), .in1(5'b01010), .out(multiplexer_5_out), .sel(ecall));
  Multiplexer #(.select(1), .width(32), .disabled("Z"), .enable("false")) multiplexer_6 (
    .in0(bit_extender_2_out), .in1(bit_extender_1_out), .out(multiplexer_6_out), .sel(S_type));
  Shifter #(.width(32), .shift("ll")) shifter_1 (.in(bit_extender_3_out), .\dist (5'b00001), .out(shifter_1_out));
  Shifter #(.width(32), .shift("ll")) shifter_2 (.in(bit_extender_4_out), .\dist (5'b00001), .out(shifter_2_out));
  Shifter #(.width(32), .shift("ll")) shifter_3 (.in(bit_extender_5_out), .\dist (5'b10010), .out(imm_U));
  or or_4 (IR3_t, IR3, IRC);
  Regifile regifile_1 (
    .Din(RDin), .Clk(CLK), .R1(R1), .R2(MDin), .WE(RegWrite), .W_num(IR[11:7]), .R1_num(multiplexer_4_out),
    .R2_num(multiplexer_5_out));
  Multiplexer #(.select(1), .width(32), .disabled("Z"), .enable("false")) multiplexer_7 (
    .in0(multiplexer_6_out), .in1(imm_U), .out(multiplexer_7_out), .sel(U_type));
  Adder #(.width(32)) adder_2 (.a(shifter_1_out), .b(PC), .out(PC_B), .cin(1'b0));  // open: cout
  Adder #(.width(32)) adder_3 (.a(shifter_2_out), .b(PC), .out(PC_J), .cin(1'b0));  // open: cout
  Multiplexer #(.select(1), .width(32), .disabled("Z"), .enable("false")) multiplexer_8 (
    .in0(R1), .in1({32{1'b0}}), .out(multiplexer_8_out), .sel(U_type));
  Multiplexer #(.select(1), .width(32), .disabled("Z"), .enable("false")) multiplexer_9 (
    .in0(MDin), .in1(multiplexer_7_out), .out(multiplexer_9_out), .sel(AluSrcB));
  ALU alu_1 (
    .X(multiplexer_8_out), .Y(multiplexer_9_out), .AluOP(AluOP), .Equal(Equ), .Result(Result), .out_4(GreEqu));  // open: Result_2, out_6
  not not_4 (not_4_out, Equ);
  and and_2 (and_2_out, Equ, Beq);
  and and_3 (and_3_out, Bne, not_4_out);
  and and_4 (and_4_out, BGEU, GreEqu);
  or or_5 (B_Src, and_2_out, and_3_out, and_4_out);
  RAM #(.addrWidth(10), .dataWidth(32), .bus("separate"), .Select("high")) ram_1 (
    .addr(Result[11:2]), .din(MDin), .data(Mem), .str(MemWrite), .sel(1'b1), .clk(CLK), .ld(1'b1), .clr(RST));
  D_Flip_Flop #(.trigger("high"), .Pre_Clr_Positions("LEGACY"), .NegatePresetClear("false"), .enable("true"), .NewFFLayout("false")) d_ff_1 (.Q(d_ff_1_q));  // open: clk, D, Qn, preset, en, reset
  // Probe on 13'h608
  Comparator #(.width(13), .mode("twosComplement")) comparator_1 (
    .a(CNT_num), .b(13'h608), .eq(comparator_1_eq), .lt(comparator_1_lt));  // open: gt
  Clock #(.highDuration(1), .lowDuration(1)) clock_1 (.out(clock_1_out));
  Multiplexer #(.select(1), .width(32), .disabled("Z"), .enable("false")) multiplexer_10 (
    .in0(Result), .in1(Mem), .out(multiplexer_10_out), .sel(MemToReg));
  Comparator #(.width(32), .mode("twosComplement")) comparator_2 (
    .a(R1), .b(32'h22), .eq(comparator_2_eq));  // open: gt, lt
  Counter #(.width(13), .max('h1fff), .ongoal("stay"), .trigger("rising"), .behavior("old")) counter_3 (
    .count(comparator_1_lt), .Q(CNT_num), .clk(clock_1_out), .clr(RST));  // open: load, D, carry, preset
  Multiplexer #(.select(2), .width(8), .disabled("Z"), .enable("false")) multiplexer_11 (
    .in0(Mem[7:0]), .in1(Mem[15:8]), .in2(Mem[23:16]), .in3(Mem[31:24]), .out(Mem_byte), .sel(Result[1:0]));
  and and_5 (and_5_out, ecall, comparator_2_eq);
  not not_5 (not_5_out, comparator_2_eq);
  and and_6 (halt, not_5_out, ecall);
  Counter #(.width(1), .max('h1), .ongoal("stay"), .trigger("rising"), .behavior("new")) counter_4 (
    .D(and_7_out), .Q(ecallFB), .clk(and_7_out), .clr(RST));  // open: load, count, carry, preset, down
  and and_7 (and_7_out, Go, halt);
  nand nand_1 (nand_1_out, d_ff_1_q, comparator_1_eq);
  assign bit_extender_6_out = {{24{Mem_byte[7]}}, Mem_byte};  // Bit_Extender bit_extender_6
  Register #(.width(32), .trigger("rising"), .Select("low")) register_1 (
    .D(MDin), .en(and_5_out), .Q(LedData), .clk(CLK), .clr(RST));
  assign CLK = nand_1_out ? clock_1_out : 1'bz;  // Controlled_Buffer controlled_buffer_1
  Pull_Resistor #(.pull(1)) pull_resistor_1 (.node(CLK));
  Multiplexer #(.select(1), .width(32), .disabled("Z"), .enable("false")) multiplexer_12 (
    .in0(multiplexer_10_out), .in1(bit_extender_6_out), .out(multiplexer_12_out), .sel(Byte));
  or or_6 (or_6_out, JALR, JAL);
  Multiplexer #(.select(1), .width(32), .disabled("Z"), .enable("false")) multiplexer_13 (
    .in0(multiplexer_12_out), .in1(PC_4), .out(RDin), .sel(or_6_out));

  // Other names for the same wires on the sheet: R2[31:0] = MDin

  // Notes on the sheet:
  //   中断源
  //   中断等待指示
  //   数码管输出应该用寄存器锁存，否则显示数据只能一闪而过
  //   数码管输出
  //   指令探针
  //   指令存储器
  //   指令字
  //   contents of rom_1 (hex, n*v repeats v):
  //   100493 100006f 100493 200913 300993 100006f 100493 200913 300993 100006f 100493 200913 300993
  //   100006f 100493 200913 300993 29c000ef 100413 100493 1f49493 900533 2200893 73 24d493 48463 fedff06f
  //   900533 2200893 73 100493 249493 900533 2200893 73 48463 fedff06f 100493 1f49493 900533 2200893 73
  //   4034d493 900533 2200893 73 4044d493 900533 2200893 73 4044d493 900533 2200893 73 4044d493 900533
  //   2200893 73 4044d493 900533 2200893 73 4044d493 900533 2200893 73 4044d493 900533 2200893 73 4044d493
  //   900533 2200893 73 100413 1f41993 41f9d993 433 c00913 300b13 140413 f47413 800293 100313 499993
  //   89e9b3 1300533 2200893 73 406282b3 fe0294e3 140413 f00f93 1f47433 1c41413 800293 100313 49d993
  //   89e9b3 1300533 2200893 73 406282b3 fe0294e3 1c45413 406b0b33 b0463 f95ff06f 2b3 fff2c293 829293
  //   ff2e293 500533 2200893 73 fff00413 493 84a023 140413 448493 84a023 140413 448493 84a023 140413
  //   448493 84a023 140413 448493 84a023 140413 448493 84a023 140413 448493 84a023 140413 448493 84a023
  //   140413 448493 84a023 140413 448493 84a023 140413 448493 84a023 140413 448493 84a023 140413 448493
  //   84a023 140413 448493 84a023 140413 448493 84a023 140413 448493 84a023 140413 448493 140413 433
  //   3c00493 42983 4aa03 149a2b3 28663 134a023 1442023 ffc48493 fe9412e3 800533 2200893 73 440413 3c00493
  //   fc9416e3 a00893 73 413 140413 800533 2200893 73 240413 800533 2200893 73 340413 800533 2200893 73
  //   440413 800533 2200893 73 540413 800533 2200893 73 640413 800533 2200893 73 740413 800533 2200893 73
  //   840413 800533 2200893 2200893 73 8067
  //   JAL
  //   JALR
  //   URET
  //   I立即数
  //   S立即数
  //   B立即数
  //   J立即数
  //   U立即数
  //   Beq
  //   Bne
  //   MemToReg
  //   MemWrite
  //   AluOP
  //   AluSrcB
  //   RegWrite
  //   为方便自动评测，需要输出PC，IR，寄存器堆写如数据RDin
  //   RAM写使能MemWrite、RAM写入数据MDin等信号
  //   数据存储器
  //   控制位
  //   暂停节拍，不能为0
  //   戳工具置1进入计数暂停模式，ctrl+k时钟自动运行到对应节拍暂停
  //   ctrl+k关闭时钟连续运行，将控制位置零，进入单步调试模式调试
  //   用这个时钟源需要去掉电路中的其他时钟源
  //   ecall指令相关
  //   可计数暂停的时钟源
endmodule

// 单周期硬布线控制器
module \单周期硬布线控制器  (
  input  [4:0] OP,
  input  [4:0] Funct,
  input  in_3,
  output [3:0] ALU_OP,
  output uret,
  output MemToReg,
  output ecall,
  output MemWrite,
  output ALU_SRC,
  output RegWrite,
  output S_type,
  output Beq,
  output Bne,
  output Jalr,
  output JAL,
  output U_ype,
  output Byte,
  output BGEU
);

  wire \控制信号自动生成_1_ecall ;

  \运算控制器自动生成  \u_运算控制器自动生成_1  (
    .OP2(OP[0]), .OP3(OP[1]), .OP4(OP[2]), .OP5(OP[3]), .OP6(OP[4]), .F12(Funct[0]), .F13(Funct[1]),
    .F14(Funct[2]), .F25(Funct[3]), .F30(Funct[4]), .S0(ALU_OP[0]), .S1(ALU_OP[1]), .S2(ALU_OP[2]),
    .S3(ALU_OP[3]));
  \控制信号自动生成  \u_控制信号自动生成_1  (
    .OP2(OP[0]), .OP3(OP[1]), .MemToReg(MemToReg), .OP4(OP[2]), .OP5(OP[3]), .OP6(OP[4]), .F12(Funct[0]),
    .F13(Funct[1]), .MemWrite(MemWrite), .F14(Funct[2]), .F25(Funct[3]), .F30(Funct[4]), .ALU_SRC(ALU_SRC),
    .RegWrite(RegWrite), .ecall(\控制信号自动生成_1_ecall ), .S_Type(S_type), .BEQ(Beq), .BNE(Bne), .JALR(Jalr),
    .JAL(JAL), .U_type(U_ype), .Byte(Byte), .BGEU(BGEU));
  and and_1 (uret, in_3, \控制信号自动生成_1_ecall );
  and and_2 (ecall, ~in_3, \控制信号自动生成_1_ecall );  // AND_Gate

  // Other names for the same wires on the sheet: IR21 = in_3; OP_CODE[4:0] = OP

  // Notes on the sheet:
  //   运算器控制器，根据指令生成运算器功能选择信号
  //   控制信号生成，产生数据通路需要的其他控制信号
endmodule

// 运算器控制器
module \运算控制器自动生成  (
  input  OP2,
  input  OP3,
  input  OP4,
  input  OP5,
  input  OP6,
  input  F12,
  input  F13,
  input  F14,
  input  F25,
  input  F30,
  output S0,
  output S1,
  output S2,
  output S3
);

  wire and_1_out, and_2_out, and_3_out, and_4_out, and_5_out, and_6_out, and_7_out, and_8_out, and_9_out,
       and_10_out, and_11_out, and_12_out, and_13_out, and_14_out, and_15_out, and_16_out, and_17_out,
       and_18_out, and_19_out, and_20_out, and_21_out, and_22_out, and_23_out, and_24_out, and_25_out,
       and_26_out, and_27_out, and_28_out, and_29_out, and_30_out, and_31_out, and_32_out, and_33_out,
       and_34_out, and_35_out, and_36_out, and_37_out, and_38_out, and_39_out, and_40_out, not_1_out,
       not_2_out, not_3_out, not_4_out, not_5_out, not_6_out, not_7_out, not_8_out, not_9_out, not_10_out,
       not_11_out, not_12_out, not_13_out, not_14_out, not_15_out, not_16_out, not_17_out, not_18_out,
       not_19_out, not_20_out, not_21_out, not_22_out, not_23_out, not_24_out, not_25_out, not_26_out,
       not_27_out, not_28_out, not_29_out, not_30_out, not_31_out, not_32_out, not_33_out, not_34_out,
       not_35_out, not_36_out, not_37_out, not_38_out, not_39_out, not_40_out, not_41_out, not_42_out,
       not_43_out, not_44_out, not_45_out, not_46_out, not_47_out, not_48_out, not_49_out, not_50_out,
       not_51_out, not_52_out, not_53_out, not_54_out, not_55_out, not_56_out, not_57_out, not_58_out,
       not_59_out, not_60_out, not_61_out, not_62_out, not_63_out, not_64_out, not_65_out, not_66_out,
       not_67_out, not_68_out, not_69_out, not_70_out, not_71_out, not_72_out, not_73_out, not_74_out,
       not_75_out, not_76_out, not_77_out, not_78_out, not_79_out, not_80_out, not_81_out, not_82_out,
       not_83_out, not_84_out, not_85_out, not_86_out, not_87_out, not_88_out, not_89_out, not_90_out,
       not_91_out, not_92_out, not_93_out, not_94_out, not_95_out, not_96_out, not_97_out, not_98_out,
       not_99_out, not_100_out, not_101_out, not_102_out, not_103_out, not_104_out, not_105_out, not_106_out,
       not_107_out, not_108_out, not_109_out, not_110_out, not_111_out, not_112_out, not_113_out,
       not_114_out, not_115_out, not_116_out, not_117_out, not_118_out, not_119_out, not_120_out,
       not_121_out, not_122_out, not_123_out, not_124_out, not_125_out, not_126_out, not_127_out,
       not_128_out, not_129_out, not_130_out, not_131_out, not_132_out, not_133_out, not_134_out,
       not_135_out, not_136_out, not_137_out, not_138_out, not_139_out, not_140_out, not_141_out,
       not_142_out, not_143_out, not_144_out, not_145_out, not_146_out, not_147_out, not_148_out,
       not_149_out, not_150_out, not_151_out, not_152_out, not_153_out, not_154_out, not_155_out,
       not_156_out, not_157_out, not_158_out, not_159_out, not_160_out, not_161_out, not_162_out,
       not_163_out, not_164_out, not_165_out, not_166_out, not_167_out, not_168_out, not_169_out,
       not_170_out, not_171_out, not_172_out, not_173_out, not_174_out, not_175_out, not_176_out,
       not_177_out, not_178_out, not_179_out, not_180_out, not_181_out, not_182_out, not_183_out,
       not_184_out, not_185_out, not_186_out, not_187_out, not_188_out, not_189_out, not_190_out,
       not_191_out, not_192_out, not_193_out, not_194_out, not_195_out, not_196_out, not_197_out,
       not_198_out, not_199_out, not_200_out, not_201_out, not_202_out, not_203_out, not_204_out,
       not_205_out, not_206_out, not_207_out, not_208_out, not_209_out, not_210_out, not_211_out,
       not_212_out, not_213_out, not_214_out, not_215_out, not_216_out, not_217_out, not_218_out,
       not_219_out, not_220_out, not_221_out, not_222_out, not_223_out, not_224_out, not_225_out;

  not not_1 (not_1_out, F30);
  not not_2 (not_2_out, F25);
  not not_3 (not_3_out, F14);
  not not_4 (not_4_out, F13);
  not not_5 (not_5_out, F12);
  not not_6 (not_6_out, OP6);
  not not_7 (not_7_out, OP3);
  not not_8 (not_8_out, OP2);
  not not_9 (not_9_out, F30);
  not not_10 (not_10_out, F25);
  not not_11 (not_11_out, OP6);
  not not_12 (not_12_out, OP3);
  not not_13 (not_13_out, OP2);
  not not_14 (not_14_out, F30);
  not not_15 (not_15_out, F25);
  not not_16 (not_16_out, F14);
  not not_17 (not_17_out, F12);
  not not_18 (not_18_out, OP6);
  not not_19 (not_19_out, OP3);
  not not_20 (not_20_out, OP2);
  not not_21 (not_21_out, F14);
  not not_22 (not_22_out, F13);
  not not_23 (not_23_out, F12);
  not not_24 (not_24_out, OP6);
  not not_25 (not_25_out, OP5);
  not not_26 (not_26_out, OP3);
  not not_27 (not_27_out, OP2);
  not not_28 (not_28_out, OP6);
  not not_29 (not_29_out, OP5);
  not not_30 (not_30_out, OP3);
  not not_31 (not_31_out, OP2);
  not not_32 (not_32_out, F13);
  not not_33 (not_33_out, F12);
  not not_34 (not_34_out, OP6);
  not not_35 (not_35_out, OP5);
  not not_36 (not_36_out, OP3);
  not not_37 (not_37_out, OP2);
  not not_38 (not_38_out, F14);
  not not_39 (not_39_out, F12);
  not not_40 (not_40_out, OP6);
  not not_41 (not_41_out, OP5);
  not not_42 (not_42_out, OP3);
  not not_43 (not_43_out, OP2);
  not not_44 (not_44_out, F25);
  not not_45 (not_45_out, F13);
  not not_46 (not_46_out, OP6);
  not not_47 (not_47_out, OP5);
  not not_48 (not_48_out, OP3);
  not not_49 (not_49_out, OP2);
  not not_50 (not_50_out, F14);
  not not_51 (not_51_out, F12);
  not not_52 (not_52_out, OP6);
  not not_53 (not_53_out, OP5);
  not not_54 (not_54_out, OP4);
  not not_55 (not_55_out, OP3);
  not not_56 (not_56_out, OP2);
  not not_57 (not_57_out, F14);
  not not_58 (not_58_out, F12);
  not not_59 (not_59_out, OP6);
  not not_60 (not_60_out, OP4);
  not not_61 (not_61_out, OP3);
  not not_62 (not_62_out, OP2);
  not not_63 (not_63_out, OP3);
  not not_64 (not_64_out, OP2);
  not not_65 (not_65_out, F25);
  not not_66 (not_66_out, F14);
  not not_67 (not_67_out, F13);
  not not_68 (not_68_out, F12);
  not not_69 (not_69_out, OP6);
  not not_70 (not_70_out, OP3);
  not not_71 (not_71_out, OP2);
  not not_72 (not_72_out, F30);
  not not_73 (not_73_out, F25);
  not not_74 (not_74_out, OP6);
  not not_75 (not_75_out, OP3);
  not not_76 (not_76_out, OP2);
  not not_77 (not_77_out, F30);
  not not_78 (not_78_out, F25);
  not not_79 (not_79_out, F14);
  not not_80 (not_80_out, F12);
  not not_81 (not_81_out, OP6);
  not not_82 (not_82_out, OP3);
  not not_83 (not_83_out, OP2);
  not not_84 (not_84_out, OP6);
  not not_85 (not_85_out, OP5);
  not not_86 (not_86_out, OP3);
  not not_87 (not_87_out, OP2);
  not not_88 (not_88_out, F14);
  not not_89 (not_89_out, F12);
  not not_90 (not_90_out, OP6);
  not not_91 (not_91_out, OP5);
  not not_92 (not_92_out, OP3);
  not not_93 (not_93_out, OP2);
  not not_94 (not_94_out, F30);
  not not_95 (not_95_out, F25);
  not not_96 (not_96_out, F13);
  not not_97 (not_97_out, OP6);
  not not_98 (not_98_out, OP5);
  not not_99 (not_99_out, OP3);
  not not_100 (not_100_out, OP2);
  not not_101 (not_101_out, F14);
  not not_102 (not_102_out, F13);
  not not_103 (not_103_out, F12);
  not not_104 (not_104_out, OP4);
  not not_105 (not_105_out, OP3);
  not not_106 (not_106_out, OP2);
  not not_107 (not_107_out, F14);
  not not_108 (not_108_out, F13);
  not not_109 (not_109_out, OP4);
  not not_110 (not_110_out, OP3);
  not not_111 (not_111_out, OP2);
  not not_112 (not_112_out, F14);
  not not_113 (not_113_out, F13);
  not not_114 (not_114_out, F12);
  not not_115 (not_115_out, OP4);
  not not_116 (not_116_out, OP3);
  not not_117 (not_117_out, OP3);
  not not_118 (not_118_out, OP2);
  not not_119 (not_119_out, F30);
  not not_120 (not_120_out, F25);
  not not_121 (not_121_out, F14);
  not not_122 (not_122_out, F13);
  not not_123 (not_123_out, F12);
  not not_124 (not_124_out, OP6);
  not not_125 (not_125_out, OP3);
  not not_126 (not_126_out, OP2);
  not not_127 (not_127_out, F25);
  not not_128 (not_128_out, F14);
  not not_129 (not_129_out, F13);
  not not_130 (not_130_out, F12);
  not not_131 (not_131_out, OP6);
  not not_132 (not_132_out, OP3);
  not not_133 (not_133_out, OP2);
  not not_134 (not_134_out, F30);
  not not_135 (not_135_out, F25);
  not not_136 (not_136_out, OP6);
  not not_137 (not_137_out, OP3);
  not not_138 (not_138_out, OP2);
  not not_139 (not_139_out, F30);
  not not_140 (not_140_out, F25);
  not not_141 (not_141_out, F14);
  not not_142 (not_142_out, OP6);
  not not_143 (not_143_out, OP3);
  not not_144 (not_144_out, OP2);
  not not_145 (not_145_out, F14);
  not not_146 (not_146_out, F13);
  not not_147 (not_147_out, F12);
  not not_148 (not_148_out, OP6);
  not not_149 (not_149_out, OP5);
  not not_150 (not_150_out, OP3);
  not not_151 (not_151_out, OP2);
  not not_152 (not_152_out, OP6);
  not not_153 (not_153_out, OP5);
  not not_154 (not_154_out, OP3);
  not not_155 (not_155_out, OP2);
  not not_156 (not_156_out, F14);
  not not_157 (not_157_out, F12);
  not not_158 (not_158_out, OP6);
  not not_159 (not_159_out, OP5);
  not not_160 (not_160_out, OP4);
  not not_161 (not_161_out, OP3);
  not not_162 (not_162_out, OP2);
  not not_163 (not_163_out, F14);
  not not_164 (not_164_out, F12);
  not not_165 (not_165_out, OP6);
  not not_166 (not_166_out, OP4);
  not not_167 (not_167_out, OP3);
  not not_168 (not_168_out, OP2);
  not not_169 (not_169_out, F14);
  not not_170 (not_170_out, F13);
  not not_171 (not_171_out, F12);
  not not_172 (not_172_out, OP4);
  not not_173 (not_173_out, OP3);
  not not_174 (not_174_out, OP2);
  not not_175 (not_175_out, F14);
  not not_176 (not_176_out, F13);
  not not_177 (not_177_out, OP4);
  not not_178 (not_178_out, OP3);
  not not_179 (not_179_out, OP2);
  not not_180 (not_180_out, F14);
  not not_181 (not_181_out, F13);
  not not_182 (not_182_out, F12);
  not not_183 (not_183_out, OP4);
  not not_184 (not_184_out, OP3);
  not not_185 (not_185_out, OP3);
  not not_186 (not_186_out, OP2);
  not not_187 (not_187_out, F30);
  not not_188 (not_188_out, F25);
  not not_189 (not_189_out, F12);
  not not_190 (not_190_out, OP6);
  not not_191 (not_191_out, OP3);
  not not_192 (not_192_out, OP2);
  not not_193 (not_193_out, F30);
  not not_194 (not_194_out, F25);
  not not_195 (not_195_out, F14);
  not not_196 (not_196_out, F12);
  not not_197 (not_197_out, OP6);
  not not_198 (not_198_out, OP3);
  not not_199 (not_199_out, OP2);
  not not_200 (not_200_out, F30);
  not not_201 (not_201_out, F25);
  not not_202 (not_202_out, F14);
  not not_203 (not_203_out, OP6);
  not not_204 (not_204_out, OP3);
  not not_205 (not_205_out, OP2);
  not not_206 (not_206_out, F12);
  not not_207 (not_207_out, OP6);
  not not_208 (not_208_out, OP5);
  not not_209 (not_209_out, OP3);
  not not_210 (not_210_out, OP2);
  not not_211 (not_211_out, F13);
  not not_212 (not_212_out, F12);
  not not_213 (not_213_out, OP6);
  not not_214 (not_214_out, OP5);
  not not_215 (not_215_out, OP3);
  not not_216 (not_216_out, OP2);
  not not_217 (not_217_out, F14);
  not not_218 (not_218_out, F12);
  not not_219 (not_219_out, OP6);
  not not_220 (not_220_out, OP5);
  not not_221 (not_221_out, OP3);
  not not_222 (not_222_out, OP2);
  not not_223 (not_223_out, F12);
  not not_224 (not_224_out, OP3);
  not not_225 (not_225_out, OP2);
  and and_1 (and_1_out, not_1_out, not_2_out, not_3_out, not_4_out, not_5_out, not_6_out, OP5, OP4, not_7_out, not_8_out);
  and and_2 (and_2_out, not_9_out, not_10_out, F14, F13, F12, not_11_out, OP5, OP4, not_12_out, not_13_out);
  and and_3 (and_3_out, not_14_out, not_15_out, not_16_out, F13, not_17_out, not_18_out, OP5, OP4, not_19_out, not_20_out);
  and and_4 (and_4_out, not_21_out, not_22_out, not_23_out, not_24_out, not_25_out, OP4, not_26_out, not_27_out);
  and and_5 (and_5_out, F14, F13, F12, not_28_out, not_29_out, OP4, not_30_out, not_31_out);
  and and_6 (and_6_out, F14, not_32_out, not_33_out, not_34_out, not_35_out, OP4, not_36_out, not_37_out);
  and and_7 (and_7_out, not_38_out, F13, not_39_out, not_40_out, not_41_out, OP4, not_42_out, not_43_out);
  and and_8 (and_8_out, F30, not_44_out, F14, not_45_out, F12, not_46_out, not_47_out, OP4, not_48_out, not_49_out);
  and and_9 (and_9_out, not_50_out, F13, not_51_out, not_52_out, not_53_out, not_54_out, not_55_out, not_56_out);
  and and_10 (and_10_out, not_57_out, F13, not_58_out, not_59_out, OP5, not_60_out, not_61_out, not_62_out);
  and and_11 (and_11_out, F14, F13, F12, OP6, OP5, OP4, not_63_out, not_64_out);
  and and_12 (and_12_out, F30, not_65_out, not_66_out, not_67_out, not_68_out, not_69_out, OP5, OP4, not_70_out, not_71_out);
  and and_13 (and_13_out, not_72_out, not_73_out, F14, F13, F12, not_74_out, OP5, OP4, not_75_out, not_76_out);
  and and_14 (and_14_out, not_77_out, not_78_out, not_79_out, F13, not_80_out, not_81_out, OP5, OP4, not_82_out, not_83_out);
  and and_15 (and_15_out, F14, F13, F12, not_84_out, not_85_out, OP4, not_86_out, not_87_out);
  and and_16 (and_16_out, not_88_out, F13, not_89_out, not_90_out, not_91_out, OP4, not_92_out, not_93_out);
  and and_17 (and_17_out, not_94_out, not_95_out, F14, not_96_out, F12, not_97_out, not_98_out, OP4, not_99_out, not_100_out);
  and and_18 (and_18_out, not_101_out, not_102_out, not_103_out, OP6, OP5, not_104_out, not_105_out, not_106_out);
  and and_19 (and_19_out, not_107_out, not_108_out, F12, OP6, OP5, not_109_out, not_110_out, not_111_out);
  and and_20 (and_20_out, not_112_out, not_113_out, not_114_out, OP6, OP5, not_115_out, not_116_out, OP2);
  and and_21 (and_21_out, F14, F13, F12, OP6, OP5, OP4, not_117_out, not_118_out);
  and and_22 (and_22_out, not_119_out, not_120_out, not_121_out, not_122_out, not_123_out, not_124_out, OP5, OP4, not_125_out, not_126_out);
  and and_23 (and_23_out, F30, not_127_out, not_128_out, not_129_out, not_130_out, not_131_out, OP5, OP4, not_132_out, not_133_out);
  and and_24 (and_24_out, not_134_out, not_135_out, F14, F13, F12, not_136_out, OP5, OP4, not_137_out, not_138_out);
  and and_25 (and_25_out, not_139_out, not_140_out, not_141_out, F13, F12, not_142_out, OP5, OP4, not_143_out, not_144_out);
  and and_26 (and_26_out, not_145_out, not_146_out, not_147_out, not_148_out, not_149_out, OP4, not_150_out, not_151_out);
  and and_27 (and_27_out, F14, F13, F12, not_152_out, not_153_out, OP4, not_154_out, not_155_out);
  and and_28 (and_28_out, not_156_out, F13, not_157_out, not_158_out, not_159_out, not_160_out, not_161_out, not_162_out);
  and and_29 (and_29_out, not_163_out, F13, not_164_out, not_165_out, OP5, not_166_out, not_167_out, not_168_out);
  and and_30 (and_30_out, not_169_out, not_170_out, not_171_out, OP6, OP5, not_172_out, not_173_out, not_174_out);
  and and_31 (and_31_out, not_175_out, not_176_out, F12, OP6, OP5, not_177_out, not_178_out, not_179_out);
  and and_32 (and_32_out, not_180_out, not_181_out, not_182_out, OP6, OP5, not_183_out, not_184_out, OP2);
  and and_33 (and_33_out, F14, F13, F12, OP6, OP5, OP4, not_185_out, not_186_out);
  and and_34 (and_34_out, not_187_out, not_188_out, F14, F13, not_189_out, not_190_out, OP5, OP4, not_191_out, not_192_out);
  and and_35 (and_35_out, not_193_out, not_194_out, not_195_out, F13, not_196_out, not_197_out, OP5, OP4, not_198_out, not_199_out);
  and and_36 (and_36_out, not_200_out, not_201_out, not_202_out, F13, F12, not_203_out, OP5, OP4, not_204_out, not_205_out);
  and and_37 (and_37_out, F14, F13, not_206_out, not_207_out, not_208_out, OP4, not_209_out, not_210_out);
  and and_38 (and_38_out, F14, not_211_out, not_212_out, not_213_out, not_214_out, OP4, not_215_out, not_216_out);
  and and_39 (and_39_out, not_217_out, F13, not_218_out, not_219_out, not_220_out, OP4, not_221_out, not_222_out);
  and and_40 (and_40_out, F14, F13, not_223_out, OP6, OP5, OP4, not_224_out, not_225_out);
  or or_1 (S0, and_1_out, and_2_out, and_3_out, and_4_out, and_5_out, and_6_out, and_7_out, and_8_out, and_9_out, and_10_out, and_11_out);
  or or_2 (S1, and_12_out, and_13_out, and_14_out, and_15_out, and_16_out, and_17_out, and_18_out, and_19_out, and_20_out, and_21_out);
  or or_3 (S2, and_22_out, and_23_out, and_24_out, and_25_out, and_26_out, and_27_out, and_28_out, and_29_out, and_30_out, and_31_out, and_32_out, and_33_out);
  or or_4 (S3, and_34_out, and_35_out, and_36_out, and_37_out, and_38_out, and_39_out, and_40_out);
endmodule

// 控制信号生成
module \控制信号自动生成  (
  input  OP2,
  input  OP3,
  input  OP4,
  input  OP5,
  input  OP6,
  input  F12,
  input  F13,
  input  F14,
  input  F25,
  input  F30,
  output MemToReg,
  output MemWrite,
  output ALU_SRC,
  output RegWrite,
  output ecall,
  output S_Type,
  output BEQ,
  output BNE,
  output JALR,
  output JAL,
  output U_type,
  output Byte,
  output BGEU
);

  wire and_3_out, and_4_out, and_5_out, and_6_out, and_7_out, and_8_out, and_9_out, and_10_out, and_11_out,
       and_12_out, and_13_out, and_14_out, and_15_out, and_16_out, and_17_out, and_18_out, and_19_out,
       and_20_out, and_21_out, and_22_out, and_23_out, and_24_out, and_25_out, and_26_out, not_1_out,
       not_2_out, not_3_out, not_4_out, not_5_out, not_6_out, not_7_out, not_8_out, not_9_out, not_10_out,
       not_11_out, not_12_out, not_13_out, not_14_out, not_15_out, not_16_out, not_17_out, not_18_out,
       not_19_out, not_20_out, not_21_out, not_22_out, not_23_out, not_24_out, not_25_out, not_26_out,
       not_27_out, not_28_out, not_29_out, not_30_out, not_31_out, not_32_out, not_33_out, not_34_out,
       not_35_out, not_36_out, not_37_out, not_38_out, not_39_out, not_40_out, not_41_out, not_42_out,
       not_43_out, not_44_out, not_45_out, not_46_out, not_47_out, not_48_out, not_49_out, not_50_out,
       not_51_out, not_52_out, not_53_out, not_54_out, not_55_out, not_56_out, not_57_out, not_58_out,
       not_59_out, not_60_out, not_61_out, not_62_out, not_63_out, not_64_out, not_65_out, not_66_out,
       not_67_out, not_68_out, not_69_out, not_70_out, not_71_out, not_72_out, not_73_out, not_74_out,
       not_75_out, not_76_out, not_77_out, not_78_out, not_79_out, not_80_out, not_81_out, not_82_out,
       not_83_out, not_84_out, not_85_out, not_86_out, not_87_out, not_88_out, not_89_out, not_90_out,
       not_91_out, not_92_out, not_93_out, not_94_out, not_95_out, not_96_out, not_97_out, not_98_out,
       not_99_out, not_100_out, not_101_out, not_102_out, not_103_out, not_104_out, not_105_out, not_106_out,
       not_107_out, not_108_out, not_109_out, not_110_out, not_111_out, not_112_out, not_113_out,
       not_114_out, not_115_out, not_116_out, not_117_out, not_118_out, not_119_out, not_120_out,
       not_121_out, not_122_out, not_123_out, not_124_out, not_125_out, not_126_out, not_127_out,
       not_128_out, not_129_out, not_130_out, not_131_out, not_132_out, not_133_out, not_134_out,
       not_135_out, not_136_out, not_137_out, not_138_out, not_139_out, not_140_out, not_141_out,
       not_142_out, not_143_out, not_144_out, not_145_out, not_146_out, not_147_out, not_148_out,
       not_149_out, not_150_out, not_151_out, not_152_out, not_153_out, not_154_out, not_155_out,
       not_156_out, not_157_out, not_158_out, not_159_out, not_160_out, not_161_out, not_162_out,
       not_163_out, not_164_out, not_165_out, not_166_out, not_167_out, not_168_out, not_169_out,
       not_170_out, not_171_out, not_172_out, not_173_out, not_174_out, not_175_out, not_176_out,
       not_177_out, not_178_out, not_179_out, not_180_out, not_181_out, not_182_out, not_183_out,
       not_184_out, not_185_out, not_186_out, not_187_out, not_188_out, not_189_out, not_190_out, not_191_out;

  not not_1 (not_1_out, OP2);
  not not_2 (not_2_out, OP3);
  not not_3 (not_3_out, OP4);
  not not_4 (not_4_out, OP5);
  not not_5 (not_5_out, OP6);
  not not_6 (not_6_out, F12);
  not not_7 (not_7_out, F14);
  not not_8 (not_8_out, OP2);
  not not_9 (not_9_out, OP3);
  not not_10 (not_10_out, OP4);
  not not_11 (not_11_out, OP6);
  not not_12 (not_12_out, F12);
  not not_13 (not_13_out, F14);
  not not_14 (not_14_out, OP2);
  not not_15 (not_15_out, OP3);
  not not_16 (not_16_out, OP4);
  not not_17 (not_17_out, OP6);
  not not_18 (not_18_out, F12);
  not not_19 (not_19_out, F14);
  not not_20 (not_20_out, OP2);
  not not_21 (not_21_out, OP3);
  not not_22 (not_22_out, OP5);
  not not_23 (not_23_out, OP6);
  not not_24 (not_24_out, F12);
  not not_25 (not_25_out, OP2);
  not not_26 (not_26_out, OP3);
  not not_27 (not_27_out, OP5);
  not not_28 (not_28_out, OP6);
  not not_29 (not_29_out, F13);
  not not_30 (not_30_out, F25);
  not not_31 (not_31_out, F30);
  not not_32 (not_32_out, OP2);
  not not_33 (not_33_out, OP3);
  not not_34 (not_34_out, OP5);
  not not_35 (not_35_out, OP6);
  not not_36 (not_36_out, F25);
  not not_37 (not_37_out, OP2);
  not not_38 (not_38_out, OP3);
  not not_39 (not_39_out, OP5);
  not not_40 (not_40_out, OP6);
  not not_41 (not_41_out, OP2);
  not not_42 (not_42_out, OP3);
  not not_43 (not_43_out, OP3);
  not not_44 (not_44_out, OP4);
  not not_45 (not_45_out, F12);
  not not_46 (not_46_out, F13);
  not not_47 (not_47_out, F14);
  not not_48 (not_48_out, F30);
  not not_49 (not_49_out, F25);
  not not_50 (not_50_out, F14);
  not not_51 (not_51_out, F13);
  not not_52 (not_52_out, F12);
  not not_53 (not_53_out, OP6);
  not not_54 (not_54_out, OP3);
  not not_55 (not_55_out, OP2);
  not not_56 (not_56_out, F25);
  not not_57 (not_57_out, F14);
  not not_58 (not_58_out, F13);
  not not_59 (not_59_out, F12);
  not not_60 (not_60_out, OP6);
  not not_61 (not_61_out, OP3);
  not not_62 (not_62_out, OP2);
  not not_63 (not_63_out, F30);
  not not_64 (not_64_out, F25);
  not not_65 (not_65_out, OP6);
  not not_66 (not_66_out, OP3);
  not not_67 (not_67_out, OP2);
  not not_68 (not_68_out, F30);
  not not_69 (not_69_out, F25);
  not not_70 (not_70_out, F12);
  not not_71 (not_71_out, OP6);
  not not_72 (not_72_out, OP3);
  not not_73 (not_73_out, OP2);
  not not_74 (not_74_out, F30);
  not not_75 (not_75_out, F25);
  not not_76 (not_76_out, F14);
  not not_77 (not_77_out, F12);
  not not_78 (not_78_out, OP6);
  not not_79 (not_79_out, OP3);
  not not_80 (not_80_out, OP2);
  not not_81 (not_81_out, F30);
  not not_82 (not_82_out, F25);
  not not_83 (not_83_out, F14);
  not not_84 (not_84_out, OP6);
  not not_85 (not_85_out, OP3);
  not not_86 (not_86_out, OP2);
  not not_87 (not_87_out, F14);
  not not_88 (not_88_out, F13);
  not not_89 (not_89_out, F12);
  not not_90 (not_90_out, OP6);
  not not_91 (not_91_out, OP5);
  not not_92 (not_92_out, OP3);
  not not_93 (not_93_out, OP2);
  not not_94 (not_94_out, OP6);
  not not_95 (not_95_out, OP5);
  not not_96 (not_96_out, OP3);
  not not_97 (not_97_out, OP2);
  not not_98 (not_98_out, F12);
  not not_99 (not_99_out, OP6);
  not not_100 (not_100_out, OP5);
  not not_101 (not_101_out, OP3);
  not not_102 (not_102_out, OP2);
  not not_103 (not_103_out, F13);
  not not_104 (not_104_out, F12);
  not not_105 (not_105_out, OP6);
  not not_106 (not_106_out, OP5);
  not not_107 (not_107_out, OP3);
  not not_108 (not_108_out, OP2);
  not not_109 (not_109_out, F14);
  not not_110 (not_110_out, F12);
  not not_111 (not_111_out, OP6);
  not not_112 (not_112_out, OP5);
  not not_113 (not_113_out, OP3);
  not not_114 (not_114_out, OP2);
  not not_115 (not_115_out, F30);
  not not_116 (not_116_out, F25);
  not not_117 (not_117_out, F14);
  not not_118 (not_118_out, F13);
  not not_119 (not_119_out, OP6);
  not not_120 (not_120_out, OP5);
  not not_121 (not_121_out, OP3);
  not not_122 (not_122_out, OP2);
  not not_123 (not_123_out, F30);
  not not_124 (not_124_out, F25);
  not not_125 (not_125_out, F13);
  not not_126 (not_126_out, OP6);
  not not_127 (not_127_out, OP5);
  not not_128 (not_128_out, OP3);
  not not_129 (not_129_out, OP2);
  not not_130 (not_130_out, F25);
  not not_131 (not_131_out, F13);
  not not_132 (not_132_out, OP6);
  not not_133 (not_133_out, OP5);
  not not_134 (not_134_out, OP3);
  not not_135 (not_135_out, OP2);
  not not_136 (not_136_out, F14);
  not not_137 (not_137_out, F12);
  not not_138 (not_138_out, OP6);
  not not_139 (not_139_out, OP5);
  not not_140 (not_140_out, OP4);
  not not_141 (not_141_out, OP3);
  not not_142 (not_142_out, OP2);
  not not_143 (not_143_out, OP4);
  not not_144 (not_144_out, F14);
  not not_145 (not_145_out, F13);
  not not_146 (not_146_out, F12);
  not not_147 (not_147_out, OP4);
  not not_148 (not_148_out, OP3);
  not not_149 (not_149_out, OP2);
  not not_150 (not_150_out, OP3);
  not not_151 (not_151_out, F12);
  not not_152 (not_152_out, F13);
  not not_153 (not_153_out, F14);
  not not_154 (not_154_out, F25);
  not not_155 (not_155_out, F30);
  not not_156 (not_156_out, OP2);
  not not_157 (not_157_out, OP3);
  not not_158 (not_158_out, OP4);
  not not_159 (not_159_out, OP6);
  not not_160 (not_160_out, F12);
  not not_161 (not_161_out, F14);
  not not_162 (not_162_out, OP2);
  not not_163 (not_163_out, OP3);
  not not_164 (not_164_out, OP4);
  not not_165 (not_165_out, F12);
  not not_166 (not_166_out, F13);
  not not_167 (not_167_out, F14);
  not not_168 (not_168_out, OP2);
  not not_169 (not_169_out, OP3);
  not not_170 (not_170_out, OP4);
  not not_171 (not_171_out, F13);
  not not_172 (not_172_out, F14);
  not not_173 (not_173_out, OP3);
  not not_174 (not_174_out, OP4);
  not not_175 (not_175_out, F12);
  not not_176 (not_176_out, F13);
  not not_177 (not_177_out, F14);
  not not_178 (not_178_out, OP4);
  not not_179 (not_179_out, OP3);
  not not_180 (not_180_out, OP6);
  not not_181 (not_181_out, OP2);
  not not_182 (not_182_out, OP3);
  not not_183 (not_183_out, OP4);
  not not_184 (not_184_out, OP5);
  not not_185 (not_185_out, OP6);
  not not_186 (not_186_out, F12);
  not not_187 (not_187_out, F13);
  not not_188 (not_188_out, F14);
  not not_189 (not_189_out, OP2);
  not not_190 (not_190_out, OP3);
  not not_191 (not_191_out, OP4);
  and and_1 (MemToReg, not_1_out, not_2_out, not_3_out, not_4_out, not_5_out, not_6_out, F13, not_7_out);
  and and_2 (MemWrite, not_8_out, not_9_out, not_10_out, OP5, not_11_out, not_12_out, F13, not_13_out);
  and and_3 (and_3_out, not_14_out, not_15_out, not_16_out, not_17_out, not_18_out, F13, not_19_out);
  and and_4 (and_4_out, not_20_out, not_21_out, OP4, not_22_out, not_23_out, not_24_out);
  and and_5 (and_5_out, not_25_out, not_26_out, OP4, not_27_out, not_28_out, not_29_out, not_30_out, not_31_out);
  and and_6 (and_6_out, not_32_out, not_33_out, OP4, not_34_out, not_35_out, F14, not_36_out);
  and and_7 (and_7_out, not_37_out, not_38_out, OP4, not_39_out, not_40_out, F13, F14);
  and and_8 (and_8_out, not_41_out, not_42_out, OP4, OP5, OP6, F13, F14);
  and and_9 (and_9_out, OP2, not_43_out, not_44_out, OP5, OP6, not_45_out, not_46_out, not_47_out);
  and and_10 (and_10_out, not_48_out, not_49_out, not_50_out, not_51_out, not_52_out, not_53_out, OP5, OP4, not_54_out, not_55_out);
  and and_11 (and_11_out, F30, not_56_out, not_57_out, not_58_out, not_59_out, not_60_out, OP5, OP4, not_61_out, not_62_out);
  and and_12 (and_12_out, not_63_out, not_64_out, F14, F13, F12, not_65_out, OP5, OP4, not_66_out, not_67_out);
  and and_13 (and_13_out, not_68_out, not_69_out, F14, F13, not_70_out, not_71_out, OP5, OP4, not_72_out, not_73_out);
  and and_14 (and_14_out, not_74_out, not_75_out, not_76_out, F13, not_77_out, not_78_out, OP5, OP4, not_79_out, not_80_out);
  and and_15 (and_15_out, not_81_out, not_82_out, not_83_out, F13, F12, not_84_out, OP5, OP4, not_85_out, not_86_out);
  and and_16 (and_16_out, not_87_out, not_88_out, not_89_out, not_90_out, not_91_out, OP4, not_92_out, not_93_out);
  and and_17 (and_17_out, F14, F13, F12, not_94_out, not_95_out, OP4, not_96_out, not_97_out);
  and and_18 (and_18_out, F14, F13, not_98_out, not_99_out, not_100_out, OP4, not_101_out, not_102_out);
  and and_19 (and_19_out, F14, not_103_out, not_104_out, not_105_out, not_106_out, OP4, not_107_out, not_108_out);
  and and_20 (and_20_out, not_109_out, F13, not_110_out, not_111_out, not_112_out, OP4, not_113_out, not_114_out);
  and and_21 (and_21_out, not_115_out, not_116_out, not_117_out, not_118_out, F12, not_119_out, not_120_out, OP4, not_121_out, not_122_out);
  and and_22 (and_22_out, not_123_out, not_124_out, F14, not_125_out, F12, not_126_out, not_127_out, OP4, not_128_out, not_129_out);
  and and_23 (and_23_out, F30, not_130_out, F14, not_131_out, F12, not_132_out, not_133_out, OP4, not_134_out, not_135_out);
  and and_24 (and_24_out, not_136_out, F13, not_137_out, not_138_out, not_139_out, not_140_out, not_141_out, not_142_out);
  and and_25 (and_25_out, OP6, OP5, not_143_out, OP3, OP2);
  and and_26 (and_26_out, not_144_out, not_145_out, not_146_out, OP6, OP5, not_147_out, not_148_out, OP2);
  and and_27 (ecall, not_149_out, not_150_out, OP4, OP5, OP6, not_151_out, not_152_out, not_153_out, not_154_out, not_155_out);
  and and_28 (S_Type, not_156_out, not_157_out, not_158_out, OP5, not_159_out, not_160_out, F13, not_161_out);
  and and_29 (BEQ, not_162_out, not_163_out, not_164_out, OP5, OP6, not_165_out, not_166_out, not_167_out);
  and and_30 (BNE, not_168_out, not_169_out, not_170_out, OP5, OP6, F12, not_171_out, not_172_out);
  and and_31 (JALR, OP2, not_173_out, not_174_out, OP5, OP6, not_175_out, not_176_out, not_177_out);
  and and_32 (JAL, OP2, OP3, not_178_out, OP5, OP6);
  and and_33 (U_type, OP2, not_179_out, OP4, OP5, not_180_out);
  and and_34 (Byte, not_181_out, not_182_out, not_183_out, not_184_out, not_185_out, not_186_out, not_187_out, not_188_out);
  and and_35 (BGEU, not_189_out, not_190_out, not_191_out, OP5, OP6, F12, F13, F14);
  or or_1 (ALU_SRC, and_3_out, and_4_out, and_5_out, and_6_out, and_7_out, and_8_out, and_9_out);
  or or_2 (RegWrite, and_10_out, and_11_out, and_12_out, and_13_out, and_14_out, and_15_out, and_16_out, and_17_out, and_18_out, and_19_out, and_20_out, and_21_out, and_22_out, and_23_out, and_24_out, and_25_out, and_26_out);
endmodule

// ALU
module ALU (
  input  [31:0] X,
  input  [31:0] Y,
  input  [3:0] AluOP,
  output out_4,
  output Equal,
  output out_6,
  output [31:0] Result,
  output [31:0] Result_2
);

  wire [0:0] comparator_1_lt, comparator_2_lt;
  wire [31:0] adder_1_out, AND_out, divider_1_out, divider_1_rem, multiplier_1_cout, multiplier_1_out,
       NOR_out, OR_out, shifter_1_out, shifter_2_out, shifter_3_out, subtractor_1_out, XOR_out;

  assign AND_out = X & Y;  // AND_Gate AND, 32 bits wide
  assign OR_out = X | Y;  // OR_Gate OR, 32 bits wide
  Shifter #(.width(32), .shift("ll")) shifter_1 (.in(X), .\dist (Y[4:0]), .out(shifter_1_out));
  Shifter #(.width(32), .shift("ar")) shifter_2 (.in(X), .\dist (Y[4:0]), .out(shifter_2_out));
  Shifter #(.width(32), .shift("lr")) shifter_3 (.in(X), .\dist (Y[4:0]), .out(shifter_3_out));
  Multiplier #(.width(32)) multiplier_1 (.a(X), .b(Y), .out(multiplier_1_out), .cout(multiplier_1_cout));  // open: cin
  Divider #(.width(32)) divider_1 (.a(X), .b(Y), .out(divider_1_out), .rem(divider_1_rem));  // open: upper
  Adder #(.width(32)) adder_1 (.a(X), .b(Y), .out(adder_1_out));  // open: cin, cout
  Subtractor #(.width(32)) subtractor_1 (.a(X), .b(Y), .out(subtractor_1_out));  // open: bin, bout
  assign XOR_out = X ^ Y;  // XOR_Gate XOR, 32 bits wide
  assign NOR_out = ~(X | Y);  // NOR_Gate NOR, 32 bits wide
  Comparator #(.width(32), .mode("twosComplement")) comparator_1 (
    .a(X), .b(Y), .eq(Equal), .lt(comparator_1_lt[0]));  // open: gt
  Comparator #(.width(32), .mode("unsigned")) comparator_2 (.a(X), .b(Y), .lt(comparator_2_lt[0]));  // open: gt, eq
  Multiplexer #(.select(4), .width(32), .disabled("Z"), .enable("false")) multiplexer_1 (
    .in0(shifter_1_out), .in1(shifter_2_out), .in2(shifter_3_out), .in3(multiplier_1_out),
    .in4(divider_1_out), .in5(adder_1_out), .in6(subtractor_1_out), .in7(AND_out), .in8(OR_out),
    .in9(XOR_out), .in10(NOR_out), .in11({{31{1'b0}}, comparator_1_lt[0]}),
    .in12({{31{1'b0}}, comparator_2_lt[0]}), .in13({32{1'b0}}), .in14({32{1'b0}}), .in15({32{1'b0}}),
    .out(Result), .sel(AluOP));
  Multiplexer #(.select(4), .width(32), .disabled("Z"), .enable("false")) multiplexer_2 (
    .in0({32{1'b0}}), .in1({32{1'b0}}), .in2({32{1'b0}}), .in3(multiplier_1_cout), .in4(divider_1_rem),
    .in5({32{1'b0}}), .in6({32{1'b0}}), .in7({32{1'b0}}), .in8({32{1'b0}}), .in9({32{1'b0}}),
    .in10({32{1'b0}}), .in11({32{1'b0}}), .in12({32{1'b0}}), .in13({32{1'b0}}), .in14({32{1'b0}}),
    .in15({32{1'b0}}), .out(Result_2), .sel(AluOP));
  Multiplexer #(.select(4), .width(1), .disabled("Z"), .enable("false")) multiplexer_3 (
    .in0(1'b0), .in1(1'b0), .in2(1'b0), .in3(1'b0), .in4(1'b0), .in5(1'b0), .in6(1'b0), .in7(1'b0),
    .in8(1'b0), .in9(1'b0), .in10(1'b0), .in11(comparator_1_lt[0]), .in12(comparator_2_lt[0]), .in13(1'b0),
    .in14(1'b0), .in15(1'b0), .out(out_6), .sel(AluOP));
  not not_1 (out_4, out_6);

  // Other names for the same wires on the sheet: Result2[31:0] = Result_2; S[3:0] = AluOP; tunnel = out_6;
  //   tunnel_t = out_4

  // Notes on the sheet:
  //   不要改变此引脚区域内容，也不要改变ALU封装形式
  //   输入引脚
  //   输出引脚
endmodule

module Regifile (
  input  [31:0] Din,
  input  Clk,
  input  WE,
  input  [4:0] R1_num,
  input  [4:0] W_num,
  input  [4:0] R2_num,
  output [31:0] R1,
  output [31:0] R2
);

  // RegisterFile registerfile_1: pin names not known; wires that end beside it: Din, Clk, WE, W_num, R1_num, R2_num, R1, R2
endmodule

module \理想流水线  (
  output RegWrite,
  output MemWrite,
  output [31:0] IF_PC,
  output [31:0] ID_PC,
  output [31:0] EX_PC,
  output [31:0] M_PC,
  output [31:0] WB_PC,
  output [31:0] RDin,
  output [31:0] MDin,
  output [31:0] LedData
);

  wire AluSrcB_EX, and_2_out, and_3_out, and_4_out, and_5_out, and_7_out, B_Src, CLK, clock_1_out,
       comparator_1_eq, comparator_1_lt, comparator_2_eq, comparator_3_eq, d_ff_1_q, ecall, ecall_halt,
       ecallFB, Equ, ex_mem_1_ecall_2, ex_mem_1_jal_2, ex_mem_1_jalr_2, ex_mem_1_memtoreg_2,
       ex_mem_1_regwrite_2, ex_mem_1_uret_2, Go, halt, id_ex_1_beq_2, id_ex_1_bne_2, id_ex_1_ecall_2,
       id_ex_1_memtoreg_2, id_ex_1_memwrite_2, id_ex_1_regwrite_2, id_ex_1_uret_2, IR1, IR2, IR3, JAL,
       JAL_EX, JAL_WB, JALR, JALR_EX, JALR_WB, mem_wb_1_ecall_2, MemToReg_WB, nand_1_out, not_1_out,
       not_2_out, not_3_out, not_4_out, not_5_out, not_6_out, not_7_out, or_2_out, RST, S_type, Stop, URET,
       W1, W2, W3, \单周期硬布线控制器_1_alu_src , \单周期硬布线控制器_1_beq , \单周期硬布线控制器_1_bne , \单周期硬布线控制器_1_ecall ,
       \单周期硬布线控制器_1_memtoreg , \单周期硬布线控制器_1_memwrite , \单周期硬布线控制器_1_regwrite ;
  wire [3:0] AluOP_EX, \单周期硬布线控制器_1_alu_op ;
  wire [4:0] ex_mem_1_w_num_2, id_ex_1_w_num_2, multiplexer_4_out, multiplexer_5_out, W__WB;
  wire [12:0] CNT_num;
  wire [15:0] \LoadUse次数 , \总周期数 , \插入气泡数 , \无条件分支数 , \条件分支成功数 ;
  wire [31:0] AluResult, bit_extender_1_out, bit_extender_2_out, bit_extender_3_out, bit_extender_4_out,
       bit_extender_5_out, EX_IR, ex_mem_1_aluresult_2, ex_mem_1_pc_4_2, ex_mem_1_rega_2, id_ex_1_imm_2,
       id_ex_1_imm_b_2, id_ex_1_imm_j_2, id_ex_1_pc_4_2, ID_IR, if_id_1_pc_4_2, IF_IR, imm_U, MEM_IR,
       mem_wb_1_aluresult_2, mem_wb_1_memdata_2, mem_wb_1_pc_4_2, multiplexer_1_out, multiplexer_2_out,
       multiplexer_3_out, multiplexer_6_out, multiplexer_7_out, multiplexer_8_out, PC_4, PC_B, PC_JAL, R1,
       R1_EX, R1_WB, R2, R2_EX, R2_WB, ram_1_data, shifter_1_out, shifter_2_out, WB_IR;

  Button \u_总复位  (.out(RST));
  Button _1 (.out(IR1));
  Button _2 (.out(IR2));
  Button _3 (.out(IR3));
  // Probe on \总周期数 
  // Probe on \总周期数 
  Button \u_继续运行  (.out(Go));
  LED #(.active("true")) led_1 (.in(W1));
  LED #(.active("true")) led_2 (.in(W2));
  LED #(.active("true")) led_3 (.in(W3));
  Hex_Digit_Display hex_digit_display_1 (.value(LedData[31:28]));  // open: dp
  // Probe on IF_PC[19:0]
  // RiscV_Probe riscv_probe_1: pin names not known; wires that end beside it: IF_IR
  Multiplexer #(.select(1), .width(32), .disabled("Z"), .enable("false")) multiplexer_1 (
    .in0(PC_4), .in1(AluResult), .out(multiplexer_1_out), .sel(JALR_EX));
  Hex_Digit_Display hex_digit_display_2 (.value(LedData[27:24]));  // open: dp
  Hex_Digit_Display hex_digit_display_3 (.value(LedData[23:20]));  // open: dp
  // Probe on ID_PC[19:0]
  // RiscV_Probe riscv_probe_2: pin names not known; wires that end beside it: ID_IR
  not not_1 (not_1_out, halt);
  Counter #(.width(16), .max('hffff), .ongoal("wrap"), .trigger("rising"), .behavior("new")) counter_1 (
    .count(not_1_out), .Q(\总周期数 ), .clk(CLK), .clr(RST));  // open: load, D, carry, preset, down
  Multiplexer #(.select(1), .width(32), .disabled("Z"), .enable("false")) multiplexer_2 (
    .in0(multiplexer_1_out), .in1(PC_JAL), .out(multiplexer_2_out), .sel(JAL_EX));
  Hex_Digit_Display hex_digit_display_4 (.value(LedData[19:16]));  // open: dp
  Hex_Digit_Display hex_digit_display_5 (.value(LedData[15:12]));  // open: dp
  Multiplexer #(.select(1), .width(32), .disabled("Z"), .enable("false")) multiplexer_3 (
    .in0(multiplexer_2_out), .in1(PC_B), .out(multiplexer_3_out), .sel(B_Src));
  Hex_Digit_Display hex_digit_display_6 (.value(LedData[7:4]));  // open: dp
  Hex_Digit_Display hex_digit_display_7 (.value(LedData[11:8]));  // open: dp
  // Probe on EX_PC[19:0]
  // RiscV_Probe riscv_probe_3: pin names not known; wires that end beside it: EX_IR
  Register #(.width(32), .trigger("rising"), .Select("low")) PC (
    .D(multiplexer_3_out), .en(not_2_out), .Q(IF_PC), .clk(CLK), .clr(RST));
  not not_2 (not_2_out, Stop);
  Hex_Digit_Display hex_digit_display_8 (.value(LedData[3:0]));  // open: dp
  // Probe on \总周期数 
  // Probe on M_PC[19:0]
  // RiscV_Probe riscv_probe_4: pin names not known; wires that end beside it: MEM_IR
  Adder #(.width(32)) adder_1 (.a(IF_PC), .b(32'h4), .out(PC_4), .cin(1'b0));  // open: cout
  // RiscV_Probe riscv_probe_5: pin names not known; wires that end beside it: IF_IR
  // Probe on \总周期数 
  // Probe on \无条件分支数 
  // Probe on \条件分支成功数 
  // Probe on \插入气泡数 
  // Probe on \LoadUse次数 
  ROM #(.addrWidth(10), .dataWidth(32), .Select("high")) rom_1 (.addr(IF_PC[11:2]), .data(IF_IR));
  // Probe on IF_PC[11:0]
  // Probe on WB_PC[19:0]
  // RiscV_Probe riscv_probe_6: pin names not known; wires that end beside it: WB_IR
  IF_ID if_id_1 (
    .PC(IF_PC), .IR(IF_IR), .PC_4(PC_4), .PC_2(ID_PC), .IR_2(ID_IR), .PC_4_2(if_id_1_pc_4_2), .CLK(CLK),
    .\RST_为1同步清零 (RST));  // open: halt_为1暂停, predict, predict_2, PredictAddr, PredictAddr_2
  // Probe on ID_PC[11:0]
  // Probe on EX_PC[11:0]
  // Probe on M_PC[11:0]
  D_Flip_Flop #(.trigger("high"), .Pre_Clr_Positions("LEGACY"), .NegatePresetClear("false"), .enable("true"), .NewFFLayout("false")) d_ff_1 (.Q(d_ff_1_q));  // open: clk, D, Qn, preset, en, reset
  // Probe on 13'h14
  // Probe on WB_PC[11:0]
  Comparator #(.width(13), .mode("twosComplement")) comparator_1 (
    .a(CNT_num), .b(13'h14), .eq(comparator_1_eq), .lt(comparator_1_lt));  // open: gt
  Clock #(.highDuration(1), .lowDuration(1)) clock_1 (.out(clock_1_out));
  nand nand_1 (nand_1_out, d_ff_1_q, comparator_1_eq);
  Counter #(.width(13), .max('h1fff), .ongoal("stay"), .trigger("rising"), .behavior("old")) counter_2 (
    .count(comparator_1_lt), .Q(CNT_num), .clk(clock_1_out), .clr(RST));  // open: load, D, carry, preset
  and and_1 (ecall, ~ecallFB, \单周期硬布线控制器_1_ecall );  // AND_Gate
  assign CLK = nand_1_out ? clock_1_out : 1'bz;  // Controlled_Buffer controlled_buffer_1
  \单周期硬布线控制器  \u_单周期硬布线控制器_1  (
    .Funct({ID_IR[30], ID_IR[25], ID_IR[14:12]}), .OP(ID_IR[6:2]), .ALU_OP(\单周期硬布线控制器_1_alu_op ),
    .MemToReg(\单周期硬布线控制器_1_memtoreg ), .MemWrite(\单周期硬布线控制器_1_memwrite ), .ALU_SRC(\单周期硬布线控制器_1_alu_src ),
    .RegWrite(\单周期硬布线控制器_1_regwrite ), .ecall(\单周期硬布线控制器_1_ecall ), .S_type(S_type), .Jalr(JALR),
    .Beq(\单周期硬布线控制器_1_beq ), .JAL(JAL), .Bne(\单周期硬布线控制器_1_bne ), .in_3(ID_IR[21]), .uret(URET));  // open: U_ype, Byte, BGEU
  assign bit_extender_1_out = {{20{ID_IR[31]}}, ID_IR[31:20]};  // Bit_Extender bit_extender_1
  assign bit_extender_2_out = {{20{ID_IR[31]}}, {ID_IR[31:25], ID_IR[11:7]}};  // Bit_Extender bit_extender_2
  assign bit_extender_3_out = {{20{ID_IR[31]}}, {ID_IR[31], ID_IR[7], ID_IR[30:25], ID_IR[11:8]}};  // Bit_Extender bit_extender_3
  assign bit_extender_4_out = {{12{ID_IR[31]}}, {ID_IR[31], ID_IR[19:12], ID_IR[20], ID_IR[30:21]}};  // Bit_Extender bit_extender_4
  assign bit_extender_5_out = {{12{ID_IR[31]}}, ID_IR[31:12]};  // Bit_Extender bit_extender_5
  // RiscV_Probe riscv_probe_7: pin names not known; wires that end beside it: ID_IR
  Pull_Resistor #(.pull(1)) pull_resistor_1 (.node(CLK));
  Multiplexer #(.select(1), .width(5), .disabled("Z"), .enable("false")) multiplexer_4 (
    .in0(ID_IR[19:15]), .in1(5'b10001), .out(multiplexer_4_out), .sel(ecall));
  Multiplexer #(.select(1), .width(5), .disabled("Z"), .enable("false")) multiplexer_5 (
    .in0(ID_IR[24:20]), .in1(5'b01010), .out(multiplexer_5_out), .sel(ecall));
  Multiplexer #(.select(1), .width(32), .disabled("Z"), .enable("false")) multiplexer_6 (
    .in0(bit_extender_1_out), .in1(bit_extender_2_out), .out(multiplexer_6_out), .sel(S_type));
  Shifter #(.width(32), .shift("ll")) shifter_1 (.in(bit_extender_3_out), .\dist (5'b00001), .out(shifter_1_out));
  Shifter #(.width(32), .shift("ll")) shifter_2 (.in(bit_extender_4_out), .\dist (5'b00001), .out(shifter_2_out));
  Shifter #(.width(32), .shift("ll")) shifter_3 (.in(bit_extender_5_out), .\dist (5'b10010), .out(imm_U));
  Regifile regifile_1 (
    .Din(RDin), .Clk(CLK), .R1(R1), .R2(R2), .WE(RegWrite), .W_num(W__WB), .R1_num(multiplexer_4_out),
    .R2_num(multiplexer_5_out));
  and and_2 (and_2_out, id_ex_1_beq_2, Equ);
  ID_EX id_ex_1 (
    .PC(ID_PC), .IR(ID_IR), .PC_4(if_id_1_pc_4_2), .RegA(R1), .RegB(R2), .imm(multiplexer_6_out),
    .imm_B(shifter_1_out), .imm_J(shifter_2_out), .Beq(\单周期硬布线控制器_1_beq ), .Bne(\单周期硬布线控制器_1_bne ),
    .MemToReg(\单周期硬布线控制器_1_memtoreg ), .MemWrite(\单周期硬布线控制器_1_memwrite ), .AluOP(\单周期硬布线控制器_1_alu_op ),
    .AluSrcB(\单周期硬布线控制器_1_alu_src ), .RegWrite(\单周期硬布线控制器_1_regwrite ), .JAL(JAL), .JALR(JALR), .URET(URET),
    .PC_2(EX_PC), .IR_2(EX_IR), .PC_4_2(id_ex_1_pc_4_2), .RegA_2(R1_EX), .RegB_2(R2_EX),
    .imm_2(id_ex_1_imm_2), .imm_B_2(id_ex_1_imm_b_2), .imm_J_2(id_ex_1_imm_j_2), .Beq_2(id_ex_1_beq_2),
    .Bne_2(id_ex_1_bne_2), .MemToReg_2(id_ex_1_memtoreg_2), .MemWrite_2(id_ex_1_memwrite_2),
    .AluOP_2(AluOP_EX), .AluSrcB_2(AluSrcB_EX), .RegWrite_2(id_ex_1_regwrite_2), .JAL_2(JAL_EX),
    .JALR_2(JALR_EX), .URET_2(id_ex_1_uret_2), .CLK(CLK), .W_num_2(id_ex_1_w_num_2), .ecall(ecall),
    .ecall_2(id_ex_1_ecall_2), .\RST_为1同步清零 (RST), .imm_U(imm_U), .W_num(ID_IR[11:7]));  // open: imm_U_2, halt_为1暂停, R1_fwd_ID, R2_fwd_ID, R1_fwd_EX, R2_fwd_EX, predict, predict_2, PredictAddr, PredictAddr_2
  or or_1 (B_Src, and_2_out, and_3_out);
  and and_3 (and_3_out, id_ex_1_bne_2, not_3_out);
  not not_3 (not_3_out, Equ);
  Multiplexer #(.select(1), .width(32), .disabled("Z"), .enable("false")) multiplexer_7 (
    .in0(R2_EX), .in1(id_ex_1_imm_2), .out(multiplexer_7_out), .sel(AluSrcB_EX));
  Adder #(.width(32)) adder_2 (.a(id_ex_1_imm_b_2), .b(EX_PC), .out(PC_B), .cin(1'b0));  // open: cout
  Adder #(.width(32)) adder_3 (.a(id_ex_1_imm_j_2), .b(EX_PC), .out(PC_JAL), .cin(1'b0));  // open: cout
  // RiscV_Probe riscv_probe_8: pin names not known; wires that end beside it: EX_IR
  ALU alu_1 (
    .X(R1_EX), .Y(multiplexer_7_out), .AluOP(AluOP_EX), .Equal(Equ), .Result(AluResult));  // open: Result_2, out_4, out_6
  EX_MEM ex_mem_1 (
    .PC(EX_PC), .IR(EX_IR), .PC_4(id_ex_1_pc_4_2), .RegA(R1_EX), .RegWrite(id_ex_1_regwrite_2), .JAL(JAL_EX),
    .JALR(JALR_EX), .PC_2(M_PC), .IR_2(MEM_IR), .PC_4_2(ex_mem_1_pc_4_2), .RegA_2(ex_mem_1_rega_2),
    .RegB_2(MDin), .MemToReg_2(ex_mem_1_memtoreg_2), .MemWrite_2(MemWrite), .RegWrite_2(ex_mem_1_regwrite_2),
    .JAL_2(ex_mem_1_jal_2), .JALR_2(ex_mem_1_jalr_2), .URET_2(ex_mem_1_uret_2), .CLK(CLK),
    .AluResult_2(ex_mem_1_aluresult_2), .W_num_2(ex_mem_1_w_num_2), .ecall_2(ex_mem_1_ecall_2), .RegB(R2_EX),
    .AluResult(AluResult), .MemToReg(id_ex_1_memtoreg_2), .MemWrite(id_ex_1_memwrite_2),
    .URET(id_ex_1_uret_2), .W_num(id_ex_1_w_num_2), .ecall(id_ex_1_ecall_2), .\RST_为1同步清零 (RST));  // open: AluOP, AluSrcB, Beq_2, Bne_2, AluOP_2, AluSrcB_2, halt_为1暂停, Beq, Bne
  // RiscV_Probe riscv_probe_9: pin names not known; wires that end beside it: MEM_IR, MEM_IR
  RAM #(.addrWidth(10), .dataWidth(32), .bus("separate"), .Select("high")) ram_1 (
    .addr(ex_mem_1_aluresult_2[11:2]), .din(MDin), .data(ram_1_data), .str(MemWrite), .sel(1'b1), .clk(CLK),
    .ld(1'b1), .clr(RST));
  MEM_WB mem_wb_1 (
    .PC(M_PC), .PC_2(WB_PC), .IR(MEM_IR), .IR_2(WB_IR), .PC_4(ex_mem_1_pc_4_2), .PC_4_2(mem_wb_1_pc_4_2),
    .RegA(ex_mem_1_rega_2), .RegA_2(R1_WB), .RegB(MDin), .AluResult(ex_mem_1_aluresult_2),
    .AluResult_2(mem_wb_1_aluresult_2), .MemToReg(ex_mem_1_memtoreg_2), .MemToReg_2(MemToReg_WB),
    .RegWrite(ex_mem_1_regwrite_2), .RegWrite_2(RegWrite), .JAL(ex_mem_1_jal_2), .JAL_2(JAL_WB),
    .JALR(ex_mem_1_jalr_2), .JALR_2(JALR_WB), .URET(ex_mem_1_uret_2), .W_num(ex_mem_1_w_num_2),
    .W_num_2(W__WB), .ecall(ex_mem_1_ecall_2), .ecall_2(mem_wb_1_ecall_2), .CLK(CLK), .\halt_为1暂停 (RST),
    .MemData(ram_1_data), .MemData_2(mem_wb_1_memdata_2));  // open: RegB_2, Beq, Beq_2, Bne, Bne_2, MemWrite, MemWrite_2, AluOP, AluOP_2, AluSrcB, AluSrcB_2, URET_2, RST_为1同步清零
  Multiplexer #(.select(1), .width(32), .disabled("Z"), .enable("false")) multiplexer_8 (
    .in0(mem_wb_1_aluresult_2), .in1(mem_wb_1_memdata_2), .out(multiplexer_8_out), .sel(MemToReg_WB));
  // RiscV_Probe riscv_probe_10: pin names not known; wires that end beside it: WB_IR, mem_wb_1_pc_4_2
  or or_2 (or_2_out, JALR_WB, JAL_WB);
  Multiplexer #(.select(1), .width(32), .disabled("Z"), .enable("false")) multiplexer_9 (
    .in0(multiplexer_8_out), .in1(mem_wb_1_pc_4_2), .out(RDin), .sel(or_2_out));
  Comparator #(.width(32), .mode("twosComplement")) comparator_2 (
    .a(R1), .b(32'h22), .eq(comparator_2_eq));  // open: gt, lt
  not not_4 (not_4_out, comparator_2_eq);
  and and_4 (and_4_out, Go, halt);
  and and_5 (and_5_out, ecall, comparator_2_eq);
  and and_6 (halt, not_4_out, ecall);
  Counter #(.width(1), .max('h1), .ongoal("stay"), .trigger("rising"), .behavior("new")) counter_3 (
    .D(and_4_out), .Q(ecallFB), .clk(and_4_out), .clr(RST));  // open: load, count, carry, preset, down
  Comparator #(.width(32), .mode("twosComplement")) comparator_3 (
    .a(R1_WB), .b(32'h22), .eq(comparator_3_eq));  // open: gt, lt
  Register #(.width(32), .trigger("rising"), .Select("low")) register_1 (
    .D(R2), .en(and_5_out), .Q(LedData), .clk(CLK), .clr(RST));
  and and_7 (and_7_out, comparator_3_eq, mem_wb_1_ecall_2);
  not not_5 (not_5_out, comparator_3_eq);
  and and_8 (ecall_halt, mem_wb_1_ecall_2, not_5_out);
  not not_6 (not_6_out, Go);
  not not_7 (not_7_out, RST);
  and and_9 (Stop, ecall_halt, not_6_out, not_7_out);
  Register #(.width(32), .trigger("rising"), .Select("low")) register_2 (
    .D(R2_WB), .en(and_7_out), .Q(LedData), .clk(CLK), .clr(RST));

  // Other names for the same wires on the sheet: IR[31:0] = IF_IR; MEM_PC[31:0] = M_PC; MemWrite_Mem = MemWrite;
  //   PC[31:0] = IF_PC; RegWrite_WB = RegWrite

  // Notes on the sheet:
  //   中断源
  //   时空图监测，可删除
  //   中断等待指示
  //   IF
  //   数码管输出
  //   指令存储器
  //   指令字
  //   contents of rom_1 (hex, n*v repeats v):
  //   413 493 913 993 46413 14e493 296913 39e993 842023 942223 1242423 1342623 a00893 493 913 993 73
  //   控制位
  //   流水调试日志用
  //   暂停节拍，不能为0
  //   JAL
  //   JALR
  //   URET
  //   I立即数
  //   S立即数
  //   B立即数
  //   J立即数
  //   U立即数
  //   可计数暂停的时钟源
  //   ID
  //   Beq
  //   Bne
  //   MemToReg
  //   MemWrite
  //   AluOP
  //   AluSrcB
  //   RegWrite
  //   用这个时钟源需要去掉电路中的其他时钟源
  //   为方便自动评测，需要输出流水线各段保存的PC值，注意是PC不是PC+4，另外ID段寄存器写入信息，Mem段内存写入信息也要输出
  //   戳工具置1进入计数暂停模式，ctrl+k时钟自动运行到对应节拍暂停
  //   ctrl+k关闭时钟连续运行，将控制位置零，进入单步调试模式调试
  //   Beq
  //   Bne
  //   MemToReg
  //   MemWrite
  //   AluOP
  //   AluSrcB
  //   RegWrite
  //   JAL
  //   JALR
  //   URET
  //   EX
  //   MemToReg
  //   MemWrite
  //   RegWrite
  //   JAL
  //   JALR
  //   URET
  //   MEM
  //   数据存储器
  //   MemToReg
  //   RegWrite
  //   JAL
  //   JALR
  //   URET
  //   WB
  //   ecall指令相关
  //   ecall为1，$a7==34,LED显示$a0的值，否则停机等待GO键
  //   ecall触发时暂停，按下GO继续
endmodule

module \气泡流水线  (
  output RegWrite,
  output MemWrite,
  output [31:0] IF_PC,
  output [31:0] ID_PC,
  output [31:0] EX_PC,
  output [31:0] M_PC,
  output [31:0] WB_PC,
  output [31:0] RDin,
  output [31:0] MDin,
  output [31:0] LedData
);

  wire AluSrcB_EX, and_1_out, and_2_out, and_3_out, and_4_out, and_5_out, and_6_out, B_Src, Branch, CLK,
       clock_1_out, comparator_1_eq, comparator_1_lt, comparator_2_eq, d_ff_1_q, DataRelated, ecall,
       ecall_halt, Equ, ex_mem_1_ecall_2, ex_mem_1_jal_2, ex_mem_1_jalr_2, ex_mem_1_memtoreg_2,
       ex_mem_1_uret_2, Go, id_ex_1_beq_2, id_ex_1_bne_2, id_ex_1_ecall_2, id_ex_1_memtoreg_2,
       id_ex_1_memwrite_2, id_ex_1_uret_2, IR1, IR2, IR3, JAL, JAL_EX, JAL_WB, JALR, JALR_EX, JALR_WB,
       mem_wb_1_ecall_2, MemToReg_WB, multiplexer_10_out, multiplexer_11_out, nand_1_out, not_1_out,
       not_2_out, not_3_out, not_4_out, not_5_out, not_6_out, not_7_out, not_8_out, not_9_out, or_1_out,
       or_2_out, or_3_out, or_5_out, or_7_out, or_8_out, or_9_out, or_10_out, RegWrite_EX, RegWrite_MEM, RST,
       S_type, Stop, URET, W1, W2, W3, \单周期硬布线控制器_1_alu_src , \单周期硬布线控制器_1_beq , \单周期硬布线控制器_1_bne ,
       \单周期硬布线控制器_1_memtoreg , \单周期硬布线控制器_1_memwrite , \单周期硬布线控制器_1_regwrite ;
  wire [3:0] AluOP_EX, \单周期硬布线控制器_1_alu_op ;
  wire [4:0] Funct, R1_num, R2_num, W__EX, W__MEM, W__WB;
  wire [12:0] CNT_num;
  wire [15:0] adder_4_out, \DataRelated次数 , multiplier_1_out, \总周期数 , \插入气泡数 , \无条件分支数 , \条件分支成功数 ;
  wire [31:0] AluResult, bit_extender_1_out, bit_extender_2_out, bit_extender_3_out, bit_extender_4_out,
       bit_extender_5_out, EX_IR, ex_mem_1_aluresult_2, ex_mem_1_pc_4_2, ex_mem_1_rega_2, id_ex_1_imm_2,
       id_ex_1_imm_b_2, id_ex_1_imm_j_2, id_ex_1_pc_4_2, ID_IR, if_id_1_pc_4_2, IF_IR, imm_U, MEM_IR,
       mem_wb_1_aluresult_2, mem_wb_1_memdata_2, mem_wb_1_pc_4_2, multiplexer_1_out, multiplexer_2_out,
       multiplexer_3_out, multiplexer_6_out, multiplexer_7_out, multiplexer_8_out, PC_4, PC_B, PC_JAL, R1,
       R1_EX, R1_WB, R2, R2_EX, R2_WB, ram_1_data, shifter_1_out, shifter_2_out, WB_IR;

  Button \u_总复位  (.out(RST));
  Button _1 (.out(IR1));
  Button _2 (.out(IR2));
  Button _3 (.out(IR3));
  // Probe on \总周期数 
  // Probe on \总周期数 
  Button \u_继续运行  (.out(Go));
  LED #(.active("true")) led_1 (.in(W1));
  LED #(.active("true")) led_2 (.in(W2));
  LED #(.active("true")) led_3 (.in(W3));
  Hex_Digit_Display hex_digit_display_1 (.value(LedData[31:28]));  // open: dp
  // Probe on IF_PC[19:0]
  // RiscV_Probe riscv_probe_1: pin names not known; wires that end beside it: IF_IR
  Multiplexer #(.select(1), .width(32), .disabled("Z"), .enable("false")) multiplexer_1 (
    .in0(PC_4), .in1(AluResult), .out(multiplexer_1_out), .sel(JALR_EX));
  Hex_Digit_Display hex_digit_display_2 (.value(LedData[23:20]));  // open: dp
  Hex_Digit_Display hex_digit_display_3 (.value(LedData[27:24]));  // open: dp
  // Probe on ID_PC[19:0]
  // RiscV_Probe riscv_probe_2: pin names not known; wires that end beside it: {ID_IR[31], Funct[4], ID_IR[29:26], Funct[3], ID_IR[24:15], Funct[2:0], ID_IR[11:0]}
  Multiplexer #(.select(1), .width(32), .disabled("Z"), .enable("false")) multiplexer_2 (
    .in0(multiplexer_1_out), .in1(PC_JAL), .out(multiplexer_2_out), .sel(JAL_EX));
  Hex_Digit_Display hex_digit_display_4 (.value(LedData[19:16]));  // open: dp
  Hex_Digit_Display hex_digit_display_5 (.value(LedData[15:12]));  // open: dp
  \数据相关检测器  \u_数据相关检测器_1  (
    .OP(ID_IR[6:2]), .R1_num(R1_num), .W__EX(W__EX), .W__MEM(W__MEM), .DataRelated(DataRelated),
    .Funct(Funct), .R2_num(R2_num), .RegWrite_EX(RegWrite_EX), .RegWrite_MEM(RegWrite_MEM));
  Multiplexer #(.select(1), .width(32), .disabled("Z"), .enable("false")) multiplexer_3 (
    .in0(multiplexer_2_out), .in1(PC_B), .out(multiplexer_3_out), .sel(B_Src));
  Hex_Digit_Display hex_digit_display_6 (.value(LedData[11:8]));  // open: dp
  Hex_Digit_Display hex_digit_display_7 (.value(LedData[7:4]));  // open: dp
  // Probe on EX_PC[19:0]
  // RiscV_Probe riscv_probe_3: pin names not known; wires that end beside it: EX_IR
  Register #(.width(32), .trigger("rising"), .Select("low")) PC (
    .D(multiplexer_3_out), .en(not_1_out), .Q(IF_PC), .clk(CLK), .clr(RST));
  not not_1 (not_1_out, or_1_out);
  or or_1 (or_1_out, DataRelated, Stop);
  Hex_Digit_Display hex_digit_display_8 (.value(LedData[3:0]));  // open: dp
  not not_2 (not_2_out, Stop);
  // Probe on \总周期数 
  // Probe on M_PC[19:0]
  // RiscV_Probe riscv_probe_4: pin names not known; wires that end beside it: MEM_IR
  Counter #(.width(16), .max('hffff), .ongoal("wrap"), .trigger("rising"), .behavior("new")) counter_1 (
    .count(not_2_out), .Q(\总周期数 ), .clk(CLK), .clr(RST));  // open: load, D, carry, preset, down
  Adder #(.width(32)) adder_1 (.a(IF_PC), .b(32'h4), .out(PC_4), .cin(1'b0));  // open: cout
  // RiscV_Probe riscv_probe_5: pin names not known; wires that end beside it: IF_IR
  // Probe on \总周期数 
  // Probe on \无条件分支数 
  // Probe on \条件分支成功数 
  // Probe on \插入气泡数 
  // Probe on {16{1'b0}}
  ROM #(.addrWidth(10), .dataWidth(32), .Select("high")) rom_1 (.addr(IF_PC[11:2]), .data(IF_IR));
  // Probe on IF_PC[11:0]
  // Probe on WB_PC[19:0]
  // RiscV_Probe riscv_probe_6: pin names not known; wires that end beside it: WB_IR
  IF_ID if_id_1 (
    .PC(IF_PC), .IR(IF_IR), .PC_4(PC_4), .PC_2(ID_PC),
    .IR_2({ID_IR[31], Funct[4], ID_IR[29:26], Funct[3], ID_IR[24:15], Funct[2:0], ID_IR[11:0]}),
    .PC_4_2(if_id_1_pc_4_2), .CLK(CLK), .\RST_为1同步清零 (or_3_out), .\halt_为1暂停 (or_2_out));  // open: predict, predict_2, PredictAddr, PredictAddr_2
  or or_2 (or_2_out, DataRelated, Stop);
  or or_3 (or_3_out, RST, Branch);
  // Probe on ID_PC[11:0]
  // Probe on EX_PC[11:0]
  // Probe on M_PC[11:0]
  D_Flip_Flop #(.trigger("high"), .Pre_Clr_Positions("LEGACY"), .NegatePresetClear("false"), .enable("true"), .NewFFLayout("false")) d_ff_1 (.Q(d_ff_1_q));  // open: clk, D, Qn, preset, en, reset
  // Probe on 13'hc
  // Probe on WB_PC[11:0]
  Comparator #(.width(13), .mode("twosComplement")) comparator_1 (
    .a(CNT_num), .b(13'hc), .eq(comparator_1_eq), .lt(comparator_1_lt));  // open: gt
  Clock #(.highDuration(1), .lowDuration(1)) clock_1 (.out(clock_1_out));
  \单周期硬布线控制器  \u_单周期硬布线控制器_1  (
    .Funct(Funct), .OP(ID_IR[6:2]), .ALU_OP(\单周期硬布线控制器_1_alu_op ), .MemToReg(\单周期硬布线控制器_1_memtoreg ),
    .MemWrite(\单周期硬布线控制器_1_memwrite ), .ALU_SRC(\单周期硬布线控制器_1_alu_src ), .RegWrite(\单周期硬布线控制器_1_regwrite ),
    .ecall(ecall), .S_type(S_type), .Jalr(JALR), .Beq(\单周期硬布线控制器_1_beq ), .JAL(JAL), .Bne(\单周期硬布线控制器_1_bne ),
    .in_3(ID_IR[21]), .uret(URET));  // open: U_ype, Byte, BGEU
  assign bit_extender_1_out = {{20{ID_IR[31]}}, {ID_IR[31], Funct[4], ID_IR[29:26], Funct[3], ID_IR[11:7]}};  // Bit_Extender bit_extender_1
  // RiscV_Probe riscv_probe_7: pin names not known; wires that end beside it: {ID_IR[31], Funct[4], ID_IR[29:26], Funct[3], ID_IR[24:15], Funct[2:0], ID_IR[11:0]}
  nand nand_1 (nand_1_out, d_ff_1_q, comparator_1_eq);
  Counter #(.width(13), .max('h1fff), .ongoal("stay"), .trigger("rising"), .behavior("old")) counter_2 (
    .count(comparator_1_lt), .Q(CNT_num), .clk(clock_1_out));  // open: load, D, carry, clr, preset
  Multiplexer #(.select(1), .width(5), .disabled("Z"), .enable("false")) multiplexer_4 (
    .in0(ID_IR[19:15]), .in1(5'b10001), .out(R1_num), .sel(ecall));
  Multiplexer #(.select(1), .width(5), .disabled("Z"), .enable("false")) multiplexer_5 (
    .in0(ID_IR[24:20]), .in1(5'b01010), .out(R2_num), .sel(ecall));
  assign bit_extender_2_out = {{20{ID_IR[31]}}, {ID_IR[31], Funct[4], ID_IR[29:26], Funct[3], ID_IR[24:20]}};  // Bit_Extender bit_extender_2
  assign bit_extender_3_out = {{20{ID_IR[31]}}, {ID_IR[31], ID_IR[7], Funct[4], ID_IR[29:26], Funct[3], ID_IR[11:8]}};  // Bit_Extender bit_extender_3
  assign bit_extender_4_out = {{12{ID_IR[31]}}, {ID_IR[31], ID_IR[19:15], Funct[2:0], ID_IR[20], Funct[4], ID_IR[29:26], Funct[3], ID_IR[24:21]}};  // Bit_Extender bit_extender_4
  assign bit_extender_5_out = {{12{ID_IR[31]}}, {ID_IR[31], Funct[4], ID_IR[29:26], Funct[3], ID_IR[24:15], Funct[2:0]}};  // Bit_Extender bit_extender_5
  assign CLK = nand_1_out ? clock_1_out : 1'bz;  // Controlled_Buffer controlled_buffer_1
  Multiplexer #(.select(1), .width(32), .disabled("Z"), .enable("false")) multiplexer_6 (
    .in0(bit_extender_2_out), .in1(bit_extender_1_out), .out(multiplexer_6_out), .sel(S_type));
  Shifter #(.width(32), .shift("ll")) shifter_1 (.in(bit_extender_3_out), .\dist (5'b00001), .out(shifter_1_out));
  Shifter #(.width(32), .shift("ll")) shifter_2 (.in(bit_extender_4_out), .\dist (5'b00001), .out(shifter_2_out));
  Shifter #(.width(32), .shift("ll")) shifter_3 (.in(bit_extender_5_out), .\dist (5'b01100), .out(imm_U));
  Pull_Resistor #(.pull(1)) pull_resistor_1 (.node(CLK));
  Regifile regifile_1 (
    .Din(RDin), .Clk(CLK), .R1(R1), .R2(R2), .WE(RegWrite), .W_num(W__WB), .R1_num(R1_num), .R2_num(R2_num));
  or or_4 (B_Src, and_1_out, and_2_out);
  and and_1 (and_1_out, id_ex_1_beq_2, Equ);
  ID_EX id_ex_1 (
    .PC(ID_PC), .IR({ID_IR[31], Funct[4], ID_IR[29:26], Funct[3], ID_IR[24:15], Funct[2:0], ID_IR[11:0]}),
    .PC_4(if_id_1_pc_4_2), .RegA(R1), .RegB(R2), .imm(multiplexer_6_out), .imm_B(shifter_1_out),
    .imm_J(shifter_2_out), .Beq(\单周期硬布线控制器_1_beq ), .Bne(\单周期硬布线控制器_1_bne ),
    .MemToReg(\单周期硬布线控制器_1_memtoreg ), .MemWrite(\单周期硬布线控制器_1_memwrite ), .AluOP(\单周期硬布线控制器_1_alu_op ),
    .AluSrcB(\单周期硬布线控制器_1_alu_src ), .RegWrite(\单周期硬布线控制器_1_regwrite ), .JAL(JAL), .JALR(JALR), .URET(URET),
    .PC_2(EX_PC), .IR_2(EX_IR), .PC_4_2(id_ex_1_pc_4_2), .RegA_2(R1_EX), .RegB_2(R2_EX),
    .imm_2(id_ex_1_imm_2), .imm_B_2(id_ex_1_imm_b_2), .imm_J_2(id_ex_1_imm_j_2), .Beq_2(id_ex_1_beq_2),
    .Bne_2(id_ex_1_bne_2), .MemToReg_2(id_ex_1_memtoreg_2), .MemWrite_2(id_ex_1_memwrite_2),
    .AluOP_2(AluOP_EX), .AluSrcB_2(AluSrcB_EX), .RegWrite_2(RegWrite_EX), .JAL_2(JAL_EX), .JALR_2(JALR_EX),
    .URET_2(id_ex_1_uret_2), .CLK(CLK), .W_num_2(W__EX), .ecall(ecall), .ecall_2(id_ex_1_ecall_2),
    .\RST_为1同步清零 (or_5_out), .imm_U(imm_U), .W_num(ID_IR[11:7]), .\halt_为1暂停 (Stop));  // open: imm_U_2, R1_fwd_ID, R2_fwd_ID, R1_fwd_EX, R2_fwd_EX, predict, predict_2, PredictAddr, PredictAddr_2
  or or_5 (or_5_out, RST, DataRelated, Branch);
  and and_2 (and_2_out, id_ex_1_bne_2, not_3_out);
  not not_3 (not_3_out, Equ);
  Multiplexer #(.select(1), .width(32), .disabled("Z"), .enable("false")) multiplexer_7 (
    .in0(R2_EX), .in1(id_ex_1_imm_2), .out(multiplexer_7_out), .sel(AluSrcB_EX));
  Adder #(.width(32)) adder_2 (.a(id_ex_1_imm_b_2), .b(EX_PC), .out(PC_B), .cin(1'b0));  // open: cout
  Adder #(.width(32)) adder_3 (.a(id_ex_1_imm_j_2), .b(EX_PC), .out(PC_JAL), .cin(1'b0));  // open: cout
  // RiscV_Probe riscv_probe_8: pin names not known; wires that end beside it: EX_IR
  ALU alu_1 (
    .X(R1_EX), .Y(multiplexer_7_out), .AluOP(AluOP_EX), .Equal(Equ), .Result(AluResult));  // open: Result_2, out_4, out_6
  or or_6 (Branch, JAL_EX, JALR_EX, B_Src);
  EX_MEM ex_mem_1 (
    .PC(EX_PC), .IR(EX_IR), .PC_4(id_ex_1_pc_4_2), .RegA(R1_EX), .RegWrite(RegWrite_EX), .JAL(JAL_EX),
    .JALR(JALR_EX), .PC_2(M_PC), .IR_2(MEM_IR), .PC_4_2(ex_mem_1_pc_4_2), .RegA_2(ex_mem_1_rega_2),
    .RegB_2(MDin), .MemToReg_2(ex_mem_1_memtoreg_2), .MemWrite_2(MemWrite), .RegWrite_2(RegWrite_MEM),
    .JAL_2(ex_mem_1_jal_2), .JALR_2(ex_mem_1_jalr_2), .URET_2(ex_mem_1_uret_2), .CLK(CLK),
    .AluResult_2(ex_mem_1_aluresult_2), .W_num_2(W__MEM), .ecall_2(ex_mem_1_ecall_2), .\halt_为1暂停 (Stop),
    .RegB(R2_EX), .AluResult(AluResult), .MemToReg(id_ex_1_memtoreg_2), .MemWrite(id_ex_1_memwrite_2),
    .URET(id_ex_1_uret_2), .W_num(W__EX), .ecall(id_ex_1_ecall_2), .\RST_为1同步清零 (RST));  // open: AluOP, AluSrcB, Beq_2, Bne_2, AluOP_2, AluSrcB_2, Beq, Bne
  not not_4 (not_4_out, Stop);
  and and_3 (and_3_out, B_Src, not_4_out);
  Counter #(.width(16), .max('hffff), .ongoal("wrap"), .trigger("rising"), .behavior("new")) counter_3 (
    .count(and_3_out), .Q(\条件分支成功数 ), .clk(CLK), .clr(RST));  // open: load, D, carry, preset, down
  // RiscV_Probe riscv_probe_9: pin names not known; wires that end beside it: MEM_IR, MEM_IR
  RAM #(.addrWidth(10), .dataWidth(32), .bus("separate"), .Select("high")) ram_1 (
    .addr(ex_mem_1_aluresult_2[11:2]), .din(MDin), .data(ram_1_data), .str(MemWrite), .sel(1'b1), .clk(CLK),
    .ld(1'b1), .clr(RST));
  not not_5 (not_5_out, Stop);
  or or_7 (or_7_out, JAL_EX, JALR_EX);
  and and_4 (and_4_out, or_7_out, not_5_out);
  Counter #(.width(16), .max('hffff), .ongoal("wrap"), .trigger("rising"), .behavior("new")) counter_4 (
    .count(and_4_out), .Q(\无条件分支数 ), .clk(CLK), .clr(RST));  // open: load, D, carry, preset, down
  MEM_WB mem_wb_1 (
    .PC(M_PC), .PC_2(WB_PC), .IR(MEM_IR), .IR_2(WB_IR), .PC_4(ex_mem_1_pc_4_2), .PC_4_2(mem_wb_1_pc_4_2),
    .RegA(ex_mem_1_rega_2), .RegA_2(R1_WB), .RegB(MDin), .RegB_2(R2_WB), .AluResult(ex_mem_1_aluresult_2),
    .AluResult_2(mem_wb_1_aluresult_2), .MemToReg(ex_mem_1_memtoreg_2), .MemToReg_2(MemToReg_WB),
    .RegWrite(RegWrite_MEM), .RegWrite_2(RegWrite), .JAL(ex_mem_1_jal_2), .JAL_2(JAL_WB),
    .JALR(ex_mem_1_jalr_2), .JALR_2(JALR_WB), .URET(ex_mem_1_uret_2), .W_num(W__MEM), .W_num_2(W__WB),
    .ecall(ex_mem_1_ecall_2), .ecall_2(mem_wb_1_ecall_2), .\RST_为1同步清零 (RST), .CLK(CLK), .\halt_为1暂停 (Stop),
    .MemData(ram_1_data), .MemData_2(mem_wb_1_memdata_2));  // open: Beq, Beq_2, Bne, Bne_2, MemWrite, MemWrite_2, AluOP, AluOP_2, AluSrcB, AluSrcB_2, URET_2
  Multiplexer #(.select(1), .width(32), .disabled("Z"), .enable("false")) multiplexer_8 (
    .in0(mem_wb_1_aluresult_2), .in1(mem_wb_1_memdata_2), .out(multiplexer_8_out), .sel(MemToReg_WB));
  // RiscV_Probe riscv_probe_10: pin names not known; wires that end beside it: WB_IR, mem_wb_1_pc_4_2
  and and_5 (and_5_out, DataRelated, not_6_out);
  or or_8 (or_8_out, JALR_WB, JAL_WB);
  Multiplexer #(.select(1), .width(32), .disabled("Z"), .enable("false")) multiplexer_9 (
    .in0(multiplexer_8_out), .in1(mem_wb_1_pc_4_2), .out(RDin), .sel(or_8_out));
  not not_6 (not_6_out, Stop);
  Counter #(.width(16), .max('hffff), .ongoal("wrap"), .trigger("rising"), .behavior("new")) counter_5 (
    .count(and_5_out), .Q(\DataRelated次数 ), .clk(CLK), .clr(RST));  // open: load, D, carry, preset, down
  Comparator #(.width(32), .mode("twosComplement")) comparator_2 (
    .a(R1_WB), .b(32'h22), .eq(comparator_2_eq));  // open: gt, lt
  and and_6 (and_6_out, mem_wb_1_ecall_2, comparator_2_eq);
  not not_7 (not_7_out, comparator_2_eq);
  Adder #(.width(16)) adder_4 (.a(\条件分支成功数 ), .b(\无条件分支数 ), .out(adder_4_out));  // open: cin, cout
  and and_7 (ecall_halt, mem_wb_1_ecall_2, not_7_out);
  not not_8 (not_8_out, Go);
  and and_8 (Stop, ecall_halt, not_8_out, not_9_out);
  Register #(.width(32), .trigger("rising"), .Select("low")) register_1 (
    .D(R2_WB), .en(and_6_out), .Q(LedData), .clk(CLK), .clr(RST));
  not not_9 (not_9_out, RST);
  Multiplier #(.width(16)) multiplier_1 (.a(adder_4_out), .b(16'h2), .out(multiplier_1_out));  // open: cin, cout
  Adder #(.width(16)) adder_5 (.a(multiplier_1_out), .b(\DataRelated次数 ), .out(\插入气泡数 ));  // open: cin, cout
  Multiplexer #(.select(1), .width(1), .disabled("Z"), .enable("false")) multiplexer_10 (
    .in0(1'b0), .in1(1'b1), .out(multiplexer_10_out), .sel(ecall_halt));
  or or_9 (or_9_out, Go, RST);
  Multiplexer #(.select(1), .width(1), .disabled("Z"), .enable("false")) multiplexer_11 (
    .in0(multiplexer_10_out), .in1(1'b0), .out(multiplexer_11_out), .sel(or_9_out));
  D_Flip_Flop #(.trigger("rising"), .Pre_Clr_Positions("ABOVE_BELOW"), .NegatePresetClear("false"), .enable("false"), .NewFFLayout("true")) d_ff_2 (
    .clk(ecall_halt), .D(1'b1), .reset(or_10_out));  // open: Q, Qn, preset
  or or_10 (or_10_out, Go, RST);
  Register #(.width(1), .trigger("rising"), .Select("low")) register_2 (
    .D(multiplexer_11_out), .clk(CLK));  // open: en, Q, clr

  // Other names for the same wires on the sheet: ID_IR (some bits) = Funct; OP[4:0] = ID_IR[6:2]; IR[31:0] = IF_IR;
  //   MEM_PC[31:0] = M_PC; MemWrite_Mem = MemWrite; PC[31:0] = IF_PC; RegWrite_WB = RegWrite

  // Notes on the sheet:
  //   中断源
  //   时空图监测，可删除
  //   中断等待指示
  //   IF
  //   数码管输出
  //   数据相关和ecall触发都暂停
  //   指令存储器
  //   指令字
  //   contents of rom_1 (hex, n*v repeats v):
  //   100493 100006f 100493 200913 300993 100006f 100493 200913 300993 100006f 100493 200913 300993
  //   100006f 100493 200913 300993 29c000ef 100413 100493 1f49493 900533 2200893 73 24d493 48463 fedff06f
  //   900533 2200893 73 100493 249493 900533 2200893 73 48463 fedff06f 100493 1f49493 900533 2200893 73
  //   4034d493 900533 2200893 73 4044d493 900533 2200893 73 4044d493 900533 2200893 73 4044d493 900533
  //   2200893 73 4044d493 900533 2200893 73 4044d493 900533 2200893 73 4044d493 900533 2200893 73 4044d493
  //   900533 2200893 73 100413 1f41993 41f9d993 433 c00913 300b13 140413 f47413 800293 100313 499993
  //   89e9b3 1300533 2200893 73 406282b3 fe0294e3 140413 f00f93 1f47433 1c41413 800293 100313 49d993
  //   89e9b3 1300533 2200893 73 406282b3 fe0294e3 1c45413 406b0b33 b0463 f95ff06f 2b3 fff2c293 829293
  //   ff2e293 500533 2200893 73 fff00413 493 84a023 140413 448493 84a023 140413 448493 84a023 140413
  //   448493 84a023 140413 448493 84a023 140413 448493 84a023 140413 448493 84a023 140413 448493 84a023
  //   140413 448493 84a023 140413 448493 84a023 140413 448493 84a023 140413 448493 84a023 140413 448493
  //   84a023 140413 448493 84a023 140413 448493 84a023 140413 448493 84a023 140413 448493 140413 433
  //   3c00493 42983 4aa03 149a2b3 28663 134a023 1442023 ffc48493 fe9412e3 800533 2200893 73 440413 3c00493
  //   fc9416e3 a00893 73 413 140413 800533 2200893 73 240413 800533 2200893 73 340413 800533 2200893 73
  //   440413 800533 2200893 73 540413 800533 2200893 73 640413 800533 2200893 73 740413 800533 2200893 73
  //   840413 800533 2200893 2200893 73 8067
  //   分支指令插入气泡
  //   控制位
  //   数据相关和ecall触发暂停
  //   流水调试日志用
  //   暂停节拍，不能为0
  //   S立即数
  //   B立即数
  //   J立即数
  //   U立即数
  //   戳工具置1进入计数暂停模式，ctrl+k时钟自动运行到对应节拍暂停
  //   ctrl+k关闭时钟连续运行，将控制位置零，进入单步调试模式调试
  //   JAL
  //   JALR
  //   URET
  //   I立即数
  //   ID
  //   Beq
  //   Bne
  //   MemToReg
  //   MemWrite
  //   AluOP
  //   AluSrcB
  //   RegWrite
  //   可计数暂停的时钟源
  //   下降沿触发
  //   Beq
  //   Bne
  //   MemToReg
  //   MemWrite
  //   AluOP
  //   AluSrcB
  //   RegWrite
  //   JAL
  //   JALR
  //   URET
  //   数据相关和分支指令都插入气泡
  //   为方便自动评测，需要输出流水线各段保存的PC值，注意是PC不是PC+4，另外ID段寄存器写入信息，Mem段内存写入信息也要输出
  //   EX
  //   MemToReg
  //   MemWrite
  //   RegWrite
  //   JAL
  //   JALR
  //   URET
  //   数据存储器
  //   MEM
  //   MemToReg
  //   RegWrite
  //   JAL
  //   JALR
  //   URET
  //   ecall
  //   WB
  //   ecall为1，$a7==34,LED显示$a0的值，否则停机等待GO键
  //   ecall触发时暂停，按下GO继续
  //   气泡流水线不考虑LoadUse
  //   DataRelated插入一个气泡，分支插入2个气泡
  //   ecall触发时暂停，按下GO继续
  //   ecall触发时暂停，按下GO继续
  //   废案
endmodule

module \重定向流水线  (
  output RegWrite,
  output MemWrite,
  output [31:0] IF_PC,
  output [31:0] ID_PC,
  output [31:0] EX_PC,
  output [31:0] M_PC,
  output [31:0] WB_PC,
  output [31:0] RDin,
  output [31:0] MDin,
  output [31:0] LedData
);

  wire AluSrcB_EX, and_1_out, and_2_out, and_3_out, and_4_out, and_5_out, and_6_out, B_Src, Branch, CLK,
       clock_1_out, comparator_1_eq, comparator_1_lt, comparator_2_eq, d_ff_1_q, ecall, ecall_halt, Equ,
       ex_mem_1_ecall_2, ex_mem_1_jal_2, ex_mem_1_jalr_2, ex_mem_1_memtoreg_2, ex_mem_1_uret_2, Go,
       id_ex_1_beq_2, id_ex_1_bne_2, id_ex_1_ecall_2, id_ex_1_memwrite_2, id_ex_1_uret_2, IR1, IR2, IR3, JAL,
       JAL_EX, JAL_WB, JALR, JALR_EX, JALR_WB, LoadUse, mem_wb_1_ecall_2, MemToReg_EX, MemToReg_WB,
       multiplexer_12_out, multiplexer_13_out, nand_1_out, not_1_out, not_2_out, not_3_out, not_4_out,
       not_5_out, not_6_out, not_7_out, not_8_out, not_9_out, or_1_out, or_2_out, or_3_out, or_5_out,
       or_7_out, or_8_out, or_9_out, or_10_out, RegWrite_EX, RegWrite_MEM, RST, S_type, Stop, URET, W1, W2,
       W3, \单周期硬布线控制器_1_alu_src , \单周期硬布线控制器_1_beq , \单周期硬布线控制器_1_bne , \单周期硬布线控制器_1_memtoreg ,
       \单周期硬布线控制器_1_memwrite , \单周期硬布线控制器_1_regwrite ;
  wire [1:0] R1_fwd_EX, R1_fwd_ID, R2_fwd_EX, R2_fwd_ID;
  wire [3:0] AluOP_EX, \单周期硬布线控制器_1_alu_op ;
  wire [4:0] Funct, R1_num, R2_num, W__EX, W__MEM, W__WB;
  wire [12:0] CNT_num;
  wire [15:0] adder_4_out, \LoadUse次数 , multiplier_1_out, \总周期数 , \插入气泡数 , \无条件分支数 , \条件分支成功数 ;
  wire [31:0] AluResult, AluResult_MEM, bit_extender_1_out, bit_extender_2_out, bit_extender_3_out,
       bit_extender_4_out, bit_extender_5_out, EX_IR, ex_mem_1_pc_4_2, ex_mem_1_rega_2, id_ex_1_imm_2,
       id_ex_1_imm_b_2, id_ex_1_imm_j_2, id_ex_1_pc_4_2, id_ex_1_rega_2, id_ex_1_regb_2, ID_IR,
       if_id_1_pc_4_2, IF_IR, imm_U, MEM_IR, mem_wb_1_aluresult_2, mem_wb_1_memdata_2, mem_wb_1_pc_4_2,
       multiplexer_1_out, multiplexer_2_out, multiplexer_3_out, multiplexer_6_out, multiplexer_9_out,
       multiplexer_10_out, PC_4, PC_B, PC_JAL, R1, R1_EX, R1_WB, R2, R2_EX, R2_WB, ram_1_data, shifter_1_out,
       shifter_2_out, WB_IR;

  Button \u_总复位  (.out(RST));
  Button _1 (.out(IR1));
  Button _2 (.out(IR2));
  Button _3 (.out(IR3));
  // Probe on \总周期数 
  // Probe on \总周期数 
  Button \u_继续运行  (.out(Go));
  LED #(.active("true")) led_1 (.in(W1));
  LED #(.active("true")) led_2 (.in(W2));
  LED #(.active("true")) led_3 (.in(W3));
  Hex_Digit_Display hex_digit_display_1 (.value(LedData[31:28]));  // open: dp
  // Probe on IF_PC[19:0]
  // RiscV_Probe riscv_probe_1: pin names not known; wires that end beside it: IF_IR
  Multiplexer #(.select(1), .width(32), .disabled("Z"), .enable("false")) multiplexer_1 (
    .in0(PC_4), .in1(AluResult), .out(multiplexer_1_out), .sel(JALR_EX));
  Hex_Digit_Display hex_digit_display_2 (.value(LedData[23:20]));  // open: dp
  Hex_Digit_Display hex_digit_display_3 (.value(LedData[27:24]));  // open: dp
  // Probe on ID_PC[19:0]
  // RiscV_Probe riscv_probe_2: pin names not known; wires that end beside it: {ID_IR[31], Funct[4], ID_IR[29:26], Funct[3], ID_IR[24:15], Funct[2:0], ID_IR[11:0]}
  Multiplexer #(.select(1), .width(32), .disabled("Z"), .enable("false")) multiplexer_2 (
    .in0(multiplexer_1_out), .in1(PC_JAL), .out(multiplexer_2_out), .sel(JAL_EX));
  Hex_Digit_Display hex_digit_display_4 (.value(LedData[19:16]));  // open: dp
  Hex_Digit_Display hex_digit_display_5 (.value(LedData[15:12]));  // open: dp
  \Load_Use检测  \load_use检测_1  (
    .OP(ID_IR[6:2]), .R1_num(R1_num), .W__EX(W__EX), .LoadUse(LoadUse), .Funct(Funct), .R2_num(R2_num),
    .MemToReg_EX(MemToReg_EX));
  \fwd生成  \fwd生成_1  (
    .OP(ID_IR[6:2]), .R1_num(R1_num), .W__EX(W__EX), .W__MEM(W__MEM), .R1_fwd(R1_fwd_ID), .Funct(Funct),
    .R2_num(R2_num), .RegWrite_EX(RegWrite_EX), .RegWrite_MEM(RegWrite_MEM), .R2_fwd(R2_fwd_ID));
  Multiplexer #(.select(1), .width(32), .disabled("Z"), .enable("false")) multiplexer_3 (
    .in0(multiplexer_2_out), .in1(PC_B), .out(multiplexer_3_out), .sel(B_Src));
  Hex_Digit_Display hex_digit_display_6 (.value(LedData[11:8]));  // open: dp
  Hex_Digit_Display hex_digit_display_7 (.value(LedData[7:4]));  // open: dp
  // Probe on EX_PC[19:0]
  // RiscV_Probe riscv_probe_3: pin names not known; wires that end beside it: EX_IR
  Register #(.width(32), .trigger("rising"), .Select("low")) PC (
    .D(multiplexer_3_out), .en(not_1_out), .Q(IF_PC), .clk(CLK), .clr(RST));
  not not_1 (not_1_out, or_1_out);
  or or_1 (or_1_out, LoadUse, Stop);
  Hex_Digit_Display hex_digit_display_8 (.value(LedData[3:0]));  // open: dp
  not not_2 (not_2_out, Stop);
  // Probe on \总周期数 
  // Probe on M_PC[19:0]
  // RiscV_Probe riscv_probe_4: pin names not known; wires that end beside it: MEM_IR
  Counter #(.width(16), .max('hffff), .ongoal("wrap"), .trigger("rising"), .behavior("new")) counter_1 (
    .count(not_2_out), .Q(\总周期数 ), .clk(CLK), .clr(RST));  // open: load, D, carry, preset, down
  Adder #(.width(32)) adder_1 (.a(IF_PC), .b(32'h4), .out(PC_4), .cin(1'b0));  // open: cout
  // RiscV_Probe riscv_probe_5: pin names not known; wires that end beside it: IF_IR
  // Probe on \总周期数 
  // Probe on \无条件分支数 
  // Probe on \条件分支成功数 
  // Probe on \插入气泡数 
  // Probe on \LoadUse次数 
  ROM #(.addrWidth(10), .dataWidth(32), .Select("high")) rom_1 (.addr(IF_PC[11:2]), .data(IF_IR));
  // Probe on IF_PC[11:0]
  // Probe on WB_PC[19:0]
  // RiscV_Probe riscv_probe_6: pin names not known; wires that end beside it: WB_IR
  IF_ID if_id_1 (
    .PC(IF_PC), .IR(IF_IR), .PC_4(PC_4), .PC_2(ID_PC),
    .IR_2({ID_IR[31], Funct[4], ID_IR[29:26], Funct[3], ID_IR[24:15], Funct[2:0], ID_IR[11:0]}),
    .PC_4_2(if_id_1_pc_4_2), .CLK(CLK), .\RST_为1同步清零 (or_3_out), .\halt_为1暂停 (or_2_out));  // open: predict, predict_2, PredictAddr, PredictAddr_2
  or or_2 (or_2_out, LoadUse, Stop);
  or or_3 (or_3_out, RST, Branch);
  // Probe on ID_PC[11:0]
  // Probe on EX_PC[11:0]
  // Probe on M_PC[11:0]
  D_Flip_Flop #(.trigger("high"), .Pre_Clr_Positions("LEGACY"), .NegatePresetClear("false"), .enable("true"), .NewFFLayout("false")) d_ff_1 (.Q(d_ff_1_q));  // open: clk, D, Qn, preset, en, reset
  // Probe on 13'h8f9
  // Probe on WB_PC[11:0]
  Comparator #(.width(13), .mode("twosComplement")) comparator_1 (
    .a(CNT_num), .b(13'h8f9), .eq(comparator_1_eq), .lt(comparator_1_lt));  // open: gt
  Clock #(.highDuration(1), .lowDuration(1)) clock_1 (.out(clock_1_out));
  \单周期硬布线控制器  \u_单周期硬布线控制器_1  (
    .Funct(Funct), .OP(ID_IR[6:2]), .ALU_OP(\单周期硬布线控制器_1_alu_op ), .MemToReg(\单周期硬布线控制器_1_memtoreg ),
    .MemWrite(\单周期硬布线控制器_1_memwrite ), .ALU_SRC(\单周期硬布线控制器_1_alu_src ), .RegWrite(\单周期硬布线控制器_1_regwrite ),
    .ecall(ecall), .S_type(S_type), .Jalr(JALR), .Beq(\单周期硬布线控制器_1_beq ), .JAL(JAL), .Bne(\单周期硬布线控制器_1_bne ),
    .in_3(ID_IR[21]), .uret(URET));  // open: U_ype, Byte, BGEU
  assign bit_extender_1_out = {{20{ID_IR[31]}}, {ID_IR[31], Funct[4], ID_IR[29:26], Funct[3], ID_IR[11:7]}};  // Bit_Extender bit_extender_1
  // RiscV_Probe riscv_probe_7: pin names not known; wires that end beside it: {ID_IR[31], Funct[4], ID_IR[29:26], Funct[3], ID_IR[24:15], Funct[2:0], ID_IR[11:0]}
  nand nand_1 (nand_1_out, d_ff_1_q, comparator_1_eq);
  Counter #(.width(13), .max('h1fff), .ongoal("stay"), .trigger("rising"), .behavior("old")) counter_2 (
    .count(comparator_1_lt), .Q(CNT_num), .clk(clock_1_out));  // open: load, D, carry, clr, preset
  Multiplexer #(.select(1), .width(5), .disabled("Z"), .enable("false")) multiplexer_4 (
    .in0(ID_IR[19:15]), .in1(5'b10001), .out(R1_num), .sel(ecall));
  Multiplexer #(.select(1), .width(5), .disabled("Z"), .enable("false")) multiplexer_5 (
    .in0(ID_IR[24:20]), .in1(5'b01010), .out(R2_num), .sel(ecall));
  assign bit_extender_2_out = {{20{ID_IR[31]}}, {ID_IR[31], Funct[4], ID_IR[29:26], Funct[3], ID_IR[24:20]}};  // Bit_Extender bit_extender_2
  assign bit_extender_3_out = {{20{ID_IR[31]}}, {ID_IR[31], ID_IR[7], Funct[4], ID_IR[29:26], Funct[3], ID_IR[11:8]}};  // Bit_Extender bit_extender_3
  assign bit_extender_4_out = {{12{ID_IR[31]}}, {ID_IR[31], ID_IR[19:15], Funct[2:0], ID_IR[20], Funct[4], ID_IR[29:26], Funct[3], ID_IR[24:21]}};  // Bit_Extender bit_extender_4
  assign bit_extender_5_out = {{12{ID_IR[31]}}, {ID_IR[31], Funct[4], ID_IR[29:26], Funct[3], ID_IR[24:15], Funct[2:0]}};  // Bit_Extender bit_extender_5
  assign CLK = nand_1_out ? clock_1_out : 1'bz;  // Controlled_Buffer controlled_buffer_1
  Multiplexer #(.select(1), .width(32), .disabled("Z"), .enable("false")) multiplexer_6 (
    .in0(bit_extender_2_out), .in1(bit_extender_1_out), .out(multiplexer_6_out), .sel(S_type));
  Shifter #(.width(32), .shift("ll")) shifter_1 (.in(bit_extender_3_out), .\dist (5'b00001), .out(shifter_1_out));
  Shifter #(.width(32), .shift("ll")) shifter_2 (.in(bit_extender_4_out), .\dist (5'b00001), .out(shifter_2_out));
  Shifter #(.width(32), .shift("ll")) shifter_3 (.in(bit_extender_5_out), .\dist (5'b01100), .out(imm_U));
  Pull_Resistor #(.pull(1)) pull_resistor_1 (.node(CLK));
  Regifile regifile_1 (
    .Din(RDin), .Clk(CLK), .R1(R1), .R2(R2), .WE(RegWrite), .W_num(W__WB), .R1_num(R1_num), .R2_num(R2_num));
  or or_4 (B_Src, and_1_out, and_2_out);
  and and_1 (and_1_out, id_ex_1_beq_2, Equ);
  ID_EX id_ex_1 (
    .PC(ID_PC), .IR({ID_IR[31], Funct[4], ID_IR[29:26], Funct[3], ID_IR[24:15], Funct[2:0], ID_IR[11:0]}),
    .PC_4(if_id_1_pc_4_2), .RegA(R1), .RegB(R2), .imm(multiplexer_6_out), .imm_B(shifter_1_out),
    .imm_J(shifter_2_out), .Beq(\单周期硬布线控制器_1_beq ), .Bne(\单周期硬布线控制器_1_bne ),
    .MemToReg(\单周期硬布线控制器_1_memtoreg ), .MemWrite(\单周期硬布线控制器_1_memwrite ), .AluOP(\单周期硬布线控制器_1_alu_op ),
    .AluSrcB(\单周期硬布线控制器_1_alu_src ), .RegWrite(\单周期硬布线控制器_1_regwrite ), .JAL(JAL), .JALR(JALR), .URET(URET),
    .PC_2(EX_PC), .IR_2(EX_IR), .PC_4_2(id_ex_1_pc_4_2), .RegA_2(id_ex_1_rega_2), .RegB_2(id_ex_1_regb_2),
    .imm_2(id_ex_1_imm_2), .imm_B_2(id_ex_1_imm_b_2), .imm_J_2(id_ex_1_imm_j_2), .Beq_2(id_ex_1_beq_2),
    .Bne_2(id_ex_1_bne_2), .MemToReg_2(MemToReg_EX), .MemWrite_2(id_ex_1_memwrite_2), .AluOP_2(AluOP_EX),
    .AluSrcB_2(AluSrcB_EX), .RegWrite_2(RegWrite_EX), .JAL_2(JAL_EX), .JALR_2(JALR_EX),
    .URET_2(id_ex_1_uret_2), .CLK(CLK), .W_num_2(W__EX), .ecall(ecall), .ecall_2(id_ex_1_ecall_2),
    .\RST_为1同步清零 (or_5_out), .imm_U(imm_U), .W_num(ID_IR[11:7]), .\halt_为1暂停 (Stop), .R1_fwd_ID(R1_fwd_ID),
    .R2_fwd_ID(R2_fwd_ID), .R1_fwd_EX(R1_fwd_EX), .R2_fwd_EX(R2_fwd_EX));  // open: imm_U_2, predict, predict_2, PredictAddr, PredictAddr_2
  or or_5 (or_5_out, RST, LoadUse, Branch);
  and and_2 (and_2_out, id_ex_1_bne_2, not_3_out);
  not not_3 (not_3_out, Equ);
  Adder #(.width(32)) adder_2 (.a(id_ex_1_imm_b_2), .b(EX_PC), .out(PC_B), .cin(1'b0));  // open: cout
  Adder #(.width(32)) adder_3 (.a(id_ex_1_imm_j_2), .b(EX_PC), .out(PC_JAL), .cin(1'b0));  // open: cout
  // RiscV_Probe riscv_probe_8: pin names not known; wires that end beside it: EX_IR
  Multiplexer #(.select(2), .width(32), .disabled("Z"), .enable("false")) multiplexer_7 (
    .in0(id_ex_1_rega_2), .in1(RDin), .in2(AluResult_MEM), .out(R1_EX), .sel(R1_fwd_EX));  // open: in3
  Multiplexer #(.select(2), .width(32), .disabled("Z"), .enable("false")) multiplexer_8 (
    .in0(id_ex_1_regb_2), .in1(RDin), .in2(AluResult_MEM), .out(R2_EX), .sel(R2_fwd_EX));  // open: in3
  or or_6 (Branch, JAL_EX, JALR_EX, B_Src);
  Multiplexer #(.select(1), .width(32), .disabled("Z"), .enable("false")) multiplexer_9 (
    .in0(R2_EX), .in1(id_ex_1_imm_2), .out(multiplexer_9_out), .sel(AluSrcB_EX));
  ALU alu_1 (
    .X(R1_EX), .Y(multiplexer_9_out), .AluOP(AluOP_EX), .Equal(Equ), .Result(AluResult));  // open: Result_2, out_4, out_6
  not not_4 (not_4_out, Stop);
  and and_3 (and_3_out, B_Src, not_4_out);
  Counter #(.width(16), .max('hffff), .ongoal("wrap"), .trigger("rising"), .behavior("new")) counter_3 (
    .count(and_3_out), .Q(\条件分支成功数 ), .clk(CLK), .clr(RST));  // open: load, D, carry, preset, down
  EX_MEM ex_mem_1 (
    .PC(EX_PC), .IR(EX_IR), .PC_4(id_ex_1_pc_4_2), .RegA(R1_EX), .RegWrite(RegWrite_EX), .JAL(JAL_EX),
    .JALR(JALR_EX), .PC_2(M_PC), .IR_2(MEM_IR), .PC_4_2(ex_mem_1_pc_4_2), .RegA_2(ex_mem_1_rega_2),
    .RegB_2(MDin), .MemToReg_2(ex_mem_1_memtoreg_2), .MemWrite_2(MemWrite), .RegWrite_2(RegWrite_MEM),
    .JAL_2(ex_mem_1_jal_2), .JALR_2(ex_mem_1_jalr_2), .URET_2(ex_mem_1_uret_2), .CLK(CLK),
    .AluResult_2(AluResult_MEM), .W_num_2(W__MEM), .ecall_2(ex_mem_1_ecall_2), .\halt_为1暂停 (Stop),
    .RegB(R2_EX), .AluResult(AluResult), .MemToReg(MemToReg_EX), .MemWrite(id_ex_1_memwrite_2),
    .URET(id_ex_1_uret_2), .W_num(W__EX), .ecall(id_ex_1_ecall_2), .\RST_为1同步清零 (RST));  // open: AluOP, AluSrcB, Beq_2, Bne_2, AluOP_2, AluSrcB_2, Beq, Bne
  // RiscV_Probe riscv_probe_9: pin names not known; wires that end beside it: MEM_IR, MEM_IR
  not not_5 (not_5_out, Stop);
  or or_7 (or_7_out, JAL_EX, JALR_EX);
  and and_4 (and_4_out, or_7_out, not_5_out);
  Counter #(.width(16), .max('hffff), .ongoal("wrap"), .trigger("rising"), .behavior("new")) counter_4 (
    .count(and_4_out), .Q(\无条件分支数 ), .clk(CLK), .clr(RST));  // open: load, D, carry, preset, down
  RAM #(.addrWidth(10), .dataWidth(32), .bus("separate"), .Select("high")) ram_1 (
    .addr(AluResult_MEM[11:2]), .din(MDin), .data(ram_1_data), .str(MemWrite), .sel(1'b1), .clk(CLK),
    .ld(1'b1), .clr(RST));
  MEM_WB mem_wb_1 (
    .PC(M_PC), .PC_2(WB_PC), .IR(MEM_IR), .IR_2(WB_IR), .PC_4(ex_mem_1_pc_4_2), .PC_4_2(mem_wb_1_pc_4_2),
    .RegA(ex_mem_1_rega_2), .RegA_2(R1_WB), .RegB(MDin), .RegB_2(R2_WB), .AluResult(AluResult_MEM),
    .AluResult_2(mem_wb_1_aluresult_2), .MemToReg(ex_mem_1_memtoreg_2), .MemToReg_2(MemToReg_WB),
    .RegWrite(RegWrite_MEM), .RegWrite_2(RegWrite), .JAL(ex_mem_1_jal_2), .JAL_2(JAL_WB),
    .JALR(ex_mem_1_jalr_2), .JALR_2(JALR_WB), .URET(ex_mem_1_uret_2), .W_num(W__MEM), .W_num_2(W__WB),
    .ecall(ex_mem_1_ecall_2), .ecall_2(mem_wb_1_ecall_2), .\RST_为1同步清零 (RST), .CLK(CLK), .\halt_为1暂停 (Stop),
    .MemData(ram_1_data), .MemData_2(mem_wb_1_memdata_2));  // open: Beq, Beq_2, Bne, Bne_2, MemWrite, MemWrite_2, AluOP, AluOP_2, AluSrcB, AluSrcB_2, URET_2
  and and_5 (and_5_out, LoadUse, not_6_out);
  Multiplexer #(.select(1), .width(32), .disabled("Z"), .enable("false")) multiplexer_10 (
    .in0(mem_wb_1_aluresult_2), .in1(mem_wb_1_memdata_2), .out(multiplexer_10_out), .sel(MemToReg_WB));
  // RiscV_Probe riscv_probe_10: pin names not known; wires that end beside it: WB_IR, mem_wb_1_pc_4_2
  not not_6 (not_6_out, Stop);
  Counter #(.width(16), .max('hffff), .ongoal("wrap"), .trigger("rising"), .behavior("new")) counter_5 (
    .count(and_5_out), .Q(\LoadUse次数 ), .clk(CLK), .clr(RST));  // open: load, D, carry, preset, down
  or or_8 (or_8_out, JALR_WB, JAL_WB);
  Multiplexer #(.select(1), .width(32), .disabled("Z"), .enable("false")) multiplexer_11 (
    .in0(multiplexer_10_out), .in1(mem_wb_1_pc_4_2), .out(RDin), .sel(or_8_out));
  Comparator #(.width(32), .mode("twosComplement")) comparator_2 (
    .a(R1_WB), .b(32'h22), .eq(comparator_2_eq));  // open: gt, lt
  Adder #(.width(16)) adder_4 (.a(\条件分支成功数 ), .b(\无条件分支数 ), .out(adder_4_out));  // open: cin, cout
  not not_7 (not_7_out, comparator_2_eq);
  and and_6 (and_6_out, mem_wb_1_ecall_2, comparator_2_eq);
  and and_7 (ecall_halt, mem_wb_1_ecall_2, not_7_out);
  not not_8 (not_8_out, Go);
  and and_8 (Stop, ecall_halt, not_8_out, not_9_out);
  Multiplier #(.width(16)) multiplier_1 (.a(adder_4_out), .b(16'h2), .out(multiplier_1_out));  // open: cin, cout
  not not_9 (not_9_out, RST);
  Adder #(.width(16)) adder_5 (.a(multiplier_1_out), .b(\LoadUse次数 ), .out(\插入气泡数 ));  // open: cin, cout
  Register #(.width(32), .trigger("rising"), .Select("low")) register_1 (
    .D(R2_WB), .en(and_6_out), .Q(LedData), .clk(CLK), .clr(RST));
  Multiplexer #(.select(1), .width(1), .disabled("Z"), .enable("false")) multiplexer_12 (
    .in0(1'b0), .in1(1'b1), .out(multiplexer_12_out), .sel(ecall_halt));
  or or_9 (or_9_out, Go, RST);
  Multiplexer #(.select(1), .width(1), .disabled("Z"), .enable("false")) multiplexer_13 (
    .in0(multiplexer_12_out), .in1(1'b0), .out(multiplexer_13_out), .sel(or_9_out));
  D_Flip_Flop #(.trigger("rising"), .Pre_Clr_Positions("ABOVE_BELOW"), .NegatePresetClear("false"), .enable("false"), .NewFFLayout("true")) d_ff_2 (
    .clk(ecall_halt), .D(1'b1), .reset(or_10_out));  // open: Q, Qn, preset
  or or_10 (or_10_out, Go, RST);
  Register #(.width(1), .trigger("rising"), .Select("low")) register_2 (
    .D(multiplexer_13_out), .clk(CLK));  // open: en, Q, clr

  // Other names for the same wires on the sheet: ID_IR (some bits) = Funct; OP[4:0] = ID_IR[6:2]; IR[31:0] = IF_IR;
  //   MEM_PC[31:0] = M_PC; MemWrite_Mem = MemWrite; PC[31:0] = IF_PC; RegWrite_WB = RegWrite

  // Notes on the sheet:
  //   中断源
  //   时空图监测，可删除
  //   中断等待指示
  //   数码管输出
  //   IF
  //   数据相关和ecall触发都暂停
  //   指令存储器
  //   指令字
  //   contents of rom_1 (hex, n*v repeats v):
  //   100493 100006f 100493 200913 300993 100006f 100493 200913 300993 100006f 100493 200913 300993
  //   100006f 100493 200913 300993 29c000ef 100413 100493 1f49493 900533 2200893 73 24d493 48463 fedff06f
  //   900533 2200893 73 100493 249493 900533 2200893 73 48463 fedff06f 100493 1f49493 900533 2200893 73
  //   4034d493 900533 2200893 73 4044d493 900533 2200893 73 4044d493 900533 2200893 73 4044d493 900533
  //   2200893 73 4044d493 900533 2200893 73 4044d493 900533 2200893 73 4044d493 900533 2200893 73 4044d493
  //   900533 2200893 73 100413 1f41993 41f9d993 433 c00913 300b13 140413 f47413 800293 100313 499993
  //   89e9b3 1300533 2200893 73 406282b3 fe0294e3 140413 f00f93 1f47433 1c41413 800293 100313 49d993
  //   89e9b3 1300533 2200893 73 406282b3 fe0294e3 1c45413 406b0b33 b0463 f95ff06f 2b3 fff2c293 829293
  //   ff2e293 500533 2200893 73 fff00413 493 84a023 140413 448493 84a023 140413 448493 84a023 140413
  //   448493 84a023 140413 448493 84a023 140413 448493 84a023 140413 448493 84a023 140413 448493 84a023
  //   140413 448493 84a023 140413 448493 84a023 140413 448493 84a023 140413 448493 84a023 140413 448493
  //   84a023 140413 448493 84a023 140413 448493 84a023 140413 448493 84a023 140413 448493 140413 433
  //   3c00493 42983 4aa03 149a2b3 28663 134a023 1442023 ffc48493 fe9412e3 800533 2200893 73 440413 3c00493
  //   fc9416e3 a00893 73 413 140413 800533 2200893 73 240413 800533 2200893 73 340413 800533 2200893 73
  //   440413 800533 2200893 73 540413 800533 2200893 73 640413 800533 2200893 73 740413 800533 2200893 73
  //   840413 800533 2200893 2200893 73 8067
  //   分支插入气泡
  //   控制位
  //   LoadUse和Ecall指令触发暂停
  //   流水调试日志用
  //   暂停节拍，不能为0
  //   S立即数
  //   B立即数
  //   J立即数
  //   U立即数
  //   戳工具置1进入计数暂停模式，ctrl+k时钟自动运行到对应节拍暂停
  //   ctrl+k关闭时钟连续运行，将控制位置零，进入单步调试模式调试
  //   JAL
  //   JALR
  //   URET
  //   I立即数
  //   ID
  //   Beq
  //   Bne
  //   MemToReg
  //   MemWrite
  //   AluOP
  //   AluSrcB
  //   RegWrite
  //   可计数暂停的时钟源
  //   下降沿触发
  //   Beq
  //   Bne
  //   MemToReg
  //   MemWrite
  //   AluOP
  //   AluSrcB
  //   RegWrite
  //   JAL
  //   JALR
  //   URET
  //   LoadUse和分支插入气泡
  //   为方便自动评测，需要输出流水线各段保存的PC值，注意是PC不是PC+4，另外ID段寄存器写入信息，Mem段内存写入信息也要输出
  //   EX
  //   MemToReg
  //   MemWrite
  //   RegWrite
  //   JAL
  //   JALR
  //   URET
  //   MEM
  //   数据存储器
  //   MemToReg
  //   RegWrite
  //   JALR
  //   URET
  //   JAL
  //   ecall
  //   WB
  //   ecall为1，$a7==34,LED显示$a0的值，否则停机等待GO键
  //   ecall触发时暂停，按下GO继续
  //   LoadUse插入一个气泡，分支插入2个气泡
  //   ecall触发时暂停，按下GO继续
  //   ecall触发时暂停，按下GO继续
  //   废案
endmodule
module \流水线单级中断  (
  input  IR1,
  input  IR2,
  input  IR3,
  output RegWrite,
  output MemWrite,
  output [31:0] IF_PC,
  output [31:0] ID_PC,
  output [31:0] EX_PC,
  output [31:0] M_PC,
  output [31:0] WB_PC,
  output [31:0] RDin,
  output [31:0] MDin,
  output [31:0] LedData
);

  wire AluSrcB_EX, and_1_out, and_2_out, and_3_out, and_5_out, and_6_out, and_7_out, and_8_out, and_9_out,
       and_10_out, B_Src, Branch, CLK, clock_1_out, CLR1, CLR2, CLR3, comparator_1_eq, comparator_1_lt,
       comparator_2_eq, d_ff_1_q, d_ff_2_q, d_ff_3_q, d_ff_5_q, d_ff_6_q, ecall, ecall_halt, Equ,
       ex_mem_1_ecall_2, ex_mem_1_jal_2, ex_mem_1_jalr_2, ex_mem_1_memtoreg_2, ex_mem_1_uret_2, Go,
       id_ex_1_beq_2, id_ex_1_bne_2, id_ex_1_ecall_2, id_ex_1_memwrite_2, IE, INTR, INTR1, INTR2, INTR3,
       IR1_t, IR2_t, IR3_t, IRA, IRB, IRC, IRHAVE, JAL, JAL_EX, JAL_WB, JALR, JALR_EX, JALR_WB, LoadUse,
       mem_wb_1_ecall_2, MemToReg_EX, MemToReg_WB, nand_1_out, not_1_out, not_2_out, not_3_out, not_4_out,
       not_5_out, not_6_out, not_7_out, not_8_out, not_9_out, or_6_out, or_7_out, or_8_out, or_9_out,
       or_12_out, or_13_out, or_14_out, or_15_out, or_18_out, or_19_out, RegWrite_EX, RegWrite_MEM, RST,
       S_type, Stop, URET, URET_EX, W1, W2, W3, \单周期硬布线控制器_1_alu_src , \单周期硬布线控制器_1_beq , \单周期硬布线控制器_1_bne ,
       \单周期硬布线控制器_1_memtoreg , \单周期硬布线控制器_1_memwrite , \单周期硬布线控制器_1_regwrite ;
  wire [1:0] priority_encoder_1_out, priority_encoder_2_out, R1_fwd_EX, R1_fwd_ID, R2_fwd_EX, R2_fwd_ID,
       register_1_q;
  wire [3:0] AluOP_EX, \单周期硬布线控制器_1_alu_op ;
  wire [4:0] Funct, R1_num, R2_num, W__EX, W__MEM, W__WB;
  wire [12:0] CNT_num;
  wire [15:0] adder_4_out, \LoadUse次数 , multiplier_1_out, \总周期数 , \插入气泡数 , \无条件分支数 , \条件分支成功数 ;
  wire [31:0] AluResult, AluResult_MEM, bit_extender_1_out, bit_extender_2_out, bit_extender_3_out,
       bit_extender_4_out, bit_extender_5_out, EX_IR, ex_mem_1_pc_4_2, ex_mem_1_rega_2, id_ex_1_imm_2,
       id_ex_1_imm_b_2, id_ex_1_imm_j_2, id_ex_1_pc_4_2, id_ex_1_rega_2, id_ex_1_regb_2, ID_IR,
       if_id_1_pc_4_2, IF_IR, imm_U, IR_PC, MEM_IR, mem_wb_1_aluresult_2, mem_wb_1_memdata_2,
       mem_wb_1_pc_4_2, MEPC, multiplexer_2_out, multiplexer_3_out, multiplexer_4_out, multiplexer_5_out,
       multiplexer_6_out, multiplexer_7_out, multiplexer_10_out, multiplexer_13_out, multiplexer_14_out,
       PC_4, PC_B, PC_JAL, R1, R1_EX, R1_WB, R2, R2_EX, R2_WB, ram_1_data, shifter_1_out, shifter_2_out,
       WB_IR;

  Button \u_总复位  (.out(RST));
  Button _1 (.out(IRA));
  Button _2 (.out(IRB));
  Button _3 (.out(IRC));
  // Probe on \总周期数 
  // Probe on \总周期数 
  Button \u_继续运行  (.out(Go));
  LED #(.active("true")) led_1 (.in(W1));
  LED #(.active("true")) led_2 (.in(W2));
  LED #(.active("true")) led_3 (.in(W3));
  or or_1 (W1, INTR1, d_ff_1_q);
  or or_2 (W2, INTR2, d_ff_2_q);
  or or_3 (W3, INTR3, d_ff_3_q);
  Hex_Digit_Display hex_digit_display_1 (.value(LedData[31:28]));  // open: dp
  // Probe on IF_PC[19:0]
  // RiscV_Probe riscv_probe_1: pin names not known; wires that end beside it: IF_IR
  or or_4 (IR1_t, IR1, IRA);
  D_Flip_Flop #(.trigger("rising"), .Pre_Clr_Positions("LEGACY"), .NegatePresetClear("false"), .enable("true"), .NewFFLayout("false")) d_ff_1 (
    .clk(IRA), .D(1'b1), .Q(d_ff_1_q), .reset(INTR1));  // open: Qn, preset, en
  D_Flip_Flop #(.trigger("rising"), .Pre_Clr_Positions("LEGACY"), .NegatePresetClear("false"), .enable("true"), .NewFFLayout("false")) d_ff_2 (
    .clk(IRB), .D(1'b1), .Q(d_ff_2_q), .reset(INTR2));  // open: Qn, preset, en
  D_Flip_Flop #(.trigger("rising"), .Pre_Clr_Positions("LEGACY"), .NegatePresetClear("false"), .enable("true"), .NewFFLayout("false")) d_ff_3 (
    .clk(IRC), .D(1'b1), .Q(d_ff_3_q), .reset(INTR3));  // open: Qn, preset, en
  Multiplexer #(.select(2), .width(32), .disabled("Z"), .enable("false")) multiplexer_1 (
    .in0(32'h30ac), .in1(32'h3150), .in2(32'h31f4), .out(IR_PC), .sel(priority_encoder_1_out));  // open: in3
  Priority_Encoder #(.select(2), .disabled("Z")) priority_encoder_1 (
    .in0(INTR1), .in1(INTR2), .in2(INTR3), .out(priority_encoder_1_out));  // open: in3, gs, en_out, en_in
  or or_5 (IRHAVE, INTR1, INTR2, INTR3);
  or or_6 (or_6_out, ~IRHAVE, URET_EX);  // OR_Gate
  Hex_Digit_Display hex_digit_display_2 (.value(LedData[27:24]));  // open: dp
  Hex_Digit_Display hex_digit_display_3 (.value(LedData[23:20]));  // open: dp
  // Probe on ID_PC[19:0]
  // RiscV_Probe riscv_probe_2: pin names not known; wires that end beside it: {ID_IR[31], Funct[4], ID_IR[29:26], Funct[3], ID_IR[24:15], Funct[2:0], ID_IR[11:0]}
  or or_7 (or_7_out, d_ff_1_q, INTR1);
  or or_8 (or_8_out, d_ff_2_q, INTR2);
  or or_9 (or_9_out, d_ff_3_q, INTR3);
  D_Flip_Flop #(.trigger("rising"), .Pre_Clr_Positions("LEGACY"), .NegatePresetClear("false"), .enable("true"), .NewFFLayout("true")) d_ff_4 (
    .clk(CLK), .D(or_6_out), .Q(IE));  // open: Qn, preset, en, reset
  Hex_Digit_Display hex_digit_display_4 (.value(LedData[19:16]));  // open: dp
  Hex_Digit_Display hex_digit_display_5 (.value(LedData[15:12]));  // open: dp
  or or_10 (IR2_t, IR2, IRB);
  and and_1 (and_1_out, or_7_out, ~CLR1);  // AND_Gate
  and and_2 (and_2_out, or_8_out, ~CLR2);  // AND_Gate
  and and_3 (and_3_out, or_9_out, ~CLR3);  // AND_Gate
  Register #(.width(2), .trigger("rising"), .Select("low")) register_1 (
    .D(priority_encoder_1_out), .en(INTR), .Q(register_1_q), .clk(CLK));  // open: clr
  and and_4 (INTR, IRHAVE, IE);
  Hex_Digit_Display hex_digit_display_6 (.value(LedData[11:8]));  // open: dp
  Hex_Digit_Display hex_digit_display_7 (.value(LedData[7:4]));  // open: dp
  // Probe on EX_PC[19:0]
  // RiscV_Probe riscv_probe_3: pin names not known; wires that end beside it: EX_IR
  D_Flip_Flop #(.trigger("rising"), .Pre_Clr_Positions("LEGACY"), .NegatePresetClear("false"), .enable("true"), .NewFFLayout("false")) u_IR1 (
    .clk(CLK), .D(and_1_out), .Q(INTR1));  // open: Qn, preset, en, reset
  D_Flip_Flop #(.trigger("rising"), .Pre_Clr_Positions("LEGACY"), .NegatePresetClear("false"), .enable("true"), .NewFFLayout("false")) IR1_2 (
    .clk(CLK), .D(and_2_out), .Q(INTR2));  // open: Qn, preset, en, reset
  D_Flip_Flop #(.trigger("rising"), .Pre_Clr_Positions("LEGACY"), .NegatePresetClear("false"), .enable("true"), .NewFFLayout("false")) IR1_3 (
    .clk(CLK), .D(and_3_out), .Q(INTR3));  // open: Qn, preset, en, reset
  Demultiplexer #(.select(2), .width(1), .tristate("false"), .disabled("Z"), .enable("false")) demultiplexer_1 (
    .out0(CLR1), .out1(CLR2), .out2(CLR3), .in(URET_EX), .sel(register_1_q));  // open: out3
  Hex_Digit_Display hex_digit_display_8 (.value(LedData[3:0]));  // open: dp
  or or_11 (IR3_t, IR3, IRC);
  // Probe on \总周期数 
  // Probe on M_PC[19:0]
  // RiscV_Probe riscv_probe_4: pin names not known; wires that end beside it: MEM_IR
  // Probe on \总周期数 
  // Probe on \无条件分支数 
  // Probe on \条件分支成功数 
  // Probe on \插入气泡数 
  // Probe on \LoadUse次数 
  Multiplexer #(.select(1), .width(32), .disabled("Z"), .enable("false")) multiplexer_2 (
    .in0(PC_4), .in1(AluResult), .out(multiplexer_2_out), .sel(JALR_EX));
  // Probe on IF_PC[11:0]
  // Probe on WB_PC[19:0]
  // RiscV_Probe riscv_probe_5: pin names not known; wires that end beside it: WB_IR
  Multiplexer #(.select(1), .width(32), .disabled("Z"), .enable("false")) multiplexer_3 (
    .in0(multiplexer_2_out), .in1(PC_JAL), .out(multiplexer_3_out), .sel(JAL_EX));
  D_Flip_Flop #(.trigger("rising"), .Pre_Clr_Positions("LEGACY"), .NegatePresetClear("false"), .enable("true"), .NewFFLayout("false")) d_ff_5 (
    .clk(CLK), .D(URET_EX), .Q(d_ff_5_q));  // open: Qn, preset, en, reset
  // Probe on ID_PC[11:0]
  // Probe on EX_PC[11:0]
  Multiplexer #(.select(1), .width(32), .disabled("Z"), .enable("false")) multiplexer_4 (
    .in0(multiplexer_3_out), .in1(PC_B), .out(multiplexer_4_out), .sel(B_Src));
  Multiplexer #(.select(1), .width(32), .disabled("Z"), .enable("false")) multiplexer_5 (
    .in0(ID_PC), .in1(IF_PC), .out(multiplexer_5_out), .sel(d_ff_5_q));
  // Probe on M_PC[11:0]
  D_Flip_Flop #(.trigger("high"), .Pre_Clr_Positions("LEGACY"), .NegatePresetClear("false"), .enable("true"), .NewFFLayout("false")) d_ff_6 (.Q(d_ff_6_q));  // open: clk, D, Qn, preset, en, reset
  // Probe on 13'h8f9
  Multiplexer #(.select(1), .width(32), .disabled("Z"), .enable("false")) multiplexer_6 (
    .in0(multiplexer_5_out), .in1(multiplexer_4_out), .out(multiplexer_6_out), .sel(Branch));
  // Probe on WB_PC[11:0]
  Comparator #(.width(13), .mode("twosComplement")) comparator_1 (
    .a(CNT_num), .b(13'h8f9), .eq(comparator_1_eq), .lt(comparator_1_lt));  // open: gt
  Clock #(.highDuration(1), .lowDuration(1)) clock_1 (.out(clock_1_out));
  Multiplexer #(.select(2), .width(32), .disabled("Z"), .enable("false")) multiplexer_7 (
    .in0(multiplexer_4_out), .in1(IR_PC), .in2(MEPC), .out(multiplexer_7_out), .sel(priority_encoder_2_out));  // open: in3
  Priority_Encoder #(.select(2), .disabled("Z")) priority_encoder_2 (
    .in0(1'b1), .in1(INTR), .in2(URET_EX), .out(priority_encoder_2_out));  // open: in3, gs, en_out, en_in
  Register #(.width(32), .trigger("rising"), .Select("low")) register_2 (
    .D(multiplexer_6_out), .en(INTR), .Q(MEPC), .clk(CLK));  // open: clr
  nand nand_1 (nand_1_out, d_ff_6_q, comparator_1_eq);
  Counter #(.width(13), .max('h1fff), .ongoal("stay"), .trigger("rising"), .behavior("old")) counter_1 (
    .count(comparator_1_lt), .Q(CNT_num), .clk(clock_1_out));  // open: load, D, carry, clr, preset
  Register #(.width(32), .trigger("rising"), .Select("low")) PC (
    .D(multiplexer_7_out), .en(not_1_out), .Q(IF_PC), .clk(CLK), .clr(RST));
  not not_1 (not_1_out, or_12_out);
  or or_12 (or_12_out, LoadUse, Stop);
  assign CLK = nand_1_out ? clock_1_out : 1'bz;  // Controlled_Buffer controlled_buffer_1
  Pull_Resistor #(.pull(1)) pull_resistor_1 (.node(CLK));
  Adder #(.width(32)) adder_1 (.a(IF_PC), .b(32'h4), .out(PC_4), .cin(1'b0));  // open: cout
  ROM #(.addrWidth(10), .dataWidth(32), .Select("high")) rom_1 (.addr(IF_PC[11:2]), .data(IF_IR));
  // RiscV_Probe riscv_probe_6: pin names not known; wires that end beside it: IF_IR
  or or_13 (or_13_out, URET_EX, RST, Branch, INTR);
  IF_ID if_id_1 (
    .PC(IF_PC), .IR(IF_IR), .PC_4(PC_4), .PC_2(ID_PC),
    .IR_2({ID_IR[31], Funct[4], ID_IR[29:26], Funct[3], ID_IR[24:15], Funct[2:0], ID_IR[11:0]}),
    .PC_4_2(if_id_1_pc_4_2), .CLK(CLK), .\RST_为1同步清零 (or_13_out), .\halt_为1暂停 (or_14_out));  // open: predict, predict_2, PredictAddr, PredictAddr_2
  or or_14 (or_14_out, LoadUse, Stop);
  assign bit_extender_1_out = {{20{ID_IR[31]}}, {ID_IR[31], Funct[4], ID_IR[29:26], Funct[3], ID_IR[11:7]}};  // Bit_Extender bit_extender_1
  // RiscV_Probe riscv_probe_7: pin names not known; wires that end beside it: {ID_IR[31], Funct[4], ID_IR[29:26], Funct[3], ID_IR[24:15], Funct[2:0], ID_IR[11:0]}
  \单周期硬布线控制器  \u_单周期硬布线控制器_1  (
    .Funct(Funct), .OP(ID_IR[6:2]), .ALU_OP(\单周期硬布线控制器_1_alu_op ), .MemToReg(\单周期硬布线控制器_1_memtoreg ),
    .MemWrite(\单周期硬布线控制器_1_memwrite ), .ALU_SRC(\单周期硬布线控制器_1_alu_src ), .RegWrite(\单周期硬布线控制器_1_regwrite ),
    .ecall(ecall), .S_type(S_type), .Jalr(JALR), .Beq(\单周期硬布线控制器_1_beq ), .JAL(JAL), .Bne(\单周期硬布线控制器_1_bne ),
    .in_3(ID_IR[21]), .uret(URET));  // open: U_ype, Byte, BGEU
  assign bit_extender_2_out = {{20{ID_IR[31]}}, {ID_IR[31], Funct[4], ID_IR[29:26], Funct[3], ID_IR[24:20]}};  // Bit_Extender bit_extender_2
  assign bit_extender_3_out = {{20{ID_IR[31]}}, {ID_IR[31], ID_IR[7], Funct[4], ID_IR[29:26], Funct[3], ID_IR[11:8]}};  // Bit_Extender bit_extender_3
  assign bit_extender_4_out = {{12{ID_IR[31]}}, {ID_IR[31], ID_IR[19:15], Funct[2:0], ID_IR[20], Funct[4], ID_IR[29:26], Funct[3], ID_IR[24:21]}};  // Bit_Extender bit_extender_4
  assign bit_extender_5_out = {{12{ID_IR[31]}}, {ID_IR[31], Funct[4], ID_IR[29:26], Funct[3], ID_IR[24:15], Funct[2:0]}};  // Bit_Extender bit_extender_5
  Multiplexer #(.select(1), .width(5), .disabled("Z"), .enable("false")) multiplexer_8 (
    .in0(ID_IR[19:15]), .in1(5'b10001), .out(R1_num), .sel(ecall));
  Multiplexer #(.select(1), .width(5), .disabled("Z"), .enable("false")) multiplexer_9 (
    .in0(ID_IR[24:20]), .in1(5'b01010), .out(R2_num), .sel(ecall));
  Multiplexer #(.select(1), .width(32), .disabled("Z"), .enable("false")) multiplexer_10 (
    .in0(bit_extender_2_out), .in1(bit_extender_1_out), .out(multiplexer_10_out), .sel(S_type));
  Shifter #(.width(32), .shift("ll")) shifter_1 (.in(bit_extender_3_out), .\dist (5'b00001), .out(shifter_1_out));
  Shifter #(.width(32), .shift("ll")) shifter_2 (.in(bit_extender_4_out), .\dist (5'b00001), .out(shifter_2_out));
  Shifter #(.width(32), .shift("ll")) shifter_3 (.in(bit_extender_5_out), .\dist (5'b01100), .out(imm_U));
  Regifile regifile_1 (
    .Din(RDin), .Clk(CLK), .R1(R1), .R2(R2), .WE(RegWrite), .W_num(W__WB), .R1_num(R1_num), .R2_num(R2_num));
  and and_5 (and_5_out, id_ex_1_beq_2, Equ);
  ID_EX id_ex_1 (
    .PC(ID_PC), .IR({ID_IR[31], Funct[4], ID_IR[29:26], Funct[3], ID_IR[24:15], Funct[2:0], ID_IR[11:0]}),
    .PC_4(if_id_1_pc_4_2), .RegA(R1), .RegB(R2), .imm(multiplexer_10_out), .imm_B(shifter_1_out),
    .imm_J(shifter_2_out), .Beq(\单周期硬布线控制器_1_beq ), .Bne(\单周期硬布线控制器_1_bne ),
    .MemToReg(\单周期硬布线控制器_1_memtoreg ), .MemWrite(\单周期硬布线控制器_1_memwrite ), .AluOP(\单周期硬布线控制器_1_alu_op ),
    .AluSrcB(\单周期硬布线控制器_1_alu_src ), .RegWrite(\单周期硬布线控制器_1_regwrite ), .JAL(JAL), .JALR(JALR), .URET(URET),
    .PC_2(EX_PC), .IR_2(EX_IR), .PC_4_2(id_ex_1_pc_4_2), .RegA_2(id_ex_1_rega_2), .RegB_2(id_ex_1_regb_2),
    .imm_2(id_ex_1_imm_2), .imm_B_2(id_ex_1_imm_b_2), .imm_J_2(id_ex_1_imm_j_2), .Beq_2(id_ex_1_beq_2),
    .Bne_2(id_ex_1_bne_2), .MemToReg_2(MemToReg_EX), .MemWrite_2(id_ex_1_memwrite_2), .AluOP_2(AluOP_EX),
    .AluSrcB_2(AluSrcB_EX), .RegWrite_2(RegWrite_EX), .JAL_2(JAL_EX), .JALR_2(JALR_EX), .URET_2(URET_EX),
    .CLK(CLK), .W_num_2(W__EX), .ecall(ecall), .ecall_2(id_ex_1_ecall_2), .\RST_为1同步清零 (or_15_out),
    .imm_U(imm_U), .W_num(ID_IR[11:7]), .\halt_为1暂停 (Stop), .R1_fwd_ID(R1_fwd_ID), .R2_fwd_ID(R2_fwd_ID),
    .R1_fwd_EX(R1_fwd_EX), .R2_fwd_EX(R2_fwd_EX));  // open: imm_U_2, predict, predict_2, PredictAddr, PredictAddr_2
  or or_15 (or_15_out, INTR, RST, LoadUse, Branch, URET_EX);
  or or_16 (B_Src, and_5_out, and_6_out);
  and and_6 (and_6_out, id_ex_1_bne_2, not_2_out);
  not not_2 (not_2_out, Equ);
  // RiscV_Probe riscv_probe_8: pin names not known; wires that end beside it: EX_IR
  Multiplexer #(.select(2), .width(32), .disabled("Z"), .enable("false")) multiplexer_11 (
    .in0(id_ex_1_rega_2), .in1(RDin), .in2(AluResult_MEM), .out(R1_EX), .sel(R1_fwd_EX));  // open: in3
  Multiplexer #(.select(2), .width(32), .disabled("Z"), .enable("false")) multiplexer_12 (
    .in0(id_ex_1_regb_2), .in1(RDin), .in2(AluResult_MEM), .out(R2_EX), .sel(R2_fwd_EX));  // open: in3
  Adder #(.width(32)) adder_2 (.a(id_ex_1_imm_b_2), .b(EX_PC), .out(PC_B), .cin(1'b0));  // open: cout
  Adder #(.width(32)) adder_3 (.a(id_ex_1_imm_j_2), .b(EX_PC), .out(PC_JAL), .cin(1'b0));  // open: cout
  or or_17 (Branch, JAL_EX, JALR_EX, B_Src);
  Adder #(.width(16)) adder_4 (.a(\条件分支成功数 ), .b(\无条件分支数 ), .out(adder_4_out));  // open: cin, cout
  Multiplexer #(.select(1), .width(32), .disabled("Z"), .enable("false")) multiplexer_13 (
    .in0(R2_EX), .in1(id_ex_1_imm_2), .out(multiplexer_13_out), .sel(AluSrcB_EX));
  \Load_Use检测  \load_use检测_1  (
    .OP(ID_IR[6:2]), .R1_num(R1_num), .W__EX(W__EX), .LoadUse(LoadUse), .Funct(Funct), .R2_num(R2_num),
    .MemToReg_EX(MemToReg_EX));
  \fwd生成  \fwd生成_1  (
    .OP(ID_IR[6:2]), .R1_num(R1_num), .W__EX(W__EX), .W__MEM(W__MEM), .R1_fwd(R1_fwd_ID), .Funct(Funct),
    .R2_num(R2_num), .RegWrite_EX(RegWrite_EX), .RegWrite_MEM(RegWrite_MEM), .R2_fwd(R2_fwd_ID));
  Multiplier #(.width(16)) multiplier_1 (.a(adder_4_out), .b(16'h2), .out(multiplier_1_out));  // open: cin, cout
  EX_MEM ex_mem_1 (
    .PC(EX_PC), .IR(EX_IR), .PC_4(id_ex_1_pc_4_2), .RegA(R1_EX), .RegWrite(RegWrite_EX), .JAL(JAL_EX),
    .JALR(JALR_EX), .PC_2(M_PC), .IR_2(MEM_IR), .PC_4_2(ex_mem_1_pc_4_2), .RegA_2(ex_mem_1_rega_2),
    .RegB_2(MDin), .MemToReg_2(ex_mem_1_memtoreg_2), .MemWrite_2(MemWrite), .RegWrite_2(RegWrite_MEM),
    .JAL_2(ex_mem_1_jal_2), .JALR_2(ex_mem_1_jalr_2), .URET_2(ex_mem_1_uret_2), .CLK(CLK),
    .AluResult_2(AluResult_MEM), .W_num_2(W__MEM), .ecall_2(ex_mem_1_ecall_2), .\halt_为1暂停 (Stop),
    .RegB(R2_EX), .AluResult(AluResult), .MemToReg(MemToReg_EX), .MemWrite(id_ex_1_memwrite_2),
    .URET(URET_EX), .W_num(W__EX), .ecall(id_ex_1_ecall_2), .\RST_为1同步清零 (RST));  // open: AluOP, AluSrcB, Beq_2, Bne_2, AluOP_2, AluSrcB_2, Beq, Bne
  ALU alu_1 (
    .X(R1_EX), .Y(multiplexer_13_out), .AluOP(AluOP_EX), .Equal(Equ), .Result(AluResult));  // open: Result_2, out_4, out_6
  not not_3 (not_3_out, Stop);
  Adder #(.width(16)) adder_5 (.a(multiplier_1_out), .b(\LoadUse次数 ), .out(\插入气泡数 ));  // open: cin, cout
  // RiscV_Probe riscv_probe_9: pin names not known; wires that end beside it: MEM_IR, MEM_IR
  Counter #(.width(16), .max('hffff), .ongoal("wrap"), .trigger("rising"), .behavior("new")) counter_2 (
    .count(not_3_out), .Q(\总周期数 ), .clk(CLK), .clr(RST));  // open: load, D, carry, preset, down
  RAM #(.addrWidth(10), .dataWidth(32), .bus("separate"), .Select("high")) ram_1 (
    .addr(AluResult_MEM[11:2]), .din(MDin), .data(ram_1_data), .str(MemWrite), .sel(1'b1), .clk(CLK),
    .ld(1'b1), .clr(RST));
  not not_4 (not_4_out, Stop);
  and and_7 (and_7_out, B_Src, not_4_out);
  Counter #(.width(16), .max('hffff), .ongoal("wrap"), .trigger("rising"), .behavior("new")) counter_3 (
    .count(and_7_out), .Q(\条件分支成功数 ), .clk(CLK), .clr(RST));  // open: load, D, carry, preset, down
  MEM_WB mem_wb_1 (
    .PC(M_PC), .PC_2(WB_PC), .IR(MEM_IR), .IR_2(WB_IR), .PC_4(ex_mem_1_pc_4_2), .PC_4_2(mem_wb_1_pc_4_2),
    .RegA(ex_mem_1_rega_2), .RegA_2(R1_WB), .RegB(MDin), .RegB_2(R2_WB), .AluResult(AluResult_MEM),
    .AluResult_2(mem_wb_1_aluresult_2), .MemToReg(ex_mem_1_memtoreg_2), .MemToReg_2(MemToReg_WB),
    .RegWrite(RegWrite_MEM), .RegWrite_2(RegWrite), .JAL(ex_mem_1_jal_2), .JAL_2(JAL_WB),
    .JALR(ex_mem_1_jalr_2), .JALR_2(JALR_WB), .URET(ex_mem_1_uret_2), .W_num(W__MEM), .W_num_2(W__WB),
    .ecall(ex_mem_1_ecall_2), .ecall_2(mem_wb_1_ecall_2), .\RST_为1同步清零 (RST), .CLK(CLK), .\halt_为1暂停 (Stop),
    .MemData(ram_1_data), .MemData_2(mem_wb_1_memdata_2));  // open: Beq, Beq_2, Bne, Bne_2, MemWrite, MemWrite_2, AluOP, AluOP_2, AluSrcB, AluSrcB_2, URET_2
  Multiplexer #(.select(1), .width(32), .disabled("Z"), .enable("false")) multiplexer_14 (
    .in0(mem_wb_1_aluresult_2), .in1(mem_wb_1_memdata_2), .out(multiplexer_14_out), .sel(MemToReg_WB));
  or or_18 (or_18_out, JALR_WB, JAL_WB);
  // RiscV_Probe riscv_probe_10: pin names not known; wires that end beside it: WB_IR, mem_wb_1_pc_4_2
  not not_5 (not_5_out, Stop);
  or or_19 (or_19_out, JAL_EX, JALR_EX);
  and and_8 (and_8_out, or_19_out, not_5_out);
  Counter #(.width(16), .max('hffff), .ongoal("wrap"), .trigger("rising"), .behavior("new")) counter_4 (
    .count(and_8_out), .Q(\无条件分支数 ), .clk(CLK), .clr(RST));  // open: load, D, carry, preset, down
  Multiplexer #(.select(1), .width(32), .disabled("Z"), .enable("false")) multiplexer_15 (
    .in0(multiplexer_14_out), .in1(mem_wb_1_pc_4_2), .out(RDin), .sel(or_18_out));
  and and_9 (and_9_out, LoadUse, not_6_out);
  Comparator #(.width(32), .mode("twosComplement")) comparator_2 (
    .a(R1_WB), .b(32'h22), .eq(comparator_2_eq));  // open: gt, lt
  not not_6 (not_6_out, Stop);
  Counter #(.width(16), .max('hffff), .ongoal("wrap"), .trigger("rising"), .behavior("new")) counter_5 (
    .count(and_9_out), .Q(\LoadUse次数 ), .clk(CLK), .clr(RST));  // open: load, D, carry, preset, down
  and and_10 (and_10_out, mem_wb_1_ecall_2, comparator_2_eq);
  and and_11 (ecall_halt, mem_wb_1_ecall_2, not_7_out);
  not not_7 (not_7_out, comparator_2_eq);
  not not_8 (not_8_out, Go);
  not not_9 (not_9_out, RST);
  and and_12 (Stop, ecall_halt, not_8_out, not_9_out);
  Register #(.width(32), .trigger("rising"), .Select("low")) register_3 (
    .D(R2_WB), .en(and_10_out), .Q(LedData), .clk(CLK), .clr(RST));

  // Other names for the same wires on the sheet: ID_IR (some bits) = Funct; OP[4:0] = ID_IR[6:2]; IR[31:0] = IF_IR;
  //   MEM_PC[31:0] = M_PC; MemWrite_Mem = MemWrite; PC[31:0] = IF_PC; RegWrite_WB = RegWrite

  // Notes on the sheet:
  //   中断源
  //   时空图监测，可删除
  //   中断等待指示
  //   识别中断类型找地址
  //   中断响应阶段
  //   中断使能位(用于开关中断)
  //   数码管输出
  //   Reset 
  //   Reset 
  //   Reset 
  //   判断中断使能
  //   清除中断
  //   中断响应
  //   控制位
  //   流水调试日志用
  //   暂停节拍，不能为0
  //   保存断点
  //   戳工具置1进入计数暂停模式，ctrl+k时钟自动运行到对应节拍暂停
  //   ctrl+k关闭时钟连续运行，将控制位置零，进入单步调试模式调试
  //   IF
  //   数据相关和ecall触发都暂停
  //   可计数暂停的时钟源
  //   指令存储器
  //   指令字
  //   contents of rom_1 (hex, n*v repeats v):
  //   7d000113 100413 1f41993 41f9d993 433 c00913 800b13 140413 f47413 800293 100313 499993 89e9b3 1300533
  //   2200893 73 406282b3 fe0294e3 140413 f00f93 1f47433 1c41413 800293 100313 49d993 89e9b3 1300533
  //   2200893 73 406282b3 fe0294e3 1c45413 406b0b33 b0463 f95ff06f 2b3 fff2c293 1029293 fff2e293 500533
  //   2200893 73 f5dff06f 1112023 410113 a12023 410113 812023 410113 1312023 410113 1412023 410113 1512023
  //   410113 1612023 410113 100b13 300a13 100a93 1600433 441413 14469b3 1300533 2200893 73 fe0416e3
  //   415a0a33 fe0a10e3 ffc10113 12b03 ffc10113 12a83 ffc10113 12a03 ffc10113 12983 ffc10113 12403
  //   ffc10113 12503 ffc10113 12883 200073 1112023 410113 a12023 410113 812023 410113 1312023 410113
  //   1412023 410113 1512023 410113 1612023 410113 200b13 300a13 100a93 1600433 441413 14469b3 1300533
  //   2200893 73 fe0416e3 415a0a33 fe0a10e3 ffc10113 12b03 ffc10113 12a83 ffc10113 12a03 ffc10113 12983
  //   ffc10113 12403 ffc10113 12503 ffc10113 12883 200073 1112023 410113 a12023 410113 812023 410113
  //   1312023 410113 1412023 410113 1512023 410113 1612023 410113 300b13 300a13 100a93 1600433 441413
  //   14469b3 1300533 2200893 73 fe0416e3 415a0a33 fe0a10e3 ffc10113 12b03 ffc10113 12a83 ffc10113 12a03
  //   ffc10113 12983 ffc10113 12403 ffc10113 12503 ffc10113 12883 200073
  //   分支插入气泡
  //   为方便自动评测，需要输出流水线各段保存的PC值，注意是PC不是PC+4，另外ID段寄存器写入信息，Mem段内存写入信息也要输出
  //   LoadUse和Ecall指令触发暂停
  //   JAL
  //   JALR
  //   URET
  //   I立即数
  //   S立即数
  //   B立即数
  //   J立即数
  //   U立即数
  //   Beq
  //   Bne
  //   MemToReg
  //   MemWrite
  //   AluOP
  //   AluSrcB
  //   RegWrite
  //   ID
  //   下降沿触发
  //   LoadUse和分支插入气泡
  //   Beq
  //   Bne
  //   MemToReg
  //   MemWrite
  //   AluOP
  //   AluSrcB
  //   RegWrite
  //   JAL
  //   JALR
  //   URET
  //   EX
  //   MemToReg
  //   MemWrite
  //   LoadUse插入一个气泡，分支插入2个气泡
  //   RegWrite
  //   JAL
  //   JALR
  //   URET
  //   MEM
  //   数据存储器
  //   MemToReg
  //   RegWrite
  //   JAL
  //   JALR
  //   URET
  //   ecall
  //   WB
  //   ecall为1，$a7==34,LED显示$a0的值，否则停机等待GO键
  //   ecall触发时暂停，按下GO继续
endmodule

module \动态分支预测  (
  output RegWrite,
  output MemWrite,
  output [31:0] IF_PC,
  output [31:0] ID_PC,
  output [31:0] EX_PC,
  output [31:0] M_PC,
  output [31:0] WB_PC,
  output [31:0] RDin,
  output [31:0] MDin,
  output [31:0] LedData
);

  wire AluSrcB_EX, and_2_out, and_3_out, and_4_out, and_5_out, and_6_out, and_7_out, and_8_out,
       B_Instruction, B_Src, Branch, branchtargetbuffer_1_predictjump, CLK, clock_1_out, comparator_1_eq,
       comparator_2_eq, comparator_2_lt, comparator_3_eq, comparator_4_eq, d_ff_1_q, ecall, ecall_EX,
       ecall_halt, Equ, ex_mem_1_ecall_2, ex_mem_1_jal_2, ex_mem_1_jalr_2, ex_mem_1_memtoreg_2,
       ex_mem_1_uret_2, Go, id_ex_1_beq_2, id_ex_1_bne_2, id_ex_1_memwrite_2, id_ex_1_uret_2,
       if_id_1_predict_2, IR1, IR2, IR3, JAL, JAL_EX, JAL_WB, JALR, JALR_EX, JALR_WB, LoadUse,
       mem_wb_1_ecall_2, MemToReg_EX, MemToReg_WB, multiplexer_5_out, multiplexer_15_out, multiplexer_16_out,
       nand_1_out, not_1_out, not_2_out, not_3_out, not_4_out, not_5_out, not_6_out, not_7_out, not_8_out,
       not_9_out, not_10_out, or_1_out, or_3_out, or_4_out, or_7_out, or_9_out, or_10_out, or_11_out,
       or_12_out, Perror, Predict_EX, RegWrite_EX, RegWrite_MEM, RST, S_type, Stop, URET, W1, W2, W3,
       xor_1_out, \单周期硬布线控制器_1_alu_src , \单周期硬布线控制器_1_beq , \单周期硬布线控制器_1_bne , \单周期硬布线控制器_1_memtoreg ,
       \单周期硬布线控制器_1_memwrite , \单周期硬布线控制器_1_regwrite ;
  wire [1:0] R1_fwd_EX, R1_fwd_ID, R2_fwd_EX, R2_fwd_ID;
  wire [3:0] AluOP_EX, \单周期硬布线控制器_1_alu_op ;
  wire [4:0] Funct, R1_num, R2_num, W__EX, W__MEM, W__WB;
  wire [12:0] CNT_num;
  wire [15:0] adder_5_out, \LoadUse次数 , multiplier_1_out, \总周期数 , \插入气泡数 , \无条件分支数 , \条件分支成功数 ;
  wire [31:0] adder_1_out, AluResult, AluResult_MEM, and_1_out, bit_extender_1_out, bit_extender_2_out,
       bit_extender_3_out, bit_extender_4_out, bit_extender_5_out, BranchAddr,
       branchtargetbuffer_1_predictaddr, EX_IR, ex_mem_1_pc_4_2, ex_mem_1_rega_2, id_ex_1_imm_2,
       id_ex_1_imm_b_2, id_ex_1_imm_j_2, id_ex_1_pc_4_2, id_ex_1_rega_2, id_ex_1_regb_2, ID_IR,
       if_id_1_pc_4_2, if_id_1_predictaddr_2, IF_IR, imm_U, MEM_IR, mem_wb_1_aluresult_2, mem_wb_1_memdata_2,
       mem_wb_1_pc_4_2, multiplexer_1_out, multiplexer_3_out, multiplexer_4_out, multiplexer_6_out,
       multiplexer_9_out, multiplexer_12_out, multiplexer_13_out, PC_4, PC_B, PC_JAL, PredictAddr_EX, R1,
       R1_EX, R1_WB, R2, R2_EX, R2_WB, ram_1_data, register_2_q, shifter_1_out, shifter_2_out, WB_IR;

  Button \u_总复位  (.out(RST));
  Button _1 (.out(IR1));
  Button _2 (.out(IR2));
  Button _3 (.out(IR3));
  // Probe on \总周期数 
  // Probe on \总周期数 
  assign and_1_out = AluResult & 32'hfffffffe;  // AND_Gate and_1, 32 bits wide
  Button \u_继续运行  (.out(Go));
  LED #(.active("true")) led_1 (.in(W1));
  LED #(.active("true")) led_2 (.in(W2));
  LED #(.active("true")) led_3 (.in(W3));
  Multiplexer #(.select(1), .width(32), .disabled("Z"), .enable("false")) multiplexer_1 (
    .in0(PC_JAL), .in1(and_1_out), .out(multiplexer_1_out), .sel(JALR_EX));
  Hex_Digit_Display hex_digit_display_1 (.value(LedData[31:28]));  // open: dp
  // Probe on IF_PC[19:0]
  // RiscV_Probe riscv_probe_1: pin names not known; wires that end beside it: IF_IR
  Multiplexer #(.select(1), .width(32), .disabled("Z"), .enable("false")) multiplexer_2 (
    .in0(multiplexer_1_out), .in1(PC_B), .out(BranchAddr), .sel(B_Src));
  Adder #(.width(32)) adder_1 (.a(EX_PC), .b(32'h4), .out(adder_1_out));  // open: cin, cout
  Comparator #(.width(32), .mode("twosComplement")) comparator_1 (
    .a(BranchAddr), .b(PredictAddr_EX), .eq(comparator_1_eq));  // open: gt, lt
  Hex_Digit_Display hex_digit_display_2 (.value(LedData[27:24]));  // open: dp
  Hex_Digit_Display hex_digit_display_3 (.value(LedData[23:20]));  // open: dp
  // Probe on ID_PC[19:0]
  // RiscV_Probe riscv_probe_2: pin names not known; wires that end beside it: {ID_IR[31], Funct[4], ID_IR[29:26], Funct[3], ID_IR[24:15], Funct[2:0], ID_IR[11:0]}
  Multiplexer #(.select(1), .width(32), .disabled("Z"), .enable("false")) multiplexer_3 (
    .in0(adder_1_out), .in1(BranchAddr), .out(multiplexer_3_out), .sel(Branch));
  Multiplexer #(.select(1), .width(32), .disabled("Z"), .enable("false")) multiplexer_4 (
    .in0(PC_4), .in1(branchtargetbuffer_1_predictaddr), .out(multiplexer_4_out),
    .sel(branchtargetbuffer_1_predictjump));
  BranchTargetBuffer branchtargetbuffer_1 (
    .CLK(CLK), .PC(IF_PC), .EX_BRANCHTAKEN(Branch), .EX_BRANCH(B_Instruction), .EX_PC(EX_PC),
    .EX_BRANCHADDR(BranchAddr), .PREDICTJUMP(branchtargetbuffer_1_predictjump),
    .PREDICTADDR(branchtargetbuffer_1_predictaddr));
  xor xor_1 (xor_1_out, Branch, Predict_EX);
  Multiplexer #(.select(1), .width(1), .disabled("Z"), .enable("false")) multiplexer_5 (
    .in0(1'b0), .in1(not_1_out), .out(multiplexer_5_out), .sel(Branch));
  not not_1 (not_1_out, comparator_1_eq);
  Hex_Digit_Display hex_digit_display_4 (.value(LedData[15:12]));  // open: dp
  Hex_Digit_Display hex_digit_display_5 (.value(LedData[19:16]));  // open: dp
  Clock #(.highDuration(1), .lowDuration(1)) clock_1 (.out(clock_1_out));
  \Load_Use检测  \load_use检测_1  (
    .OP(ID_IR[6:2]), .R1_num(R1_num), .W__EX(W__EX), .LoadUse(LoadUse), .Funct(Funct), .R2_num(R2_num),
    .MemToReg_EX(MemToReg_EX));
  \fwd生成  \fwd生成_1  (
    .OP(ID_IR[6:2]), .R1_num(R1_num), .W__EX(W__EX), .W__MEM(W__MEM), .R1_fwd(R1_fwd_ID), .Funct(Funct),
    .R2_num(R2_num), .RegWrite_EX(RegWrite_EX), .RegWrite_MEM(RegWrite_MEM), .R2_fwd(R2_fwd_ID));
  Multiplexer #(.select(1), .width(32), .disabled("Z"), .enable("false")) multiplexer_6 (
    .in0(multiplexer_4_out), .in1(multiplexer_3_out), .out(multiplexer_6_out), .sel(Perror));
  Hex_Digit_Display hex_digit_display_6 (.value(LedData[7:4]));  // open: dp
  Hex_Digit_Display hex_digit_display_7 (.value(LedData[11:8]));  // open: dp
  // Probe on EX_PC[19:0]
  // RiscV_Probe riscv_probe_3: pin names not known; wires that end beside it: EX_IR
  Register #(.width(32), .trigger("rising"), .Select("low")) PC (
    .D(multiplexer_6_out), .en(not_2_out), .Q(IF_PC), .clk(CLK), .clr(RST));
  not not_2 (not_2_out, or_1_out);
  or or_1 (or_1_out, LoadUse, Stop);
  buf or_2 (Perror, xor_1_out);  // OR_Gate
  Hex_Digit_Display hex_digit_display_8 (.value(LedData[3:0]));  // open: dp
  not not_3 (not_3_out, Stop);
  // Probe on \总周期数 
  // Probe on M_PC[19:0]
  // RiscV_Probe riscv_probe_4: pin names not known; wires that end beside it: MEM_IR
  Counter #(.width(16), .max('hffff), .ongoal("wrap"), .trigger("rising"), .behavior("new")) counter_1 (
    .count(not_3_out), .Q(\总周期数 ), .clk(CLK), .clr(RST));  // open: load, D, carry, preset, down
  Adder #(.width(32)) adder_2 (.a(IF_PC), .b(32'h4), .out(PC_4), .cin(1'b0));  // open: cout
  // RiscV_Probe riscv_probe_5: pin names not known; wires that end beside it: IF_IR
  // Probe on \总周期数 
  // Probe on \无条件分支数 
  // Probe on \条件分支成功数 
  // Probe on \插入气泡数 
  // Probe on \LoadUse次数 
  ROM #(.addrWidth(10), .dataWidth(32), .Select("high")) rom_1 (.addr(IF_PC[11:2]), .data(IF_IR));
  // Probe on IF_PC[11:0]
  // Probe on WB_PC[19:0]
  // RiscV_Probe riscv_probe_6: pin names not known; wires that end beside it: WB_IR
  IF_ID if_id_1 (
    .PC(IF_PC), .IR(IF_IR), .PC_4(PC_4), .PC_2(ID_PC),
    .IR_2({ID_IR[31], Funct[4], ID_IR[29:26], Funct[3], ID_IR[24:15], Funct[2:0], ID_IR[11:0]}),
    .PC_4_2(if_id_1_pc_4_2), .CLK(CLK), .\RST_为1同步清零 (or_4_out), .\halt_为1暂停 (or_3_out),
    .predict(branchtargetbuffer_1_predictjump), .predict_2(if_id_1_predict_2),
    .PredictAddr(branchtargetbuffer_1_predictaddr), .PredictAddr_2(if_id_1_predictaddr_2));
  or or_3 (or_3_out, LoadUse, Stop);
  or or_4 (or_4_out, RST, Perror);
  // Probe on ID_PC[11:0]
  // Probe on EX_PC[11:0]
  // Probe on M_PC[11:0]
  D_Flip_Flop #(.trigger("high"), .Pre_Clr_Positions("LEGACY"), .NegatePresetClear("false"), .enable("true"), .NewFFLayout("false")) d_ff_1 (.Q(d_ff_1_q));  // open: clk, D, Qn, preset, en, reset
  // Probe on 13'h30e
  // Probe on WB_PC[11:0]
  Comparator #(.width(13), .mode("twosComplement")) comparator_2 (
    .a(CNT_num), .b(13'h30e), .eq(comparator_2_eq), .lt(comparator_2_lt));  // open: gt
  \单周期硬布线控制器  \u_单周期硬布线控制器_1  (
    .Funct(Funct), .OP(ID_IR[6:2]), .ALU_OP(\单周期硬布线控制器_1_alu_op ), .MemToReg(\单周期硬布线控制器_1_memtoreg ),
    .MemWrite(\单周期硬布线控制器_1_memwrite ), .ALU_SRC(\单周期硬布线控制器_1_alu_src ), .RegWrite(\单周期硬布线控制器_1_regwrite ),
    .ecall(ecall), .S_type(S_type), .Jalr(JALR), .Beq(\单周期硬布线控制器_1_beq ), .JAL(JAL), .Bne(\单周期硬布线控制器_1_bne ),
    .in_3(ID_IR[21]), .uret(URET));  // open: U_ype, Byte, BGEU
  assign bit_extender_1_out = {{20{ID_IR[31]}}, {ID_IR[31], Funct[4], ID_IR[29:26], Funct[3], ID_IR[11:7]}};  // Bit_Extender bit_extender_1
  // RiscV_Probe riscv_probe_7: pin names not known; wires that end beside it: {ID_IR[31], Funct[4], ID_IR[29:26], Funct[3], ID_IR[24:15], Funct[2:0], ID_IR[11:0]}
  nand nand_1 (nand_1_out, d_ff_1_q, comparator_2_eq);
  Counter #(.width(13), .max('h1fff), .ongoal("stay"), .trigger("rising"), .behavior("old")) counter_2 (
    .count(comparator_2_lt), .Q(CNT_num), .clk(clock_1_out));  // open: load, D, carry, clr, preset
  Multiplexer #(.select(1), .width(5), .disabled("Z"), .enable("false")) multiplexer_7 (
    .in0(ID_IR[19:15]), .in1(5'b10001), .out(R1_num), .sel(ecall));
  Multiplexer #(.select(1), .width(5), .disabled("Z"), .enable("false")) multiplexer_8 (
    .in0(ID_IR[24:20]), .in1(5'b01010), .out(R2_num), .sel(ecall));
  assign bit_extender_2_out = {{20{ID_IR[31]}}, {ID_IR[31], Funct[4], ID_IR[29:26], Funct[3], ID_IR[24:20]}};  // Bit_Extender bit_extender_2
  assign bit_extender_3_out = {{20{ID_IR[31]}}, {ID_IR[31], ID_IR[7], Funct[4], ID_IR[29:26], Funct[3], ID_IR[11:8]}};  // Bit_Extender bit_extender_3
  assign bit_extender_4_out = {{12{ID_IR[31]}}, {ID_IR[31], ID_IR[19:15], Funct[2:0], ID_IR[20], Funct[4], ID_IR[29:26], Funct[3], ID_IR[24:21]}};  // Bit_Extender bit_extender_4
  assign bit_extender_5_out = {{12{ID_IR[31]}}, {ID_IR[31], Funct[4], ID_IR[29:26], Funct[3], ID_IR[24:15], Funct[2:0]}};  // Bit_Extender bit_extender_5
  assign CLK = nand_1_out ? clock_1_out : 1'bz;  // Controlled_Buffer controlled_buffer_1
  Multiplexer #(.select(1), .width(32), .disabled("Z"), .enable("false")) multiplexer_9 (
    .in0(bit_extender_2_out), .in1(bit_extender_1_out), .out(multiplexer_9_out), .sel(S_type));
  Shifter #(.width(32), .shift("ll")) shifter_1 (.in(bit_extender_3_out), .\dist (5'b00001), .out(shifter_1_out));
  Shifter #(.width(32), .shift("ll")) shifter_2 (.in(bit_extender_4_out), .\dist (5'b00001), .out(shifter_2_out));
  Shifter #(.width(32), .shift("ll")) shifter_3 (.in(bit_extender_5_out), .\dist (5'b01100), .out(imm_U));
  Pull_Resistor #(.pull(1)) pull_resistor_1 (.node(CLK));
  or or_5 (B_Instruction, JAL_EX, JALR_EX, id_ex_1_bne_2, id_ex_1_beq_2);
  Regifile regifile_1 (
    .Din(RDin), .Clk(CLK), .R1(R1), .R2(R2), .WE(RegWrite), .W_num(W__WB), .R1_num(R1_num), .R2_num(R2_num));
  or or_6 (B_Src, and_2_out, and_3_out);
  and and_2 (and_2_out, id_ex_1_beq_2, Equ);
  ID_EX id_ex_1 (
    .PC(ID_PC), .IR({ID_IR[31], Funct[4], ID_IR[29:26], Funct[3], ID_IR[24:15], Funct[2:0], ID_IR[11:0]}),
    .PC_4(if_id_1_pc_4_2), .RegA(R1), .RegB(R2), .imm(multiplexer_9_out), .imm_B(shifter_1_out),
    .imm_J(shifter_2_out), .Beq(\单周期硬布线控制器_1_beq ), .Bne(\单周期硬布线控制器_1_bne ),
    .MemToReg(\单周期硬布线控制器_1_memtoreg ), .MemWrite(\单周期硬布线控制器_1_memwrite ), .AluOP(\单周期硬布线控制器_1_alu_op ),
    .AluSrcB(\单周期硬布线控制器_1_alu_src ), .RegWrite(\单周期硬布线控制器_1_regwrite ), .JAL(JAL), .JALR(JALR), .URET(URET),
    .PC_2(EX_PC), .IR_2(EX_IR), .PC_4_2(id_ex_1_pc_4_2), .RegA_2(id_ex_1_rega_2), .RegB_2(id_ex_1_regb_2),
    .imm_2(id_ex_1_imm_2), .imm_B_2(id_ex_1_imm_b_2), .imm_J_2(id_ex_1_imm_j_2), .Beq_2(id_ex_1_beq_2),
    .Bne_2(id_ex_1_bne_2), .MemToReg_2(MemToReg_EX), .MemWrite_2(id_ex_1_memwrite_2), .AluOP_2(AluOP_EX),
    .AluSrcB_2(AluSrcB_EX), .RegWrite_2(RegWrite_EX), .JAL_2(JAL_EX), .JALR_2(JALR_EX),
    .URET_2(id_ex_1_uret_2), .CLK(CLK), .W_num_2(W__EX), .ecall(ecall), .ecall_2(ecall_EX),
    .\RST_为1同步清零 (or_7_out), .imm_U(imm_U), .W_num(ID_IR[11:7]), .\halt_为1暂停 (Stop), .R1_fwd_ID(R1_fwd_ID),
    .R2_fwd_ID(R2_fwd_ID), .R1_fwd_EX(R1_fwd_EX), .R2_fwd_EX(R2_fwd_EX), .predict(if_id_1_predict_2),
    .predict_2(Predict_EX), .PredictAddr(if_id_1_predictaddr_2), .PredictAddr_2(PredictAddr_EX));  // open: imm_U_2
  or or_7 (or_7_out, RST, LoadUse, Perror);
  and and_3 (and_3_out, id_ex_1_bne_2, not_4_out);
  not not_4 (not_4_out, Equ);
  Adder #(.width(32)) adder_3 (.a(id_ex_1_imm_b_2), .b(EX_PC), .out(PC_B), .cin(1'b0));  // open: cout
  Adder #(.width(32)) adder_4 (.a(id_ex_1_imm_j_2), .b(EX_PC), .out(PC_JAL), .cin(1'b0));  // open: cout
  // RiscV_Probe riscv_probe_8: pin names not known; wires that end beside it: EX_IR
  Multiplexer #(.select(2), .width(32), .disabled("Z"), .enable("false")) multiplexer_10 (
    .in0(id_ex_1_rega_2), .in1(RDin), .in2(AluResult_MEM), .out(R1_EX), .sel(R1_fwd_EX));  // open: in3
  Multiplexer #(.select(2), .width(32), .disabled("Z"), .enable("false")) multiplexer_11 (
    .in0(id_ex_1_regb_2), .in1(RDin), .in2(AluResult_MEM), .out(R2_EX), .sel(R2_fwd_EX));  // open: in3
  or or_8 (Branch, JAL_EX, JALR_EX, B_Src);
  Multiplexer #(.select(1), .width(32), .disabled("Z"), .enable("false")) multiplexer_12 (
    .in0(R2_EX), .in1(id_ex_1_imm_2), .out(multiplexer_12_out), .sel(AluSrcB_EX));
  ALU alu_1 (
    .X(R1_EX), .Y(multiplexer_12_out), .AluOP(AluOP_EX), .Equal(Equ), .Result(AluResult));  // open: Result_2, out_4, out_6
  not not_5 (not_5_out, Stop);
  and and_4 (and_4_out, B_Src, not_5_out);
  Counter #(.width(16), .max('hffff), .ongoal("wrap"), .trigger("rising"), .behavior("new")) counter_3 (
    .count(and_4_out), .Q(\条件分支成功数 ), .clk(CLK), .clr(RST));  // open: load, D, carry, preset, down
  EX_MEM ex_mem_1 (
    .PC(EX_PC), .IR(EX_IR), .PC_4(id_ex_1_pc_4_2), .RegA(R1_EX), .RegWrite(RegWrite_EX), .JAL(JAL_EX),
    .JALR(JALR_EX), .PC_2(M_PC), .IR_2(MEM_IR), .PC_4_2(ex_mem_1_pc_4_2), .RegA_2(ex_mem_1_rega_2),
    .RegB_2(MDin), .MemToReg_2(ex_mem_1_memtoreg_2), .MemWrite_2(MemWrite), .RegWrite_2(RegWrite_MEM),
    .JAL_2(ex_mem_1_jal_2), .JALR_2(ex_mem_1_jalr_2), .URET_2(ex_mem_1_uret_2), .CLK(CLK),
    .AluResult_2(AluResult_MEM), .W_num_2(W__MEM), .ecall_2(ex_mem_1_ecall_2), .\halt_为1暂停 (Stop),
    .RegB(R2_EX), .AluResult(AluResult), .MemToReg(MemToReg_EX), .MemWrite(id_ex_1_memwrite_2),
    .URET(id_ex_1_uret_2), .W_num(W__EX), .ecall(ecall_EX), .\RST_为1同步清零 (RST));  // open: AluOP, AluSrcB, Beq_2, Bne_2, AluOP_2, AluSrcB_2, Beq, Bne
  // RiscV_Probe riscv_probe_9: pin names not known; wires that end beside it: MEM_IR, MEM_IR
  not not_6 (not_6_out, Stop);
  or or_9 (or_9_out, JAL_EX, JALR_EX);
  and and_5 (and_5_out, or_9_out, not_6_out);
  Counter #(.width(16), .max('hffff), .ongoal("wrap"), .trigger("rising"), .behavior("new")) counter_4 (
    .count(and_5_out), .Q(\无条件分支数 ), .clk(CLK), .clr(RST));  // open: load, D, carry, preset, down
  RAM #(.addrWidth(10), .dataWidth(32), .bus("separate"), .Select("high")) ram_1 (
    .addr(AluResult_MEM[11:2]), .din(MDin), .data(ram_1_data), .str(MemWrite), .sel(1'b1), .clk(CLK),
    .ld(1'b1), .clr(RST));
  MEM_WB mem_wb_1 (
    .PC(M_PC), .PC_2(WB_PC), .IR(MEM_IR), .IR_2(WB_IR), .PC_4(ex_mem_1_pc_4_2), .PC_4_2(mem_wb_1_pc_4_2),
    .RegA(ex_mem_1_rega_2), .RegA_2(R1_WB), .RegB(MDin), .RegB_2(R2_WB), .AluResult(AluResult_MEM),
    .AluResult_2(mem_wb_1_aluresult_2), .MemToReg(ex_mem_1_memtoreg_2), .MemToReg_2(MemToReg_WB),
    .RegWrite(RegWrite_MEM), .RegWrite_2(RegWrite), .JAL(ex_mem_1_jal_2), .JAL_2(JAL_WB),
    .JALR(ex_mem_1_jalr_2), .JALR_2(JALR_WB), .URET(ex_mem_1_uret_2), .W_num(W__MEM), .W_num_2(W__WB),
    .ecall(ex_mem_1_ecall_2), .ecall_2(mem_wb_1_ecall_2), .\RST_为1同步清零 (RST), .CLK(CLK), .\halt_为1暂停 (Stop),
    .MemData(ram_1_data), .MemData_2(mem_wb_1_memdata_2));  // open: Beq, Beq_2, Bne, Bne_2, MemWrite, MemWrite_2, AluOP, AluOP_2, AluSrcB, AluSrcB_2, URET_2
  and and_6 (and_6_out, LoadUse, not_7_out);
  Multiplexer #(.select(1), .width(32), .disabled("Z"), .enable("false")) multiplexer_13 (
    .in0(mem_wb_1_aluresult_2), .in1(mem_wb_1_memdata_2), .out(multiplexer_13_out), .sel(MemToReg_WB));
  // RiscV_Probe riscv_probe_10: pin names not known; wires that end beside it: WB_IR, mem_wb_1_pc_4_2
  not not_7 (not_7_out, Stop);
  Counter #(.width(16), .max('hffff), .ongoal("wrap"), .trigger("rising"), .behavior("new")) counter_5 (
    .count(and_6_out), .Q(\LoadUse次数 ), .clk(CLK), .clr(RST));  // open: load, D, carry, preset, down
  or or_10 (or_10_out, JALR_WB, JAL_WB);
  Multiplexer #(.select(1), .width(32), .disabled("Z"), .enable("false")) multiplexer_14 (
    .in0(multiplexer_13_out), .in1(mem_wb_1_pc_4_2), .out(RDin), .sel(or_10_out));
  Comparator #(.width(32), .mode("twosComplement")) comparator_3 (
    .a(R1_WB), .b(32'h22), .eq(comparator_3_eq));  // open: gt, lt
  Adder #(.width(16)) adder_5 (.a(\条件分支成功数 ), .b(\无条件分支数 ), .out(adder_5_out));  // open: cin, cout
  Comparator #(.width(32), .mode("twosComplement")) comparator_4 (
    .a(R1_EX), .b(32'h22), .eq(comparator_4_eq));  // open: gt, lt
  not not_8 (not_8_out, comparator_3_eq);
  and and_7 (and_7_out, ecall_EX, comparator_4_eq);
  and and_8 (and_8_out, mem_wb_1_ecall_2, comparator_3_eq);
  and and_9 (ecall_halt, mem_wb_1_ecall_2, not_8_out);
  not not_9 (not_9_out, Go);
  and and_10 (Stop, ecall_halt, not_9_out, not_10_out);
  Multiplier #(.width(16)) multiplier_1 (.a(adder_5_out), .b(16'h2), .out(multiplier_1_out));  // open: cin, cout
  not not_10 (not_10_out, RST);
  Adder #(.width(16)) adder_6 (.a(multiplier_1_out), .b(\LoadUse次数 ), .out(\插入气泡数 ));  // open: cin, cout
  Register #(.width(32), .trigger("rising"), .Select("low")) register_1 (
    .D(R2_EX), .en(and_7_out), .Q(LedData), .clk(CLK), .clr(RST));
  Register #(.width(32), .trigger("rising"), .Select("low")) register_2 (
    .D(R2_WB), .en(and_8_out), .Q(register_2_q), .clk(CLK), .clr(RST));
  Multiplexer #(.select(1), .width(1), .disabled("Z"), .enable("false")) multiplexer_15 (
    .in0(1'b0), .in1(1'b1), .out(multiplexer_15_out), .sel(ecall_halt));
  or or_11 (or_11_out, Go, RST);
  Multiplexer #(.select(1), .width(1), .disabled("Z"), .enable("false")) multiplexer_16 (
    .in0(multiplexer_15_out), .in1(1'b0), .out(multiplexer_16_out), .sel(or_11_out));
  D_Flip_Flop #(.trigger("rising"), .Pre_Clr_Positions("ABOVE_BELOW"), .NegatePresetClear("false"), .enable("false"), .NewFFLayout("true")) d_ff_2 (
    .clk(ecall_halt), .D(1'b1), .reset(or_12_out));  // open: Q, Qn, preset
  or or_12 (or_12_out, Go, RST);
  Register #(.width(1), .trigger("rising"), .Select("low")) register_3 (
    .D(multiplexer_16_out), .clk(CLK));  // open: en, Q, clr

  // Other names for the same wires on the sheet: ID_IR (some bits) = Funct; OP[4:0] = ID_IR[6:2]; IR[31:0] = IF_IR;
  //   MEM_PC[31:0] = M_PC; MemWrite_Mem = MemWrite; PC[31:0] = IF_PC; RegWrite_WB = RegWrite

  // Notes on the sheet:
  //   中断源
  //   时空图监测，可删除
  //   中断等待指示
  //   数码管输出
  //   IF
  //   数据相关和ecall触发都暂停
  //   指令存储器
  //   指令字
  //   contents of rom_1 (hex, n*v repeats v):
  //   100493 100006f 100493 200913 300993 100006f 100493 200913 300993 100006f 100493 200913 300993
  //   100006f 100493 200913 300993 29c000ef 100413 100493 1f49493 900533 2200893 73 24d493 48463 fedff06f
  //   900533 2200893 73 100493 249493 900533 2200893 73 48463 fedff06f 100493 1f49493 900533 2200893 73
  //   4034d493 900533 2200893 73 4044d493 900533 2200893 73 4044d493 900533 2200893 73 4044d493 900533
  //   2200893 73 4044d493 900533 2200893 73 4044d493 900533 2200893 73 4044d493 900533 2200893 73 4044d493
  //   900533 2200893 73 100413 1f41993 41f9d993 433 c00913 300b13 140413 f47413 800293 100313 499993
  //   89e9b3 1300533 2200893 73 406282b3 fe0294e3 140413 f00f93 1f47433 1c41413 800293 100313 49d993
  //   89e9b3 1300533 2200893 73 406282b3 fe0294e3 1c45413 406b0b33 b0463 f95ff06f 2b3 fff2c293 829293
  //   ff2e293 500533 2200893 73 fff00413 493 84a023 140413 448493 84a023 140413 448493 84a023 140413
  //   448493 84a023 140413 448493 84a023 140413 448493 84a023 140413 448493 84a023 140413 448493 84a023
  //   140413 448493 84a023 140413 448493 84a023 140413 448493 84a023 140413 448493 84a023 140413 448493
  //   84a023 140413 448493 84a023 140413 448493 84a023 140413 448493 84a023 140413 448493 140413 433
  //   3c00493 42983 4aa03 149a2b3 28663 134a023 1442023 ffc48493 fe9412e3 800533 2200893 73 440413 3c00493
  //   fc9416e3 a00893 73 413 140413 800533 2200893 73 240413 800533 2200893 73 340413 800533 2200893 73
  //   440413 800533 2200893 73 540413 800533 2200893 73 640413 800533 2200893 73 740413 800533 2200893 73
  //   840413 800533 2200893 2200893 73 8067
  //   分支插入气泡
  //   控制位
  //   LoadUse和Ecall指令触发暂停
  //   流水调试日志用
  //   暂停节拍，不能为0
  //   S立即数
  //   B立即数
  //   J立即数
  //   U立即数
  //   戳工具置1进入计数暂停模式，ctrl+k时钟自动运行到对应节拍暂停
  //   ctrl+k关闭时钟连续运行，将控制位置零，进入单步调试模式调试
  //   JAL
  //   JALR
  //   URET
  //   I立即数
  //   ID
  //   Beq
  //   Bne
  //   MemToReg
  //   MemWrite
  //   AluOP
  //   AluSrcB
  //   RegWrite
  //   可计数暂停的时钟源
  //   下降沿触发
  //   Beq
  //   Bne
  //   MemToReg
  //   MemWrite
  //   AluOP
  //   AluSrcB
  //   RegWrite
  //   JAL
  //   JALR
  //   URET
  //   LoadUse和分支插入气泡
  //   为方便自动评测，需要输出流水线各段保存的PC值，注意是PC不是PC+4，另外ID段寄存器写入信息，Mem段内存写入信息也要输出
  //   EX
  //   MemToReg
  //   MemWrite
  //   RegWrite
  //   JAL
  //   JALR
  //   URET
  //   MEM
  //   数据存储器
  //   MemToReg
  //   RegWrite
  //   JALR
  //   URET
  //   JAL
  //   ecall
  //   WB
  //   ecall为1，$a7==34,LED显示$a0的值，否则停机等待GO键
  //   ecall触发时暂停，按下GO继续
  //   LoadUse插入一个气泡，分支插入2个气泡
  //   ecall触发时暂停，按下GO继续
  //   ecall触发时暂停，按下GO继续
  //   废案
endmodule

module \中断按键参考电路  (
  input  \同步清零信号 ,
  output \与中断屏蔽位与 
);

  wire \_1号中断_out , and_1_out, clock_1_out, d_ff_1_q, or_1_out, or_2_out;

  Clock #(.highDuration(1), .lowDuration(1)) clock_1 (.out(clock_1_out));
  Button \_1号中断  (.out(\_1号中断_out ));
  or or_1 (or_1_out, \与中断屏蔽位与 , d_ff_1_q);
  LED #(.active("true")) \_1号中断等待指示灯  (.in(or_1_out));
  D_Flip_Flop #(.trigger("rising"), .Pre_Clr_Positions("LEGACY"), .NegatePresetClear("false"), .enable("true"), .NewFFLayout("false")) d_ff_1 (
    .clk(\_1号中断_out ), .D(1'b1), .Q(d_ff_1_q), .reset(\与中断屏蔽位与 ));  // open: Qn, preset, en
  or or_2 (or_2_out, d_ff_1_q, \与中断屏蔽位与 );
  and and_1 (and_1_out, or_2_out, ~\同步清零信号 );  // AND_Gate
  D_Flip_Flop #(.trigger("rising"), .Pre_Clr_Positions("LEGACY"), .NegatePresetClear("false"), .enable("true"), .NewFFLayout("false")) IR1 (
    .clk(clock_1_out), .D(and_1_out), .Q(\与中断屏蔽位与 ));  // open: Qn, preset, en, reset

  // Notes on the sheet:
  //   中断信号采样参考电路
  //   Reset 
endmodule

module \单周期_单级中断  (
  input  IR1,
  input  IR2,
  input  IR3,
  output RegWrite,
  output MemWrite,
  output [31:0] PC,
  output [31:0] IR,
  output [31:0] RDin,
  output [31:0] MDin,
  output [31:0] LedData
);

  wire CLK, clock_1_out, comparator_1_eq, comparator_2_eq, comparator_3_eq, comparator_4_eq, comparator_5_eq,
       comparator_5_lt, d_ff_1_q, Go, IR1_t, IR2_t, IR3_t, IRA, IRB, IRC, nand_1_out, or_1_out, W1, W2, W3;
  wire [12:0] CNT_num;
  wire [15:0] \总周期数 ;

  Button \u_继续运行  (.out(Go));
  Button _1 ();  // open: out
  Button _2 ();  // open: out
  Button _3 ();  // open: out
  LED #(.active("true")) led_1 (.in(W1));
  LED #(.active("true")) led_2 (.in(W2));
  LED #(.active("true")) led_3 (.in(W3));
  Hex_Digit_Display hex_digit_display_1 (.value(LedData[31:28]));  // open: dp
  Comparator #(.width(16), .mode("twosComplement")) comparator_1 (
    .a(16'h23b), .b(\总周期数 ), .eq(comparator_1_eq));  // open: gt, lt
  Comparator #(.width(16), .mode("twosComplement")) comparator_2 (
    .a(\总周期数 ), .b(16'h1), .eq(comparator_2_eq));  // open: gt, lt
  Comparator #(.width(16), .mode("twosComplement")) comparator_3 (
    .a(\总周期数 ), .b(16'h4), .eq(comparator_3_eq));  // open: gt, lt
  Comparator #(.width(16), .mode("twosComplement")) comparator_4 (
    .a(\总周期数 ), .b(16'h7), .eq(comparator_4_eq));  // open: gt, lt
  Hex_Digit_Display hex_digit_display_2 (.value(LedData[27:24]));  // open: dp
  Hex_Digit_Display hex_digit_display_3 (.value(LedData[23:20]));  // open: dp
  or or_1 (or_1_out, comparator_1_eq, comparator_2_eq);
  assign IRA = or_1_out ? ~CLK : 1'bz;  // Controlled_Inverter controlled_inverter_1
  assign IRB = comparator_3_eq ? ~CLK : 1'bz;  // Controlled_Inverter controlled_inverter_2
  assign IRC = comparator_4_eq ? ~CLK : 1'bz;  // Controlled_Inverter controlled_inverter_3
  Hex_Digit_Display hex_digit_display_4 (.value(LedData[15:12]));  // open: dp
  Hex_Digit_Display hex_digit_display_5 (.value(LedData[19:16]));  // open: dp
  Pull_Resistor #(.pull(0)) pull_resistor_1 (.node(IRA));
  Pull_Resistor #(.pull(0)) pull_resistor_2 (.node(IRB));
  Pull_Resistor #(.pull(0)) pull_resistor_3 (.node(IRC));
  Hex_Digit_Display hex_digit_display_6 (.value(LedData[7:4]));  // open: dp
  Hex_Digit_Display hex_digit_display_7 (.value(LedData[11:8]));  // open: dp
  // Probe on \总周期数 
  Hex_Digit_Display hex_digit_display_8 (.value(LedData[3:0]));  // open: dp
  or or_2 (IR1_t, IR1, IRA);
  or or_3 (IR2_t, IR2, IRB);
  or or_4 (IR3_t, IR3, IRC);
  D_Flip_Flop #(.trigger("high"), .Pre_Clr_Positions("LEGACY"), .NegatePresetClear("false"), .enable("true"), .NewFFLayout("false")) d_ff_1 (.Q(d_ff_1_q));  // open: clk, D, Qn, preset, en, reset
  // Probe on 13'hc
  Comparator #(.width(13), .mode("twosComplement")) comparator_5 (
    .a(CNT_num), .b(13'hc), .eq(comparator_5_eq), .lt(comparator_5_lt));  // open: gt
  Clock #(.highDuration(1), .lowDuration(1)) clock_1 (.out(clock_1_out));
  Counter #(.width(13), .max('h1fff), .ongoal("stay"), .trigger("rising"), .behavior("old")) counter_1 (
    .count(comparator_5_lt), .Q(CNT_num), .clk(clock_1_out));  // open: load, D, carry, clr, preset
  nand nand_1 (nand_1_out, d_ff_1_q, comparator_5_eq);
  assign CLK = nand_1_out ? clock_1_out : 1'bz;  // Controlled_Buffer controlled_buffer_1
  Pull_Resistor #(.pull(1)) pull_resistor_4 (.node(CLK));

  // Notes on the sheet:
  //   中断源
  //   中断等待指示
  //   总复位信号应将除ROM以外所有存储组件全部清零
  //   单级中断测试信号模拟器
  //   数码管输出
  //   数码管输出应该用寄存器锁存，否则显示数据只能一闪而过
  //   为方便自动评测，需要输出PC，IR，寄存器堆写如数据RDin
  //   RAM写使能MemWrite、RAM写入数据MDin等信号
  //   控制位
  //   暂停节拍，不能为0
  //   戳工具置1进入计数暂停模式，ctrl+k时钟自动运行到对应节拍暂停
  //   ctrl+k关闭时钟连续运行，将控制位置零，进入单步调试模式调试
  //   可计数暂停的时钟源
endmodule

module \单周期_多级中断  (
  input  IR1,
  input  IR2,
  input  IR3,
  output RegWrite,
  output MemWrite,
  output [31:0] PC,
  output [31:0] IR,
  output [31:0] RDin,
  output [31:0] MDin,
  output [31:0] LedData
);

  wire CLK, clock_1_out, comparator_1_eq, comparator_2_eq, comparator_3_eq, comparator_4_eq, comparator_5_eq,
       comparator_6_eq, comparator_6_lt, d_ff_1_q, Go, IR1_t, IR2_t, IR3_t, IRA, IRB, IRC, nand_1_out,
       or_1_out, or_2_out, W1, W2, W3;
  wire [12:0] CNT_num;
  wire [15:0] \总周期数 ;

  Button \u_继续运行  (.out(Go));
  Button _1 ();  // open: out
  Button _2 ();  // open: out
  Button _3 ();  // open: out
  LED #(.active("true")) led_1 (.in(W1));
  LED #(.active("true")) led_2 (.in(W2));
  LED #(.active("true")) led_3 (.in(W3));
  Hex_Digit_Display hex_digit_display_1 (.value(LedData[31:28]));  // open: dp
  Comparator #(.width(16), .mode("twosComplement")) comparator_1 (
    .a(\总周期数 ), .b(16'h7), .eq(comparator_1_eq));  // open: gt, lt
  Comparator #(.width(16), .mode("twosComplement")) comparator_2 (
    .a(\总周期数 ), .b(16'h241), .eq(comparator_2_eq));  // open: gt, lt
  Hex_Digit_Display hex_digit_display_2 (.value(LedData[27:24]));  // open: dp
  Hex_Digit_Display hex_digit_display_3 (.value(LedData[23:20]));  // open: dp
  Comparator #(.width(16), .mode("twosComplement")) comparator_3 (
    .a(16'h258), .b(\总周期数 ), .eq(comparator_3_eq));  // open: gt, lt
  or or_1 (or_1_out, comparator_3_eq, comparator_4_eq);
  Comparator #(.width(16), .mode("twosComplement")) comparator_4 (
    .a(\总周期数 ), .b(16'h1), .eq(comparator_4_eq));  // open: gt, lt
  Comparator #(.width(16), .mode("twosComplement")) comparator_5 (
    .a(\总周期数 ), .b(16'h4), .eq(comparator_5_eq));  // open: gt, lt
  or or_2 (or_2_out, comparator_1_eq, comparator_2_eq);
  Hex_Digit_Display hex_digit_display_4 (.value(LedData[19:16]));  // open: dp
  Hex_Digit_Display hex_digit_display_5 (.value(LedData[15:12]));  // open: dp
  Pull_Resistor #(.pull(0)) pull_resistor_1 (.node(IRA));
  assign IRA = or_1_out ? ~CLK : 1'bz;  // Controlled_Inverter controlled_inverter_1
  Pull_Resistor #(.pull(0)) pull_resistor_2 (.node(IRB));
  assign IRB = comparator_5_eq ? ~CLK : 1'bz;  // Controlled_Inverter controlled_inverter_2
  Pull_Resistor #(.pull(0)) pull_resistor_3 (.node(IRC));
  assign IRC = or_2_out ? ~CLK : 1'bz;  // Controlled_Inverter controlled_inverter_3
  Hex_Digit_Display hex_digit_display_6 (.value(LedData[7:4]));  // open: dp
  Hex_Digit_Display hex_digit_display_7 (.value(LedData[11:8]));  // open: dp
  // Probe on \总周期数 
  Hex_Digit_Display hex_digit_display_8 (.value(LedData[3:0]));  // open: dp
  or or_3 (IR1_t, IR1, IRA);
  or or_4 (IR2_t, IR2, IRB);
  or or_5 (IR3_t, IR3, IRC);
  D_Flip_Flop #(.trigger("high"), .Pre_Clr_Positions("LEGACY"), .NegatePresetClear("false"), .enable("true"), .NewFFLayout("false")) d_ff_1 (.Q(d_ff_1_q));  // open: clk, D, Qn, preset, en, reset
  // Probe on 13'hc
  Comparator #(.width(13), .mode("twosComplement")) comparator_6 (
    .a(CNT_num), .b(13'hc), .eq(comparator_6_eq), .lt(comparator_6_lt));  // open: gt
  Clock #(.highDuration(1), .lowDuration(1)) clock_1 (.out(clock_1_out));
  Counter #(.width(13), .max('h1fff), .ongoal("stay"), .trigger("rising"), .behavior("old")) counter_1 (
    .count(comparator_6_lt), .Q(CNT_num), .clk(clock_1_out));  // open: load, D, carry, clr, preset
  nand nand_1 (nand_1_out, d_ff_1_q, comparator_6_eq);
  assign CLK = nand_1_out ? clock_1_out : 1'bz;  // Controlled_Buffer controlled_buffer_1
  Pull_Resistor #(.pull(1)) pull_resistor_4 (.node(CLK));

  // Notes on the sheet:
  //   中断源
  //   中断等待指示
  //   总复位信号应将除ROM以外所有存储组件全部清零
  //   多级中断测试信号模拟器
  //   数码管输出
  //   数码管输出应该用寄存器锁存，否则显示数据只能一闪而过
  //   为方便自动评测，需要输出PC，IR，寄存器堆写如数据RDin
  //   RAM写使能MemWrite、RAM写入数据MDin等信号
  //   控制位
  //   暂停节拍，不能为0
  //   戳工具置1进入计数暂停模式，ctrl+k时钟自动运行到对应节拍暂停
  //   ctrl+k关闭时钟连续运行，将控制位置零，进入单步调试模式调试
  //   可计数暂停的时钟源
endmodule

module \封装正确性测试  (
);

  wire IR1, IR2, IR3, MemW, RegW;
  wire [31:0] EX_PC, ID_PC, IF_PC, IR, LED, MDin, MDinr, MEM_PC, PC, RDin, RDinr, WB_PC;

  \单周期RISC_V  \u_单周期risc_v_1  (
    .IR1(IR1), .IR2(IR2), .IR3(IR3), .RegWrite(RegW), .MemWrite(MemW), .PC(PC), .IR(IR), .RDin(RDin),
    .MDin(MDin), .LedData(LED));
  \气泡流水线  \u_气泡流水线_1  (
    .RegWrite(RegW), .MemWrite(MemW), .IF_PC(IF_PC), .ID_PC(ID_PC), .EX_PC(EX_PC), .M_PC(MEM_PC),
    .WB_PC(WB_PC), .RDin(RDinr), .MDin(MDinr), .LedData(LED));
  \单周期_单级中断  \u_单周期_单级中断_1  (
    .IR1(IR1), .IR2(IR2), .IR3(IR3), .RegWrite(RegW), .MemWrite(MemW), .PC(PC), .IR(IR), .RDin(RDin),
    .MDin(MDin), .LedData(LED));
  \理想流水线  \u_理想流水线_1  (
    .RegWrite(RegW), .MemWrite(MemW), .IF_PC(IF_PC), .ID_PC(ID_PC), .EX_PC(EX_PC), .M_PC(MEM_PC),
    .WB_PC(WB_PC), .RDin(RDinr), .MDin(MDinr), .LedData(LED));
  \重定向流水线  \u_重定向流水线_1  (
    .RegWrite(RegW), .MemWrite(MemW), .IF_PC(IF_PC), .ID_PC(ID_PC), .EX_PC(EX_PC), .M_PC(MEM_PC),
    .WB_PC(WB_PC), .RDin(RDinr), .MDin(MDinr), .LedData(LED));
  \单周期_多级中断  \u_单周期_多级中断_1  (
    .IR1(IR1), .IR2(IR2), .IR3(IR3), .RegWrite(RegW), .MemWrite(MemW), .PC(PC), .IR(IR), .RDin(RDin),
    .MDin(MDin), .LedData(LED));

  // Notes on the sheet:
  //   单周期封装测试
  //   气泡流水封装测试
  //   单周期+单级中断封装测试
  //   请检查上面封装有无位宽不匹配，引脚标签是否和连接的标签相对应，否则无法在educoder平台上正确测试
  //   理想流水封装测试
  //   重定向流水封装测试
  //   单周期+多级中断封装测试
endmodule

module \立即数生成  (
  input  [31:0] \指令 ,
  input  [31:0] I,
  input  [31:0] S,
  input  [31:0] B,
  input  [31:0] U,
  input  [31:0] J
);

  wire [31:0] bit_extender_3_out, bit_extender_4_out, bit_extender_5_out;

  assign I = {{20{\指令 [31]}}, \指令 [31:20]};  // Bit_Extender bit_extender_1
  assign S = {{20{\指令 [31]}}, {\指令 [31:25], \指令 [11:7]}};  // Bit_Extender bit_extender_2
  assign bit_extender_3_out = {{20{\指令 [31]}}, {\指令 [31], \指令 [7], \指令 [30:25], \指令 [11:8]}};  // Bit_Extender bit_extender_3
  assign bit_extender_4_out = {{12{\指令 [31]}}, \指令 [31:12]};  // Bit_Extender bit_extender_4
  Shifter #(.width(32), .shift("ll")) shifter_1 (.in(bit_extender_4_out), .\dist (5'b10010), .out(U));
  assign bit_extender_5_out = {{12{\指令 [31]}}, {\指令 [31], \指令 [19:12], \指令 [20], \指令 [30:21]}};  // Bit_Extender bit_extender_5
  Shifter #(.width(32), .shift("ll")) shifter_2 (.in(bit_extender_3_out), .\dist (5'b00001), .out(B));
  Shifter #(.width(32), .shift("ll")) shifter_3 (.in(bit_extender_5_out), .\dist (5'b00001), .out(J));

  // Other names for the same wires on the sheet: inst[31:0] = \指令 
endmodule

module IF_ID (
  input  [31:0] PC,
  input  [31:0] IR,
  input  [31:0] PC_4,
  input  [31:0] PredictAddr,
  input  predict,
  input  CLK,
  input  \RST_为1同步清零 ,
  input  \halt_为1暂停 ,
  output [31:0] PC_2,
  output [31:0] IR_2,
  output [31:0] PC_4_2,
  output [31:0] PredictAddr_2,
  output predict_2
);

  wire and_5_out, not_1_out, not_2_out, undriven, undriven_2, undriven_3;
  wire [31:0] and_1_out, and_2_out, and_3_out, and_4_out, bit_extender_1_out;

  not not_1 (not_1_out, \RST_为1同步清零 );
  assign bit_extender_1_out = {{31{not_1_out}}, not_1_out};  // Bit_Extender bit_extender_1
  assign and_1_out = PC & bit_extender_1_out;  // AND_Gate and_1, 32 bits wide
  assign and_2_out = IR & bit_extender_1_out;  // AND_Gate and_2, 32 bits wide
  assign and_3_out = PC_4 & bit_extender_1_out;  // AND_Gate and_3, 32 bits wide
  assign and_4_out = PredictAddr & bit_extender_1_out;  // AND_Gate and_4, 32 bits wide
  and and_5 (and_5_out, predict, not_1_out);
  Register #(.width(32), .trigger("rising"), .Select("low")) register_1 (
    .D(and_1_out), .en(not_2_out), .Q(PC_2), .clk(CLK));  // open: clr
  Register #(.width(32), .trigger("rising"), .Select("low")) register_2 (
    .D(and_2_out), .en(not_2_out), .Q(IR_2), .clk(CLK), .clr(undriven));
  Register #(.width(32), .trigger("rising"), .Select("low")) register_3 (
    .D(and_3_out), .en(not_2_out), .Q(PC_4_2), .clk(CLK), .clr(undriven_2));
  Register #(.width(32), .trigger("rising"), .Select("low")) register_4 (
    .D(and_4_out), .en(not_2_out), .Q(PredictAddr_2), .clk(CLK), .clr(undriven_3));
  Register #(.width(1), .trigger("rising"), .Select("low")) register_5 (
    .D(and_5_out), .en(not_2_out), .Q(predict_2), .clk(CLK));  // open: clr
  not not_2 (not_2_out, \halt_为1暂停 );
endmodule

module ID_EX (
  input  [31:0] PC,
  input  [31:0] IR,
  input  [31:0] PC_4,
  input  [31:0] RegA,
  input  [31:0] RegB,
  input  [31:0] imm,
  input  [31:0] imm_B,
  input  [31:0] imm_J,
  input  [31:0] imm_U,
  input  [31:0] PredictAddr,
  input  Beq,
  input  Bne,
  input  MemToReg,
  input  MemWrite,
  input  [3:0] AluOP,
  input  AluSrcB,
  input  RegWrite,
  input  JAL,
  input  JALR,
  input  URET,
  input  [4:0] W_num,
  input  ecall,
  input  [1:0] R1_fwd_ID,
  input  [1:0] R2_fwd_ID,
  input  predict,
  input  \RST_为1同步清零 ,
  input  CLK,
  input  \halt_为1暂停 ,
  output [31:0] PC_2,
  output [31:0] IR_2,
  output [31:0] PC_4_2,
  output [31:0] RegA_2,
  output [31:0] RegB_2,
  output [31:0] imm_2,
  output [31:0] imm_B_2,
  output [31:0] imm_J_2,
  output [31:0] imm_U_2,
  output [31:0] PredictAddr_2,
  output Beq_2,
  output Bne_2,
  output MemToReg_2,
  output MemWrite_2,
  output [3:0] AluOP_2,
  output AluSrcB_2,
  output RegWrite_2,
  output JAL_2,
  output JALR_2,
  output URET_2,
  output [4:0] W_num_2,
  output ecall_2,
  output [1:0] R1_fwd_EX,
  output [1:0] R2_fwd_EX,
  output predict_2
);

  wire and_11_out, and_12_out, and_13_out, and_14_out, and_16_out, and_17_out, and_18_out, and_19_out,
       and_20_out, and_22_out, and_25_out, not_1_out, not_2_out, undriven, undriven_2, undriven_3,
       undriven_4, undriven_5, undriven_6, undriven_7, undriven_8, undriven_9, undriven_10, undriven_11,
       undriven_12, undriven_13, undriven_14, undriven_15, undriven_16, undriven_17, undriven_18;
  wire [1:0] and_23_out, and_24_out, bit_extender_3_out, bit_extender_4_out;
  wire [3:0] and_15_out, bit_extender_1_out;
  wire [4:0] and_21_out, bit_extender_2_out;
  wire [31:0] and_1_out, and_2_out, and_3_out, and_4_out, and_5_out, and_6_out, and_7_out, and_8_out,
       and_9_out, and_10_out, bit_extender_5_out;

  not not_1 (not_1_out, \RST_为1同步清零 );
  assign bit_extender_1_out = {{3{not_1_out}}, not_1_out};  // Bit_Extender bit_extender_1
  assign bit_extender_2_out = {{4{not_1_out}}, not_1_out};  // Bit_Extender bit_extender_2
  assign bit_extender_3_out = {{1{not_1_out}}, not_1_out};  // Bit_Extender bit_extender_3
  assign bit_extender_4_out = {{1{not_1_out}}, not_1_out};  // Bit_Extender bit_extender_4
  assign bit_extender_5_out = {{31{not_1_out}}, not_1_out};  // Bit_Extender bit_extender_5
  assign and_1_out = PC & bit_extender_5_out;  // AND_Gate and_1, 32 bits wide
  assign and_2_out = IR & bit_extender_5_out;  // AND_Gate and_2, 32 bits wide
  assign and_3_out = PC_4 & bit_extender_5_out;  // AND_Gate and_3, 32 bits wide
  assign and_4_out = RegA & bit_extender_5_out;  // AND_Gate and_4, 32 bits wide
  assign and_5_out = RegB & bit_extender_5_out;  // AND_Gate and_5, 32 bits wide
  assign and_6_out = imm & bit_extender_5_out;  // AND_Gate and_6, 32 bits wide
  assign and_7_out = imm_B & bit_extender_5_out;  // AND_Gate and_7, 32 bits wide
  assign and_8_out = imm_J & bit_extender_5_out;  // AND_Gate and_8, 32 bits wide
  assign and_9_out = imm_U & bit_extender_5_out;  // AND_Gate and_9, 32 bits wide
  assign and_10_out = PredictAddr & bit_extender_5_out;  // AND_Gate and_10, 32 bits wide
  and and_11 (and_11_out, Beq, not_1_out);
  and and_12 (and_12_out, Bne, not_1_out);
  and and_13 (and_13_out, MemToReg, not_1_out);
  and and_14 (and_14_out, MemWrite, not_1_out);
  assign and_15_out = AluOP & bit_extender_1_out;  // AND_Gate and_15, 4 bits wide
  and and_16 (and_16_out, AluSrcB, not_1_out);
  and and_17 (and_17_out, RegWrite, not_1_out);
  and and_18 (and_18_out, JAL, not_1_out);
  and and_19 (and_19_out, JALR, not_1_out);
  and and_20 (and_20_out, URET, not_1_out);
  assign and_21_out = W_num & bit_extender_2_out;  // AND_Gate and_21, 5 bits wide
  and and_22 (and_22_out, ecall, not_1_out);
  assign and_23_out = R1_fwd_ID & bit_extender_3_out;  // AND_Gate and_23, 2 bits wide
  assign and_24_out = R2_fwd_ID & bit_extender_4_out;  // AND_Gate and_24, 2 bits wide
  and and_25 (and_25_out, predict, not_1_out);
  Register #(.width(32), .trigger("rising"), .Select("low")) register_1 (
    .D(and_1_out), .en(not_2_out), .Q(PC_2), .clk(CLK), .clr(undriven));
  Register #(.width(32), .trigger("rising"), .Select("low")) register_2 (
    .D(and_2_out), .en(not_2_out), .Q(IR_2), .clk(CLK), .clr(undriven_2));
  Register #(.width(32), .trigger("rising"), .Select("low")) register_3 (
    .D(and_3_out), .en(not_2_out), .Q(PC_4_2), .clk(CLK), .clr(undriven_3));
  Register #(.width(32), .trigger("rising"), .Select("low")) register_4 (
    .D(and_4_out), .en(not_2_out), .Q(RegA_2), .clk(CLK), .clr(undriven_4));
  Register #(.width(32), .trigger("rising"), .Select("low")) register_5 (
    .D(and_5_out), .en(not_2_out), .Q(RegB_2), .clk(CLK), .clr(undriven_5));
  Register #(.width(32), .trigger("rising"), .Select("low")) register_6 (
    .D(and_6_out), .en(not_2_out), .Q(imm_2), .clk(CLK), .clr(undriven_6));
  Register #(.width(32), .trigger("rising"), .Select("low")) register_7 (
    .D(and_7_out), .en(not_2_out), .Q(imm_B_2), .clk(CLK), .clr(undriven_7));
  Register #(.width(32), .trigger("rising"), .Select("low")) register_8 (
    .D(and_8_out), .en(not_2_out), .Q(imm_J_2), .clk(CLK), .clr(undriven_8));
  Register #(.width(32), .trigger("rising"), .Select("low")) register_9 (
    .D(and_9_out), .en(not_2_out), .Q(imm_U_2), .clk(CLK), .clr(undriven_9));
  Register #(.width(32), .trigger("rising"), .Select("low")) register_10 (
    .D(and_10_out), .en(not_2_out), .Q(PredictAddr_2), .clr(CLK));  // open: clk
  Register #(.width(1), .trigger("rising"), .Select("low")) register_11 (
    .D(and_11_out), .en(not_2_out), .Q(Beq_2), .clk(CLK), .clr(undriven_10));
  Register #(.width(1), .trigger("rising"), .Select("low")) register_12 (
    .D(and_12_out), .en(not_2_out), .Q(Bne_2), .clk(CLK), .clr(undriven_11));
  Register #(.width(1), .trigger("rising"), .Select("low")) register_13 (
    .D(and_13_out), .en(not_2_out), .Q(MemToReg_2), .clk(CLK), .clr(undriven_12));
  Register #(.width(1), .trigger("rising"), .Select("low")) register_14 (
    .D(and_14_out), .en(not_2_out), .Q(MemWrite_2), .clk(CLK), .clr(undriven_13));
  Register #(.width(4), .trigger("rising"), .Select("low")) register_15 (
    .D(and_15_out), .en(not_2_out), .Q(AluOP_2), .clk(CLK), .clr(undriven_14));
  Register #(.width(1), .trigger("rising"), .Select("low")) register_16 (
    .D(and_16_out), .en(not_2_out), .Q(AluSrcB_2), .clk(CLK), .clr(undriven_15));
  Register #(.width(1), .trigger("rising"), .Select("low")) register_17 (
    .D(and_17_out), .en(not_2_out), .Q(RegWrite_2), .clk(CLK), .clr(undriven_16));
  Register #(.width(1), .trigger("rising"), .Select("low")) register_18 (
    .D(and_18_out), .en(not_2_out), .Q(JAL_2), .clk(CLK), .clr(undriven_17));
  Register #(.width(1), .trigger("rising"), .Select("low")) register_19 (
    .D(and_19_out), .en(not_2_out), .Q(JALR_2), .clk(CLK), .clr(undriven_18));
  Register #(.width(1), .trigger("rising"), .Select("low")) register_20 (
    .D(and_20_out), .en(not_2_out), .Q(URET_2), .clk(CLK));  // open: clr
  Register #(.width(5), .trigger("rising"), .Select("low")) register_21 (
    .D(and_21_out), .en(not_2_out), .Q(W_num_2), .clk(CLK));  // open: clr
  Register #(.width(1), .trigger("rising"), .Select("low")) register_22 (
    .D(and_22_out), .en(not_2_out), .Q(ecall_2), .clk(CLK));  // open: clr
  Register #(.width(2), .trigger("rising"), .Select("low")) register_23 (
    .D(and_23_out), .en(not_2_out), .Q(R1_fwd_EX), .clk(CLK));  // open: clr
  Register #(.width(2), .trigger("rising"), .Select("low")) register_24 (
    .D(and_24_out), .en(not_2_out), .Q(R2_fwd_EX), .clk(CLK));  // open: clr
  Register #(.width(1), .trigger("rising"), .Select("low")) register_25 (
    .D(and_25_out), .en(not_2_out), .Q(predict_2), .clk(CLK));  // open: clr
  not not_2 (not_2_out, \halt_为1暂停 );
endmodule

module EX_MEM (
  input  [31:0] PC,
  input  [31:0] IR,
  input  [31:0] PC_4,
  input  [31:0] RegA,
  input  [31:0] RegB,
  input  [31:0] AluResult,
  input  Beq,
  input  Bne,
  input  MemToReg,
  input  MemWrite,
  input  [3:0] AluOP,
  input  AluSrcB,
  input  RegWrite,
  input  JAL,
  input  JALR,
  input  URET,
  input  [4:0] W_num,
  input  ecall,
  input  \RST_为1同步清零 ,
  input  CLK,
  input  \halt_为1暂停 ,
  output [31:0] PC_2,
  output [31:0] IR_2,
  output [31:0] PC_4_2,
  output [31:0] RegA_2,
  output [31:0] RegB_2,
  output [31:0] AluResult_2,
  output Beq_2,
  output Bne_2,
  output MemToReg_2,
  output MemWrite_2,
  output [3:0] AluOP_2,
  output AluSrcB_2,
  output RegWrite_2,
  output JAL_2,
  output JALR_2,
  output URET_2,
  output [4:0] W_num_2,
  output ecall_2
);

  wire and_7_out, and_8_out, and_9_out, and_10_out, and_12_out, and_13_out, and_14_out, and_15_out,
       and_16_out, and_18_out, not_1_out, not_2_out, undriven, undriven_2, undriven_3, undriven_4,
       undriven_5, undriven_6, undriven_7, undriven_8, undriven_9, undriven_10, undriven_11, undriven_12,
       undriven_13, undriven_14, undriven_15, undriven_16, undriven_17, undriven_18;
  wire [3:0] and_11_out, bit_extender_2_out;
  wire [4:0] and_17_out, bit_extender_3_out;
  wire [31:0] and_1_out, and_2_out, and_3_out, and_4_out, and_5_out, and_6_out, bit_extender_1_out;

  not not_1 (not_1_out, \RST_为1同步清零 );
  assign bit_extender_1_out = {{31{not_1_out}}, not_1_out};  // Bit_Extender bit_extender_1
  assign bit_extender_2_out = {{3{not_1_out}}, not_1_out};  // Bit_Extender bit_extender_2
  assign bit_extender_3_out = {{4{not_1_out}}, not_1_out};  // Bit_Extender bit_extender_3
  assign and_1_out = PC & bit_extender_1_out;  // AND_Gate and_1, 32 bits wide
  assign and_2_out = IR & bit_extender_1_out;  // AND_Gate and_2, 32 bits wide
  assign and_3_out = PC_4 & bit_extender_1_out;  // AND_Gate and_3, 32 bits wide
  assign and_4_out = RegA & bit_extender_1_out;  // AND_Gate and_4, 32 bits wide
  assign and_5_out = RegB & bit_extender_1_out;  // AND_Gate and_5, 32 bits wide
  assign and_6_out = AluResult & bit_extender_1_out;  // AND_Gate and_6, 32 bits wide
  and and_7 (and_7_out, Beq, not_1_out);
  and and_8 (and_8_out, Bne, not_1_out);
  and and_9 (and_9_out, MemToReg, not_1_out);
  and and_10 (and_10_out, MemWrite, not_1_out);
  assign and_11_out = AluOP & bit_extender_2_out;  // AND_Gate and_11, 4 bits wide
  and and_12 (and_12_out, AluSrcB, not_1_out);
  and and_13 (and_13_out, RegWrite, not_1_out);
  and and_14 (and_14_out, JAL, not_1_out);
  and and_15 (and_15_out, JALR, not_1_out);
  and and_16 (and_16_out, URET, not_1_out);
  assign and_17_out = W_num & bit_extender_3_out;  // AND_Gate and_17, 5 bits wide
  and and_18 (and_18_out, ecall, not_1_out);
  Register #(.width(32), .trigger("rising"), .Select("low")) register_1 (
    .D(and_1_out), .en(not_2_out), .Q(PC_2), .clk(CLK), .clr(undriven));
  Register #(.width(32), .trigger("rising"), .Select("low")) register_2 (
    .D(and_2_out), .en(not_2_out), .Q(IR_2), .clk(CLK), .clr(undriven_2));
  Register #(.width(32), .trigger("rising"), .Select("low")) register_3 (
    .D(and_3_out), .en(not_2_out), .Q(PC_4_2), .clk(CLK), .clr(undriven_3));
  Register #(.width(32), .trigger("rising"), .Select("low")) register_4 (
    .D(and_4_out), .en(not_2_out), .Q(RegA_2), .clk(CLK), .clr(undriven_4));
  Register #(.width(32), .trigger("rising"), .Select("low")) register_5 (
    .D(and_5_out), .en(not_2_out), .Q(RegB_2), .clk(CLK), .clr(undriven_5));
  Register #(.width(32), .trigger("rising"), .Select("low")) register_6 (
    .D(and_6_out), .en(not_2_out), .Q(AluResult_2), .clk(CLK), .clr(undriven_6));
  Register #(.width(1), .trigger("rising"), .Select("low")) register_7 (
    .D(and_7_out), .en(not_2_out), .Q(Beq_2), .clk(CLK), .clr(undriven_7));
  Register #(.width(1), .trigger("rising"), .Select("low")) register_8 (
    .D(and_8_out), .en(not_2_out), .Q(Bne_2), .clk(CLK), .clr(undriven_8));
  Register #(.width(1), .trigger("rising"), .Select("low")) register_9 (
    .D(and_9_out), .en(not_2_out), .Q(MemToReg_2), .clk(CLK), .clr(undriven_9));
  Register #(.width(1), .trigger("rising"), .Select("low")) register_10 (
    .D(and_10_out), .en(not_2_out), .Q(MemWrite_2), .clk(CLK), .clr(undriven_10));
  Register #(.width(4), .trigger("rising"), .Select("low")) register_11 (
    .D(and_11_out), .en(not_2_out), .Q(AluOP_2), .clk(CLK), .clr(undriven_11));
  Register #(.width(1), .trigger("rising"), .Select("low")) register_12 (
    .D(and_12_out), .en(not_2_out), .Q(AluSrcB_2), .clk(CLK), .clr(undriven_12));
  Register #(.width(1), .trigger("rising"), .Select("low")) register_13 (
    .D(and_13_out), .en(not_2_out), .Q(RegWrite_2), .clk(CLK), .clr(undriven_13));
  Register #(.width(1), .trigger("rising"), .Select("low")) register_14 (
    .D(and_14_out), .en(not_2_out), .Q(JAL_2), .clk(CLK), .clr(undriven_14));
  Register #(.width(1), .trigger("rising"), .Select("low")) register_15 (
    .D(and_15_out), .en(not_2_out), .Q(JALR_2), .clk(CLK), .clr(undriven_15));
  Register #(.width(1), .trigger("rising"), .Select("low")) register_16 (
    .D(and_16_out), .en(not_2_out), .Q(URET_2), .clk(CLK), .clr(undriven_16));
  Register #(.width(5), .trigger("rising"), .Select("low")) register_17 (
    .D(and_17_out), .en(not_2_out), .Q(W_num_2), .clk(CLK), .clr(undriven_17));
  Register #(.width(1), .trigger("rising"), .Select("low")) register_18 (
    .D(and_18_out), .en(not_2_out), .Q(ecall_2), .clk(CLK), .clr(undriven_18));
  not not_2 (not_2_out, \halt_为1暂停 );
endmodule

module MEM_WB (
  input  [31:0] PC,
  input  [31:0] IR,
  input  [31:0] PC_4,
  input  [31:0] RegA,
  input  [31:0] RegB,
  input  [31:0] AluResult,
  input  [31:0] MemData,
  input  Beq,
  input  Bne,
  input  MemToReg,
  input  MemWrite,
  input  [3:0] AluOP,
  input  AluSrcB,
  input  RegWrite,
  input  JAL,
  input  JALR,
  input  URET,
  input  [4:0] W_num,
  input  ecall,
  input  \RST_为1同步清零 ,
  input  CLK,
  input  \halt_为1暂停 ,
  output [31:0] PC_2,
  output [31:0] IR_2,
  output [31:0] PC_4_2,
  output [31:0] RegA_2,
  output [31:0] RegB_2,
  output [31:0] AluResult_2,
  output [31:0] MemData_2,
  output Beq_2,
  output Bne_2,
  output MemToReg_2,
  output MemWrite_2,
  output [3:0] AluOP_2,
  output AluSrcB_2,
  output RegWrite_2,
  output JAL_2,
  output JALR_2,
  output URET_2,
  output [4:0] W_num_2,
  output ecall_2
);

  wire and_8_out, and_9_out, and_10_out, and_11_out, and_13_out, and_14_out, and_15_out, and_16_out,
       and_17_out, and_19_out, not_1_out, not_2_out, undriven, undriven_2, undriven_3, undriven_4,
       undriven_5, undriven_6, undriven_7, undriven_8, undriven_9, undriven_10, undriven_11, undriven_12,
       undriven_13, undriven_14, undriven_15, undriven_16, undriven_17, undriven_18;
  wire [3:0] and_12_out, bit_extender_2_out;
  wire [4:0] and_18_out, bit_extender_3_out;
  wire [31:0] and_1_out, and_2_out, and_3_out, and_4_out, and_5_out, and_6_out, and_7_out, bit_extender_1_out;

  not not_1 (not_1_out, \RST_为1同步清零 );
  assign bit_extender_1_out = {{31{not_1_out}}, not_1_out};  // Bit_Extender bit_extender_1
  assign bit_extender_2_out = {{3{not_1_out}}, not_1_out};  // Bit_Extender bit_extender_2
  assign bit_extender_3_out = {{4{not_1_out}}, not_1_out};  // Bit_Extender bit_extender_3
  assign and_1_out = PC & bit_extender_1_out;  // AND_Gate and_1, 32 bits wide
  assign and_2_out = IR & bit_extender_1_out;  // AND_Gate and_2, 32 bits wide
  assign and_3_out = PC_4 & bit_extender_1_out;  // AND_Gate and_3, 32 bits wide
  assign and_4_out = RegA & bit_extender_1_out;  // AND_Gate and_4, 32 bits wide
  assign and_5_out = RegB & bit_extender_1_out;  // AND_Gate and_5, 32 bits wide
  assign and_6_out = AluResult & bit_extender_1_out;  // AND_Gate and_6, 32 bits wide
  assign and_7_out = MemData & bit_extender_1_out;  // AND_Gate and_7, 32 bits wide
  and and_8 (and_8_out, Beq, not_1_out);
  and and_9 (and_9_out, Bne, not_1_out);
  and and_10 (and_10_out, MemToReg, not_1_out);
  and and_11 (and_11_out, MemWrite, not_1_out);
  assign and_12_out = AluOP & bit_extender_2_out;  // AND_Gate and_12, 4 bits wide
  and and_13 (and_13_out, AluSrcB, not_1_out);
  and and_14 (and_14_out, RegWrite, not_1_out);
  and and_15 (and_15_out, JAL, not_1_out);
  and and_16 (and_16_out, JALR, not_1_out);
  and and_17 (and_17_out, URET, not_1_out);
  assign and_18_out = W_num & bit_extender_3_out;  // AND_Gate and_18, 5 bits wide
  and and_19 (and_19_out, ecall, not_1_out);
  Register #(.width(32), .trigger("rising"), .Select("low")) register_1 (
    .D(and_1_out), .en(not_2_out), .Q(PC_2), .clk(CLK), .clr(undriven));
  Register #(.width(32), .trigger("rising"), .Select("low")) register_2 (
    .D(and_2_out), .en(not_2_out), .Q(IR_2), .clk(CLK), .clr(undriven_2));
  Register #(.width(32), .trigger("rising"), .Select("low")) register_3 (
    .D(and_3_out), .en(not_2_out), .Q(PC_4_2), .clk(CLK), .clr(undriven_3));
  Register #(.width(32), .trigger("rising"), .Select("low")) register_4 (
    .D(and_4_out), .en(not_2_out), .Q(RegA_2), .clk(CLK), .clr(undriven_4));
  Register #(.width(32), .trigger("rising"), .Select("low")) register_5 (
    .D(and_5_out), .en(not_2_out), .Q(RegB_2), .clk(CLK), .clr(undriven_5));
  Register #(.width(32), .trigger("rising"), .Select("low")) register_6 (
    .D(and_6_out), .en(not_2_out), .Q(AluResult_2), .clk(CLK), .clr(undriven_6));
  Register #(.width(32), .trigger("rising"), .Select("low")) register_7 (
    .D(and_7_out), .en(not_2_out), .Q(MemData_2), .clk(CLK));  // open: clr
  Register #(.width(1), .trigger("rising"), .Select("low")) register_8 (
    .D(and_8_out), .en(not_2_out), .Q(Beq_2), .clk(CLK), .clr(undriven_7));
  Register #(.width(1), .trigger("rising"), .Select("low")) register_9 (
    .D(and_9_out), .en(not_2_out), .Q(Bne_2), .clk(CLK), .clr(undriven_8));
  Register #(.width(1), .trigger("rising"), .Select("low")) register_10 (
    .D(and_10_out), .en(not_2_out), .Q(MemToReg_2), .clk(CLK), .clr(undriven_9));
  Register #(.width(1), .trigger("rising"), .Select("low")) register_11 (
    .D(and_11_out), .en(not_2_out), .Q(MemWrite_2), .clk(CLK), .clr(undriven_10));
  Register #(.width(4), .trigger("rising"), .Select("low")) register_12 (
    .D(and_12_out), .en(not_2_out), .Q(AluOP_2), .clk(CLK), .clr(undriven_11));
  Register #(.width(1), .trigger("rising"), .Select("low")) register_13 (
    .D(and_13_out), .en(not_2_out), .Q(AluSrcB_2), .clk(CLK), .clr(undriven_12));
  Register #(.width(1), .trigger("rising"), .Select("low")) register_14 (
    .D(and_14_out), .en(not_2_out), .Q(RegWrite_2), .clk(CLK), .clr(undriven_13));
  Register #(.width(1), .trigger("rising"), .Select("low")) register_15 (
    .D(and_15_out), .en(not_2_out), .Q(JAL_2), .clk(CLK), .clr(undriven_14));
  Register #(.width(1), .trigger("rising"), .Select("low")) register_16 (
    .D(and_16_out), .en(not_2_out), .Q(JALR_2), .clk(CLK), .clr(undriven_15));
  Register #(.width(1), .trigger("rising"), .Select("low")) register_17 (
    .D(and_17_out), .en(not_2_out), .Q(URET_2), .clk(CLK), .clr(undriven_16));
  Register #(.width(5), .trigger("rising"), .Select("low")) register_18 (
    .D(and_18_out), .en(not_2_out), .Q(W_num_2), .clk(CLK), .clr(undriven_17));
  Register #(.width(1), .trigger("rising"), .Select("low")) register_19 (
    .D(and_19_out), .en(not_2_out), .Q(ecall_2), .clk(CLK), .clr(undriven_18));
  not not_2 (not_2_out, \halt_为1暂停 );
endmodule

module R1R2_used (
  input  OP2,
  input  OP3,
  input  OP4,
  input  OP5,
  input  OP6,
  input  F12,
  input  F13,
  input  F14,
  input  F25,
  input  F30,
  output R2_used,
  output R1_used
);

  wire and_1_out, and_2_out, and_3_out, and_4_out, and_5_out, and_6_out, and_7_out, and_8_out, and_9_out,
       and_10_out, and_11_out, and_12_out, and_13_out, and_14_out, and_15_out, and_16_out, and_17_out,
       and_18_out, and_19_out, and_20_out, not_1_out, not_2_out, not_3_out, not_4_out, not_5_out, not_6_out,
       not_7_out, not_8_out, not_9_out, not_10_out, not_11_out, not_12_out, not_13_out, not_14_out,
       not_15_out, not_16_out, not_17_out, not_18_out, not_19_out, not_20_out, not_21_out, not_22_out,
       not_23_out, not_24_out, not_25_out, not_26_out, not_27_out, not_28_out, not_29_out, not_30_out,
       not_31_out, not_32_out, not_33_out, not_34_out, not_35_out, not_36_out, not_37_out, not_38_out,
       not_39_out, not_40_out, not_41_out, not_42_out, not_43_out, not_44_out, not_45_out, not_46_out,
       not_47_out, not_48_out, not_49_out, not_50_out, not_51_out, not_52_out, not_53_out, not_54_out,
       not_55_out, not_56_out, not_57_out, not_58_out, not_59_out, not_60_out, not_61_out, not_62_out,
       not_63_out, not_64_out, not_65_out, not_66_out, not_67_out, not_68_out, not_69_out, not_70_out,
       not_71_out, not_72_out, not_73_out, not_74_out, not_75_out, not_76_out, not_77_out, not_78_out,
       not_79_out, not_80_out, not_81_out, not_82_out, not_83_out, not_84_out, not_85_out, not_86_out,
       not_87_out, not_88_out, not_89_out, not_90_out, not_91_out, not_92_out, not_93_out, not_94_out,
       not_95_out, not_96_out, not_97_out, not_98_out, not_99_out, not_100_out, not_101_out, not_102_out,
       not_103_out, not_104_out, not_105_out, not_106_out, not_107_out, not_108_out, not_109_out,
       not_110_out, not_111_out, not_112_out, not_113_out, not_114_out, not_115_out;

  not not_1 (not_1_out, F30);
  not not_2 (not_2_out, F25);
  not not_3 (not_3_out, F14);
  not not_4 (not_4_out, F13);
  not not_5 (not_5_out, F12);
  not not_6 (not_6_out, OP6);
  not not_7 (not_7_out, OP3);
  not not_8 (not_8_out, OP2);
  not not_9 (not_9_out, F25);
  not not_10 (not_10_out, F14);
  not not_11 (not_11_out, F13);
  not not_12 (not_12_out, F12);
  not not_13 (not_13_out, OP6);
  not not_14 (not_14_out, OP3);
  not not_15 (not_15_out, OP2);
  not not_16 (not_16_out, F30);
  not not_17 (not_17_out, F25);
  not not_18 (not_18_out, OP6);
  not not_19 (not_19_out, OP3);
  not not_20 (not_20_out, OP2);
  not not_21 (not_21_out, F30);
  not not_22 (not_22_out, F25);
  not not_23 (not_23_out, F12);
  not not_24 (not_24_out, OP6);
  not not_25 (not_25_out, OP3);
  not not_26 (not_26_out, OP2);
  not not_27 (not_27_out, F30);
  not not_28 (not_28_out, F25);
  not not_29 (not_29_out, F14);
  not not_30 (not_30_out, F12);
  not not_31 (not_31_out, OP6);
  not not_32 (not_32_out, OP3);
  not not_33 (not_33_out, OP2);
  not not_34 (not_34_out, F30);
  not not_35 (not_35_out, F25);
  not not_36 (not_36_out, F14);
  not not_37 (not_37_out, OP6);
  not not_38 (not_38_out, OP3);
  not not_39 (not_39_out, OP2);
  not not_40 (not_40_out, F14);
  not not_41 (not_41_out, F12);
  not not_42 (not_42_out, OP6);
  not not_43 (not_43_out, OP4);
  not not_44 (not_44_out, OP3);
  not not_45 (not_45_out, OP2);
  not not_46 (not_46_out, F14);
  not not_47 (not_47_out, F13);
  not not_48 (not_48_out, F12);
  not not_49 (not_49_out, OP3);
  not not_50 (not_50_out, OP2);
  not not_51 (not_51_out, F14);
  not not_52 (not_52_out, F13);
  not not_53 (not_53_out, F12);
  not not_54 (not_54_out, OP4);
  not not_55 (not_55_out, OP3);
  not not_56 (not_56_out, OP2);
  not not_57 (not_57_out, F14);
  not not_58 (not_58_out, F13);
  not not_59 (not_59_out, OP4);
  not not_60 (not_60_out, OP3);
  not not_61 (not_61_out, OP2);
  not not_62 (not_62_out, OP2);
  not not_63 (not_63_out, OP3);
  not not_64 (not_64_out, OP4);
  not not_65 (not_65_out, OP6);
  not not_66 (not_66_out, F12);
  not not_67 (not_67_out, F14);
  not not_68 (not_68_out, OP2);
  not not_69 (not_69_out, OP3);
  not not_70 (not_70_out, OP4);
  not not_71 (not_71_out, F13);
  not not_72 (not_72_out, F14);
  not not_73 (not_73_out, OP2);
  not not_74 (not_74_out, OP3);
  not not_75 (not_75_out, F12);
  not not_76 (not_76_out, F13);
  not not_77 (not_77_out, F14);
  not not_78 (not_78_out, OP3);
  not not_79 (not_79_out, OP4);
  not not_80 (not_80_out, F12);
  not not_81 (not_81_out, F13);
  not not_82 (not_82_out, F14);
  not not_83 (not_83_out, OP2);
  not not_84 (not_84_out, OP3);
  not not_85 (not_85_out, OP5);
  not not_86 (not_86_out, OP6);
  not not_87 (not_87_out, F12);
  not not_88 (not_88_out, OP2);
  not not_89 (not_89_out, OP3);
  not not_90 (not_90_out, OP5);
  not not_91 (not_91_out, OP6);
  not not_92 (not_92_out, F13);
  not not_93 (not_93_out, F25);
  not not_94 (not_94_out, F30);
  not not_95 (not_95_out, OP2);
  not not_96 (not_96_out, OP3);
  not not_97 (not_97_out, OP6);
  not not_98 (not_98_out, F12);
  not not_99 (not_99_out, F13);
  not not_100 (not_100_out, F14);
  not not_101 (not_101_out, F25);
  not not_102 (not_102_out, OP2);
  not not_103 (not_103_out, OP3);
  not not_104 (not_104_out, OP5);
  not not_105 (not_105_out, OP6);
  not not_106 (not_106_out, F25);
  not not_107 (not_107_out, OP2);
  not not_108 (not_108_out, OP3);
  not not_109 (not_109_out, OP5);
  not not_110 (not_110_out, OP6);
  not not_111 (not_111_out, OP2);
  not not_112 (not_112_out, OP3);
  not not_113 (not_113_out, OP6);
  not not_114 (not_114_out, F25);
  not not_115 (not_115_out, F30);
  and and_1 (and_1_out, not_1_out, not_2_out, not_3_out, not_4_out, not_5_out, not_6_out, OP5, OP4, not_7_out, not_8_out);
  and and_2 (and_2_out, F30, not_9_out, not_10_out, not_11_out, not_12_out, not_13_out, OP5, OP4, not_14_out, not_15_out);
  and and_3 (and_3_out, not_16_out, not_17_out, F14, F13, F12, not_18_out, OP5, OP4, not_19_out, not_20_out);
  and and_4 (and_4_out, not_21_out, not_22_out, F14, F13, not_23_out, not_24_out, OP5, OP4, not_25_out, not_26_out);
  and and_5 (and_5_out, not_27_out, not_28_out, not_29_out, F13, not_30_out, not_31_out, OP5, OP4, not_32_out, not_33_out);
  and and_6 (and_6_out, not_34_out, not_35_out, not_36_out, F13, F12, not_37_out, OP5, OP4, not_38_out, not_39_out);
  and and_7 (and_7_out, not_40_out, F13, not_41_out, not_42_out, OP5, not_43_out, not_44_out, not_45_out);
  and and_8 (and_8_out, not_46_out, not_47_out, not_48_out, OP6, OP5, OP4, not_49_out, not_50_out);
  and and_9 (and_9_out, not_51_out, not_52_out, not_53_out, OP6, OP5, not_54_out, not_55_out, not_56_out);
  and and_10 (and_10_out, not_57_out, not_58_out, F12, OP6, OP5, not_59_out, not_60_out, not_61_out);
  and and_11 (and_11_out, not_62_out, not_63_out, not_64_out, not_65_out, not_66_out, F13, not_67_out);
  and and_12 (and_12_out, not_68_out, not_69_out, not_70_out, OP5, OP6, not_71_out, not_72_out);
  and and_13 (and_13_out, not_73_out, not_74_out, OP5, OP6, not_75_out, not_76_out, not_77_out);
  and and_14 (and_14_out, not_78_out, not_79_out, OP5, OP6, not_80_out, not_81_out, not_82_out);
  and and_15 (and_15_out, not_83_out, not_84_out, OP4, not_85_out, not_86_out, not_87_out);
  and and_16 (and_16_out, not_88_out, not_89_out, OP4, not_90_out, not_91_out, not_92_out, not_93_out, not_94_out);
  and and_17 (and_17_out, not_95_out, not_96_out, OP4, not_97_out, not_98_out, not_99_out, not_100_out, not_101_out);
  and and_18 (and_18_out, not_102_out, not_103_out, OP4, not_104_out, not_105_out, F14, not_106_out);
  and and_19 (and_19_out, not_107_out, not_108_out, OP4, not_109_out, not_110_out, F13, F14);
  and and_20 (and_20_out, not_111_out, not_112_out, OP4, OP5, not_113_out, F13, not_114_out, not_115_out);
  or or_1 (R2_used, and_1_out, and_2_out, and_3_out, and_4_out, and_5_out, and_6_out, and_7_out, and_8_out, and_9_out, and_10_out);
  or or_2 (R1_used, and_11_out, and_12_out, and_13_out, and_14_out, and_15_out, and_16_out, and_17_out, and_18_out, and_19_out, and_20_out);
endmodule

module \数据相关检测器  (
  input  [4:0] OP,
  input  [4:0] R1_num,
  input  [4:0] W__EX,
  input  [4:0] W__MEM,
  input  [4:0] Funct,
  input  [4:0] R2_num,
  input  RegWrite_EX,
  input  RegWrite_MEM,
  output DataRelated
);

  wire and_1_out, and_2_out, and_3_out, and_4_out, and_5_out, and_6_out, and_7_out, and_8_out, and_9_out,
       and_10_out, and_11_out, and_12_out, comparator_1_eq, comparator_2_eq, comparator_3_eq,
       comparator_4_eq, comparator_5_eq, comparator_6_eq, comparator_7_eq, comparator_8_eq, not_1_out,
       not_2_out, not_3_out, not_4_out, or_1_out, or_2_out, R1_used, R2_used;

  Comparator #(.width(5), .mode("twosComplement")) comparator_1 (
    .a(R1_num), .b({5{1'b0}}), .eq(comparator_1_eq));  // open: gt, lt
  Comparator #(.width(5), .mode("twosComplement")) comparator_2 (
    .a(R1_num), .b(W__EX), .eq(comparator_2_eq));  // open: gt, lt
  Comparator #(.width(5), .mode("twosComplement")) comparator_3 (
    .a(R1_num), .b({5{1'b0}}), .eq(comparator_3_eq));  // open: gt, lt
  Comparator #(.width(5), .mode("twosComplement")) comparator_4 (
    .a(R1_num), .b(W__MEM), .eq(comparator_4_eq));  // open: gt, lt
  Comparator #(.width(5), .mode("twosComplement")) comparator_5 (
    .a(R2_num), .b({5{1'b0}}), .eq(comparator_5_eq));  // open: gt, lt
  Comparator #(.width(5), .mode("twosComplement")) comparator_6 (
    .a(R2_num), .b(W__EX), .eq(comparator_6_eq));  // open: gt, lt
  Comparator #(.width(5), .mode("twosComplement")) comparator_7 (
    .a(R2_num), .b({5{1'b0}}), .eq(comparator_7_eq));  // open: gt, lt
  Comparator #(.width(5), .mode("twosComplement")) comparator_8 (
    .a(R2_num), .b(W__MEM), .eq(comparator_8_eq));  // open: gt, lt
  not not_1 (not_1_out, comparator_1_eq);
  not not_2 (not_2_out, comparator_3_eq);
  not not_3 (not_3_out, comparator_5_eq);
  not not_4 (not_4_out, comparator_7_eq);
  and and_1 (and_1_out, not_1_out, comparator_2_eq);
  and and_2 (and_2_out, RegWrite_EX, R1_used);
  and and_3 (and_3_out, not_2_out, comparator_4_eq);
  and and_4 (and_4_out, RegWrite_MEM, R1_used);
  and and_5 (and_5_out, not_3_out, comparator_6_eq);
  and and_6 (and_6_out, RegWrite_EX, R2_used);
  and and_7 (and_7_out, not_4_out, comparator_8_eq);
  and and_8 (and_8_out, RegWrite_MEM, R2_used);
  and and_9 (and_9_out, and_1_out, and_2_out);
  and and_10 (and_10_out, and_3_out, and_4_out);
  and and_11 (and_11_out, and_5_out, and_6_out);
  and and_12 (and_12_out, and_7_out, and_8_out);
  or or_1 (or_1_out, and_9_out, and_10_out);
  or or_2 (or_2_out, and_11_out, and_12_out);
  R1R2_used r1r2_used_1 (
    .OP2(OP[0]), .OP3(OP[1]), .OP4(OP[2]), .OP5(OP[3]), .OP6(OP[4]), .F12(Funct[0]), .F13(Funct[1]),
    .F14(Funct[2]), .F25(Funct[3]), .F30(Funct[4]), .R2_used(R2_used), .R1_used(R1_used));
  or or_3 (DataRelated, or_1_out, or_2_out);

  // Other names for the same wires on the sheet: OP_CODE[4:0] = OP

  // Notes on the sheet:
  //   R1与EX的W相同
  //   EX阶段有写操作
  //   R1不是0号寄存器
  //   指令使用了R1
endmodule

module \Load_Use检测  (
  input  [4:0] OP,
  input  [4:0] R1_num,
  input  [4:0] W__EX,
  input  [4:0] Funct,
  input  [4:0] R2_num,
  input  MemToReg_EX,
  output LoadUse
);

  wire and_1_out, and_2_out, comparator_1_eq, comparator_2_eq, comparator_3_eq, comparator_4_eq, not_1_out,
       not_2_out, R1_used, R2_used;

  Comparator #(.width(5), .mode("twosComplement")) comparator_1 (
    .a(R1_num), .b(W__EX), .eq(comparator_1_eq));  // open: gt, lt
  Comparator #(.width(5), .mode("twosComplement")) comparator_2 (
    .a(R1_num), .b({5{1'b0}}), .eq(comparator_2_eq));  // open: gt, lt
  Comparator #(.width(5), .mode("twosComplement")) comparator_3 (
    .a(R2_num), .b(W__EX), .eq(comparator_3_eq));  // open: gt, lt
  Comparator #(.width(5), .mode("twosComplement")) comparator_4 (
    .a(R2_num), .b({5{1'b0}}), .eq(comparator_4_eq));  // open: gt, lt
  not not_1 (not_1_out, comparator_2_eq);
  not not_2 (not_2_out, comparator_4_eq);
  and and_1 (and_1_out, R1_used, comparator_1_eq, MemToReg_EX, not_1_out);
  and and_2 (and_2_out, R2_used, comparator_3_eq, MemToReg_EX, not_2_out);
  R1R2_used r1r2_used_1 (
    .OP2(OP[0]), .OP3(OP[1]), .OP4(OP[2]), .OP5(OP[3]), .OP6(OP[4]), .F12(Funct[0]), .F13(Funct[1]),
    .F14(Funct[2]), .F25(Funct[3]), .F30(Funct[4]), .R2_used(R2_used), .R1_used(R1_used));
  or or_1 (LoadUse, and_1_out, and_2_out);

  // Other names for the same wires on the sheet: OP_CODE[4:0] = OP

  // Notes on the sheet:
  //   R1与EX的W相同
  //   指令使用了R1
  //   EX阶段有访存操作
  //   R1不是0号寄存器
endmodule

module \fwd生成  (
  input  [4:0] OP,
  input  [4:0] R1_num,
  input  [4:0] W__EX,
  input  [4:0] W__MEM,
  input  [4:0] Funct,
  input  [4:0] R2_num,
  input  RegWrite_EX,
  input  RegWrite_MEM,
  output [1:0] R1_fwd,
  output [1:0] R2_fwd
);

  wire and_1_out, and_2_out, and_3_out, and_4_out, comparator_1_eq, comparator_2_eq, comparator_3_eq,
       comparator_4_eq, comparator_5_eq, comparator_6_eq, comparator_7_eq, comparator_8_eq, not_1_out,
       not_2_out, not_3_out, not_4_out, R1_used, R2_used;
  wire [1:0] multiplexer_1_out, multiplexer_3_out;

  Comparator #(.width(5), .mode("twosComplement")) comparator_1 (
    .a(R1_num), .b(W__MEM), .eq(comparator_1_eq));  // open: gt, lt
  Comparator #(.width(5), .mode("twosComplement")) comparator_2 (
    .a(R1_num), .b({5{1'b0}}), .eq(comparator_2_eq));  // open: gt, lt
  not not_1 (not_1_out, comparator_2_eq);
  Comparator #(.width(5), .mode("twosComplement")) comparator_3 (
    .a(R1_num), .b(W__EX), .eq(comparator_3_eq));  // open: gt, lt
  Comparator #(.width(5), .mode("twosComplement")) comparator_4 (
    .a(R1_num), .b({5{1'b0}}), .eq(comparator_4_eq));  // open: gt, lt
  not not_2 (not_2_out, comparator_4_eq);
  and and_1 (and_1_out, R1_used, comparator_1_eq, RegWrite_MEM, not_1_out);
  and and_2 (and_2_out, R1_used, comparator_3_eq, RegWrite_EX, not_2_out);
  Multiplexer #(.select(1), .width(2), .disabled("Z"), .enable("false")) multiplexer_1 (
    .in0(2'b00), .in1(2'b01), .out(multiplexer_1_out), .sel(and_1_out));
  Multiplexer #(.select(1), .width(2), .disabled("Z"), .enable("false")) multiplexer_2 (
    .in0(multiplexer_1_out), .in1(2'b10), .out(R1_fwd), .sel(and_2_out));
  Comparator #(.width(5), .mode("twosComplement")) comparator_5 (
    .a(R2_num), .b(W__MEM), .eq(comparator_5_eq));  // open: gt, lt
  Comparator #(.width(5), .mode("twosComplement")) comparator_6 (
    .a(R2_num), .b({5{1'b0}}), .eq(comparator_6_eq));  // open: gt, lt
  Comparator #(.width(5), .mode("twosComplement")) comparator_7 (
    .a(R2_num), .b(W__EX), .eq(comparator_7_eq));  // open: gt, lt
  Comparator #(.width(5), .mode("twosComplement")) comparator_8 (
    .a(R2_num), .b({5{1'b0}}), .eq(comparator_8_eq));  // open: gt, lt
  not not_3 (not_3_out, comparator_6_eq);
  not not_4 (not_4_out, comparator_8_eq);
  R1R2_used r1r2_used_1 (
    .OP2(OP[0]), .OP3(OP[1]), .OP4(OP[2]), .OP5(OP[3]), .OP6(OP[4]), .F12(Funct[0]), .F13(Funct[1]),
    .F14(Funct[2]), .F25(Funct[3]), .F30(Funct[4]), .R2_used(R2_used), .R1_used(R1_used));
  Multiplexer #(.select(1), .width(2), .disabled("Z"), .enable("false")) multiplexer_3 (
    .in0(2'b00), .in1(2'b01), .out(multiplexer_3_out), .sel(and_3_out));
  and and_3 (and_3_out, R2_used, comparator_5_eq, RegWrite_MEM, not_3_out);
  and and_4 (and_4_out, R2_used, comparator_7_eq, RegWrite_EX, not_4_out);
  Multiplexer #(.select(1), .width(2), .disabled("Z"), .enable("false")) multiplexer_4 (
    .in0(multiplexer_3_out), .in1(2'b10), .out(R2_fwd), .sel(and_4_out));

  // Other names for the same wires on the sheet: OP_CODE[4:0] = OP

  // Notes on the sheet:
  //   指令使用了R1
  //   R1与EX的W相同
  //   EX阶段有写操作
  //   R1不是0号寄存器
  //   AluResult_WB和MemData_WB无论哪个被重定向，RDin都会选择出来正确的一个，只需要将这两个数据的重定向替换为RDin的重定向即可
  //   重定向到RDin
  //   重定向到AluResult_MEM
  //   重定向针对的是ID阶段的指令，但重定向发生在EX阶段，因为EX阶段才会用到R1R2，所以AluResult_WB实际上对应的是MEM阶段的数据，只不过做重定向的时候已经是下一个周期了被传到了WB段，其他的也同理
  //   EX和MEM段的指令都需要重定向时优先前者
  //   重定向到RDin
  //   重定向到AluResult_MEM
endmodule
module BranchTargetBuffer (
  input  CLK,
  input  [31:0] PC,
  input  EX_BRANCHTAKEN,
  input  EX_BRANCH,
  input  [31:0] EX_PC,
  input  [31:0] EX_BRANCHADDR,
  output PREDICTJUMP,
  output [31:0] PREDICTADDR
);

  wire and_1_out, and_2_out, and_3_out, and_4_out, and_5_out, and_6_out, and_7_out, and_8_out, and_25_out,
       and_26_out, and_27_out, and_28_out, and_29_out, and_30_out, and_31_out, and_32_out, comparator_1_eq,
       comparator_2_eq, comparator_3_eq, comparator_4_eq, comparator_5_eq, comparator_6_eq, comparator_7_eq,
       comparator_8_eq, comparator_9_eq, comparator_10_eq, comparator_11_eq, comparator_12_eq,
       comparator_13_eq, comparator_14_eq, comparator_15_eq, comparator_16_eq, d_ff_1_q, d_ff_2_q, d_ff_3_q,
       d_ff_4_q, d_ff_5_q, d_ff_6_q, d_ff_7_q, d_ff_8_q, demultiplexer_1_out0, demultiplexer_1_out1,
       demultiplexer_1_out2, demultiplexer_1_out3, demultiplexer_1_out4, demultiplexer_1_out5,
       demultiplexer_1_out6, demultiplexer_1_out7, demultiplexer_2_out0, demultiplexer_2_out1,
       demultiplexer_2_out2, demultiplexer_2_out3, demultiplexer_2_out4, demultiplexer_2_out5,
       demultiplexer_2_out6, demultiplexer_2_out7, EX_HIT, EX_MISS, H0, H1, H2, H3, H4, H5, H6, H7,
       not_2_out, not_3_out, not_4_out, not_5_out, not_6_out, not_7_out, not_8_out, not_9_out, not_10_out,
       or_1_out, or_2_out, or_3_out, or_4_out, or_5_out, or_6_out, or_7_out, or_8_out, or_10_out, or_11_out,
       or_12_out, or_13_out, or_14_out, or_15_out, or_16_out, or_17_out, priority_encoder_2_gs, V0, V1, V2,
       V3, V4, V5, V6, V7, W0, W1, W2, W3, W4, W5, W6, W7;
  wire [0:0] controlled_buffer_1_out;
  wire [1:0] multiplexer_1_out, multiplexer_2_out, multiplexer_3_out, multiplexer_4_out, multiplexer_5_out,
       multiplexer_6_out, multiplexer_7_out, multiplexer_8_out, multiplexer_9_out, P0, P1, P2, P3, P4, P5,
       P6, P7, PNEXT;
  wire [2:0] compare_1_max_place, compare_2_max_place, compare_3_max_place, compare_4_max_place,
       compare_5_max_place, compare_6_max_place, compare_7_max_place, multiplexer_10_out,
       priority_encoder_1_out, priority_encoder_2_out;
  wire [31:0] compare_1_max, compare_2_max, compare_3_max, compare_4_max, compare_5_max, compare_6_max,
       COUNT0, COUNT1, COUNT2, COUNT3, COUNT4, COUNT5, COUNT6, COUNT7, CUR0, CUR1, CUR2, CUR3, CUR4, CUR5,
       CUR6, CUR7, NEXT0, NEXT1, NEXT2, NEXT3, NEXT4, NEXT5, NEXT6, NEXT7;

  Register #(.width(1), .trigger("rising"), .Select("low")) register_1 (
    .D(1'b1), .en(W0), .Q(V0), .clk(CLK));  // open: clr
  Register #(.width(1), .trigger("rising"), .Select("low")) register_2 (
    .D(1'b1), .en(W1), .Q(V1), .clk(CLK));  // open: clr
  Register #(.width(1), .trigger("rising"), .Select("low")) register_3 (
    .D(1'b1), .en(W2), .Q(V2), .clk(CLK));  // open: clr
  Register #(.width(1), .trigger("rising"), .Select("low")) register_4 (
    .D(1'b1), .en(W3), .Q(V3), .clk(CLK));  // open: clr
  Register #(.width(1), .trigger("rising"), .Select("low")) register_5 (
    .D(1'b1), .en(W4), .Q(V4), .clk(CLK));  // open: clr
  Register #(.width(1), .trigger("rising"), .Select("low")) register_6 (
    .D(1'b1), .en(W5), .Q(V5), .clk(CLK));  // open: clr
  Register #(.width(1), .trigger("rising"), .Select("low")) register_7 (
    .D(1'b1), .en(W6), .Q(V6), .clk(CLK));  // open: clr
  Register #(.width(1), .trigger("rising"), .Select("low")) register_8 (
    .D(1'b1), .en(W7), .Q(V7), .clk(CLK));  // open: clr
  Register #(.width(32), .trigger("rising"), .Select("low")) register_9 (
    .D(EX_PC), .en(W0), .Q(CUR0), .clk(CLK));  // open: clr
  Register #(.width(32), .trigger("rising"), .Select("low")) register_10 (
    .D(EX_PC), .en(W1), .Q(CUR1), .clk(CLK));  // open: clr
  Register #(.width(32), .trigger("rising"), .Select("low")) register_11 (
    .D(EX_PC), .en(W2), .Q(CUR2), .clk(CLK));  // open: clr
  Register #(.width(32), .trigger("rising"), .Select("low")) register_12 (
    .D(EX_PC), .en(W3), .Q(CUR3), .clk(CLK));  // open: clr
  Register #(.width(32), .trigger("rising"), .Select("low")) register_13 (
    .D(EX_PC), .en(W4), .Q(CUR4), .clk(CLK));  // open: clr
  Register #(.width(32), .trigger("rising"), .Select("low")) register_14 (
    .D(EX_PC), .en(W5), .Q(CUR5), .clk(CLK));  // open: clr
  Register #(.width(32), .trigger("rising"), .Select("low")) register_15 (
    .D(EX_PC), .en(W6), .Q(CUR6), .clk(CLK));  // open: clr
  Register #(.width(32), .trigger("rising"), .Select("low")) register_16 (
    .D(EX_PC), .en(W7), .Q(CUR7), .clk(CLK));  // open: clr
  Register #(.width(32), .trigger("rising"), .Select("low")) register_17 (
    .D(EX_BRANCHADDR), .en(W0), .Q(NEXT0), .clk(CLK));  // open: clr
  Register #(.width(32), .trigger("rising"), .Select("low")) register_18 (
    .D(EX_BRANCHADDR), .en(W1), .Q(NEXT1), .clk(CLK));  // open: clr
  Register #(.width(32), .trigger("rising"), .Select("low")) register_19 (
    .D(EX_BRANCHADDR), .en(W2), .Q(NEXT2), .clk(CLK));  // open: clr
  Register #(.width(32), .trigger("rising"), .Select("low")) register_20 (
    .D(EX_BRANCHADDR), .en(W3), .Q(NEXT3), .clk(CLK));  // open: clr
  Register #(.width(32), .trigger("rising"), .Select("low")) register_21 (
    .D(EX_BRANCHADDR), .en(W4), .Q(NEXT4), .clk(CLK));  // open: clr
  Register #(.width(32), .trigger("rising"), .Select("low")) register_22 (
    .D(EX_BRANCHADDR), .en(W5), .Q(NEXT5), .clk(CLK));  // open: clr
  Register #(.width(32), .trigger("rising"), .Select("low")) register_23 (
    .D(EX_BRANCHADDR), .en(W6), .Q(NEXT6), .clk(CLK));  // open: clr
  Register #(.width(32), .trigger("rising"), .Select("low")) register_24 (
    .D(EX_BRANCHADDR), .en(W7), .Q(NEXT7), .clk(CLK));  // open: clr
  and and_1 (and_1_out, H0, EX_BRANCH);
  and and_2 (and_2_out, H1, EX_BRANCH);
  and and_3 (and_3_out, H2, EX_BRANCH);
  and and_4 (and_4_out, H3, EX_BRANCH);
  and and_5 (and_5_out, H4, EX_BRANCH);
  and and_6 (and_6_out, H5, EX_BRANCH);
  and and_7 (and_7_out, H6, EX_BRANCH);
  and and_8 (and_8_out, H7, EX_BRANCH);
  Multiplexer #(.select(1), .width(2), .disabled("Z"), .enable("false")) multiplexer_1 (
    .in0(PNEXT), .in1(2'b01), .out(multiplexer_1_out), .sel(W0));
  Multiplexer #(.select(1), .width(2), .disabled("Z"), .enable("false")) multiplexer_2 (
    .in0(PNEXT), .in1(2'b01), .out(multiplexer_2_out), .sel(W1));
  Multiplexer #(.select(1), .width(2), .disabled("Z"), .enable("false")) multiplexer_3 (
    .in0(PNEXT), .in1(2'b01), .out(multiplexer_3_out), .sel(W2));
  Multiplexer #(.select(1), .width(2), .disabled("Z"), .enable("false")) multiplexer_4 (
    .in0(PNEXT), .in1(2'b01), .out(multiplexer_4_out), .sel(W3));
  Multiplexer #(.select(1), .width(2), .disabled("Z"), .enable("false")) multiplexer_5 (
    .in0(PNEXT), .in1(2'b01), .out(multiplexer_5_out), .sel(W4));
  Multiplexer #(.select(1), .width(2), .disabled("Z"), .enable("false")) multiplexer_6 (
    .in0(PNEXT), .in1(2'b01), .out(multiplexer_6_out), .sel(W5));
  Multiplexer #(.select(1), .width(2), .disabled("Z"), .enable("false")) multiplexer_7 (
    .in0(PNEXT), .in1(2'b01), .out(multiplexer_7_out), .sel(W6));
  Multiplexer #(.select(1), .width(2), .disabled("Z"), .enable("false")) multiplexer_8 (
    .in0(PNEXT), .in1(2'b01), .out(multiplexer_8_out), .sel(W7));
  Register #(.width(2), .trigger("rising"), .Select("low")) register_25 (
    .D(multiplexer_1_out), .en(and_1_out), .Q(P0), .clk(CLK));  // open: clr
  Register #(.width(2), .trigger("rising"), .Select("low")) register_26 (
    .D(multiplexer_2_out), .en(and_2_out), .Q(P1), .clk(CLK));  // open: clr
  Register #(.width(2), .trigger("rising"), .Select("low")) register_27 (
    .D(multiplexer_3_out), .en(and_3_out), .Q(P2), .clk(CLK));  // open: clr
  Register #(.width(2), .trigger("rising"), .Select("low")) register_28 (
    .D(multiplexer_4_out), .en(and_4_out), .Q(P3), .clk(CLK));  // open: clr
  Register #(.width(2), .trigger("rising"), .Select("low")) register_29 (
    .D(multiplexer_5_out), .en(and_5_out), .Q(P4), .clk(CLK));  // open: clr
  Register #(.width(2), .trigger("rising"), .Select("low")) register_30 (
    .D(multiplexer_6_out), .en(and_6_out), .Q(P5), .clk(CLK));  // open: clr
  Register #(.width(2), .trigger("rising"), .Select("low")) register_31 (
    .D(multiplexer_7_out), .en(and_7_out), .Q(P6), .clk(CLK));  // open: clr
  Register #(.width(2), .trigger("rising"), .Select("low")) register_32 (
    .D(multiplexer_8_out), .en(and_8_out), .Q(P7), .clk(CLK));  // open: clr
  or or_1 (or_1_out, W0, H0);
  or or_2 (or_2_out, W1, H1);
  or or_3 (or_3_out, W2, H2);
  or or_4 (or_4_out, W3, H3);
  or or_5 (or_5_out, W4, H4);
  or or_6 (or_6_out, W5, H5);
  or or_7 (or_7_out, W6, H6);
  or or_8 (or_8_out, W7, H7);
  Counter #(.width(32), .max('hffffffff), .ongoal("wrap"), .trigger("rising"), .behavior("new")) counter_1 (
    .Q(COUNT0), .clk(CLK), .clr(d_ff_1_q));  // open: load, D, count, carry, preset, down
  D_Flip_Flop #(.trigger("rising"), .Pre_Clr_Positions("LEGACY"), .NegatePresetClear("false"), .enable("true"), .NewFFLayout("false")) d_ff_1 (
    .clk(CLK), .D(or_1_out), .Q(d_ff_1_q));  // open: Qn, preset, en, reset
  Counter #(.width(32), .max('hffffffff), .ongoal("wrap"), .trigger("rising"), .behavior("new")) counter_2 (
    .Q(COUNT1), .clk(CLK), .clr(d_ff_2_q));  // open: load, D, count, carry, preset, down
  D_Flip_Flop #(.trigger("rising"), .Pre_Clr_Positions("LEGACY"), .NegatePresetClear("false"), .enable("true"), .NewFFLayout("false")) d_ff_2 (
    .clk(CLK), .D(or_2_out), .Q(d_ff_2_q));  // open: Qn, preset, en, reset
  Counter #(.width(32), .max('hffffffff), .ongoal("wrap"), .trigger("rising"), .behavior("new")) counter_3 (
    .Q(COUNT2), .clk(CLK), .clr(d_ff_3_q));  // open: load, D, count, carry, preset, down
  D_Flip_Flop #(.trigger("rising"), .Pre_Clr_Positions("LEGACY"), .NegatePresetClear("false"), .enable("true"), .NewFFLayout("false")) d_ff_3 (
    .clk(CLK), .D(or_3_out), .Q(d_ff_3_q));  // open: Qn, preset, en, reset
  Counter #(.width(32), .max('hffffffff), .ongoal("wrap"), .trigger("rising"), .behavior("new")) counter_4 (
    .Q(COUNT3), .clk(CLK), .clr(d_ff_4_q));  // open: load, D, count, carry, preset, down
  D_Flip_Flop #(.trigger("rising"), .Pre_Clr_Positions("LEGACY"), .NegatePresetClear("false"), .enable("true"), .NewFFLayout("false")) d_ff_4 (
    .clk(CLK), .D(or_4_out), .Q(d_ff_4_q));  // open: Qn, preset, en, reset
  Counter #(.width(32), .max('hffffffff), .ongoal("wrap"), .trigger("rising"), .behavior("new")) counter_5 (
    .Q(COUNT4), .clk(CLK), .clr(d_ff_5_q));  // open: load, D, count, carry, preset, down
  D_Flip_Flop #(.trigger("rising"), .Pre_Clr_Positions("LEGACY"), .NegatePresetClear("false"), .enable("true"), .NewFFLayout("false")) d_ff_5 (
    .clk(CLK), .D(or_5_out), .Q(d_ff_5_q));  // open: Qn, preset, en, reset
  Counter #(.width(32), .max('hffffffff), .ongoal("wrap"), .trigger("rising"), .behavior("new")) counter_6 (
    .Q(COUNT5), .clk(CLK), .clr(d_ff_6_q));  // open: load, D, count, carry, preset, down
  D_Flip_Flop #(.trigger("rising"), .Pre_Clr_Positions("LEGACY"), .NegatePresetClear("false"), .enable("true"), .NewFFLayout("false")) d_ff_6 (
    .clk(CLK), .D(or_6_out), .Q(d_ff_6_q));  // open: Qn, preset, en, reset
  Counter #(.width(32), .max('hffffffff), .ongoal("wrap"), .trigger("rising"), .behavior("new")) counter_7 (
    .Q(COUNT6), .clk(CLK), .clr(d_ff_7_q));  // open: load, D, count, carry, preset, down
  D_Flip_Flop #(.trigger("rising"), .Pre_Clr_Positions("LEGACY"), .NegatePresetClear("false"), .enable("true"), .NewFFLayout("false")) d_ff_7 (
    .clk(CLK), .D(or_7_out), .Q(d_ff_7_q));  // open: Qn, preset, en, reset
  Counter #(.width(32), .max('hffffffff), .ongoal("wrap"), .trigger("rising"), .behavior("new")) counter_8 (
    .Q(COUNT7), .clk(CLK), .clr(d_ff_8_q));  // open: load, D, count, carry, preset, down
  D_Flip_Flop #(.trigger("rising"), .Pre_Clr_Positions("LEGACY"), .NegatePresetClear("false"), .enable("true"), .NewFFLayout("false")) d_ff_8 (
    .clk(CLK), .D(or_8_out), .Q(d_ff_8_q));  // open: Qn, preset, en, reset
  Comparator #(.width(32), .mode("twosComplement")) comparator_1 (
    .a(CUR0), .b(EX_PC), .eq(comparator_1_eq));  // open: gt, lt
  Comparator #(.width(32), .mode("twosComplement")) comparator_2 (
    .a(CUR1), .b(EX_PC), .eq(comparator_2_eq));  // open: gt, lt
  Comparator #(.width(32), .mode("twosComplement")) comparator_3 (
    .a(CUR2), .b(EX_PC), .eq(comparator_3_eq));  // open: gt, lt
  Comparator #(.width(32), .mode("twosComplement")) comparator_4 (
    .a(CUR3), .b(EX_PC), .eq(comparator_4_eq));  // open: gt, lt
  Comparator #(.width(32), .mode("twosComplement")) comparator_5 (
    .a(CUR4), .b(EX_PC), .eq(comparator_5_eq));  // open: gt, lt
  Comparator #(.width(32), .mode("twosComplement")) comparator_6 (
    .a(CUR5), .b(EX_PC), .eq(comparator_6_eq));  // open: gt, lt
  Comparator #(.width(32), .mode("twosComplement")) comparator_7 (
    .a(CUR6), .b(EX_PC), .eq(comparator_7_eq));  // open: gt, lt
  Comparator #(.width(32), .mode("twosComplement")) comparator_8 (
    .a(CUR7), .b(EX_PC), .eq(comparator_8_eq));  // open: gt, lt
  or or_9 (EX_HIT, H0, H1, H2, H3, H4, H5, H6, H7);
  not not_1 (EX_MISS, EX_HIT);
  and and_9 (H0, comparator_1_eq, V0);
  and and_10 (H1, comparator_2_eq, V1);
  and and_11 (H2, comparator_3_eq, V2);
  and and_12 (H3, comparator_4_eq, V3);
  and and_13 (H4, comparator_5_eq, V4);
  and and_14 (H5, comparator_6_eq, V5);
  and and_15 (H6, comparator_7_eq, V6);
  and and_16 (H7, comparator_8_eq, V7);
  not not_2 (not_2_out, V0);
  not not_3 (not_3_out, V1);
  not not_4 (not_4_out, V2);
  not not_5 (not_5_out, V3);
  not not_6 (not_6_out, V4);
  not not_7 (not_7_out, V5);
  not not_8 (not_8_out, V6);
  not not_9 (not_9_out, V7);
  compare compare_1 (
    .X(COUNT0), .Y(COUNT1), .X_PLACE(3'b000), .Y_PLACE(3'b001), .MAX(compare_1_max),
    .MAX_PLACE(compare_1_max_place));
  compare compare_2 (
    .X(COUNT2), .Y(COUNT3), .X_PLACE(3'b010), .Y_PLACE(3'b011), .MAX(compare_2_max),
    .MAX_PLACE(compare_2_max_place));
  compare compare_3 (
    .X(COUNT4), .Y(COUNT5), .X_PLACE(3'b100), .Y_PLACE(3'b101), .MAX(compare_3_max),
    .MAX_PLACE(compare_3_max_place));
  compare compare_4 (
    .X(COUNT6), .Y(COUNT7), .X_PLACE(3'b110), .Y_PLACE(3'b111), .MAX(compare_4_max),
    .MAX_PLACE(compare_4_max_place));
  Multiplexer #(.select(3), .width(2), .disabled("Z"), .enable("false")) multiplexer_9 (
    .in0(P0), .in1(P1), .in2(P2), .in3(P3), .in4(P4), .in5(P5), .in6(P6), .in7(P7), .out(multiplexer_9_out),
    .sel(priority_encoder_1_out));
  Priority_Encoder #(.select(3), .disabled("Z")) priority_encoder_1 (
    .in0(H0), .in1(H1), .in2(H2), .in3(H3), .in4(H4), .in5(H5), .in6(H6), .in7(H7),
    .out(priority_encoder_1_out));  // open: gs, en_out, en_in
  Priority_Encoder #(.select(3), .disabled("Z")) priority_encoder_2 (
    .in0(not_2_out), .in1(not_3_out), .in2(not_4_out), .in3(not_5_out), .in4(not_6_out), .in5(not_7_out),
    .in6(not_8_out), .in7(not_9_out), .out(priority_encoder_2_out), .gs(priority_encoder_2_gs));  // open: en_out, en_in
  not not_10 (not_10_out, priority_encoder_2_gs);
  compare compare_5 (
    .X(compare_1_max), .Y(compare_2_max), .X_PLACE(compare_1_max_place), .Y_PLACE(compare_2_max_place),
    .MAX(compare_5_max), .MAX_PLACE(compare_5_max_place));
  compare compare_6 (
    .X(compare_3_max), .Y(compare_4_max), .X_PLACE(compare_3_max_place), .Y_PLACE(compare_4_max_place),
    .MAX(compare_6_max), .MAX_PLACE(compare_6_max_place));
  Multiplexer #(.select(1), .width(3), .disabled("Z"), .enable("false")) multiplexer_10 (
    .in0(3'b000), .in1(priority_encoder_2_out), .out(multiplexer_10_out), .sel(priority_encoder_2_gs));
  Multiplexer #(.select(3), .width(2), .disabled("Z"), .enable("false")) multiplexer_11 (
    .in0(2'b00), .in1(2'b00), .in2(2'b01), .in3(2'b10), .in4(2'b01), .in5(2'b10), .in6(2'b11), .in7(2'b11),
    .out(PNEXT), .sel({EX_BRANCHTAKEN, multiplexer_9_out}));
  Demultiplexer #(.select(3), .width(1), .tristate("false"), .disabled("Z"), .enable("true")) demultiplexer_1 (
    .out0(demultiplexer_1_out0), .out1(demultiplexer_1_out1), .out2(demultiplexer_1_out2),
    .out3(demultiplexer_1_out3), .out4(demultiplexer_1_out4), .out5(demultiplexer_1_out5),
    .out6(demultiplexer_1_out6), .out7(demultiplexer_1_out7), .in(priority_encoder_2_gs),
    .sel(multiplexer_10_out));  // open: en
  Demultiplexer #(.select(3), .width(1), .tristate("false"), .disabled("Z"), .enable("false")) demultiplexer_2 (
    .out0(demultiplexer_2_out0), .out1(demultiplexer_2_out1), .out2(demultiplexer_2_out2),
    .out3(demultiplexer_2_out3), .out4(demultiplexer_2_out4), .out5(demultiplexer_2_out5),
    .out6(demultiplexer_2_out6), .out7(demultiplexer_2_out7), .in(not_10_out), .sel(compare_7_max_place));
  compare compare_7 (
    .X(compare_5_max), .Y(compare_6_max), .X_PLACE(compare_5_max_place), .Y_PLACE(compare_6_max_place),
    .MAX_PLACE(compare_7_max_place));  // open: MAX
  or or_10 (or_10_out, demultiplexer_1_out0, demultiplexer_2_out0);
  or or_11 (or_11_out, demultiplexer_1_out1, demultiplexer_2_out1);
  or or_12 (or_12_out, demultiplexer_1_out2, demultiplexer_2_out2);
  or or_13 (or_13_out, demultiplexer_1_out3, demultiplexer_2_out3);
  or or_14 (or_14_out, demultiplexer_1_out4, demultiplexer_2_out4);
  or or_15 (or_15_out, demultiplexer_1_out5, demultiplexer_2_out5);
  or or_16 (or_16_out, demultiplexer_1_out6, demultiplexer_2_out6);
  or or_17 (or_17_out, demultiplexer_1_out7, demultiplexer_2_out7);
  and and_17 (W0, or_10_out, EX_MISS, EX_BRANCHTAKEN);
  and and_18 (W1, or_11_out, EX_MISS, EX_BRANCHTAKEN);
  and and_19 (W2, or_12_out, EX_MISS, EX_BRANCHTAKEN);
  and and_20 (W3, or_13_out, EX_MISS, EX_BRANCHTAKEN);
  and and_21 (W4, or_14_out, EX_MISS, EX_BRANCHTAKEN);
  and and_22 (W5, or_15_out, EX_MISS, EX_BRANCHTAKEN);
  and and_23 (W6, or_16_out, EX_MISS, EX_BRANCHTAKEN);
  and and_24 (W7, or_17_out, EX_MISS, EX_BRANCHTAKEN);
  Comparator #(.width(32), .mode("twosComplement")) comparator_9 (
    .a(CUR0), .b(PC), .eq(comparator_9_eq));  // open: gt, lt
  Comparator #(.width(32), .mode("twosComplement")) comparator_10 (
    .a(CUR1), .b(PC), .eq(comparator_10_eq));  // open: gt, lt
  Comparator #(.width(32), .mode("twosComplement")) comparator_11 (
    .a(CUR2), .b(PC), .eq(comparator_11_eq));  // open: gt, lt
  Comparator #(.width(32), .mode("twosComplement")) comparator_12 (
    .a(CUR3), .b(PC), .eq(comparator_12_eq));  // open: gt, lt
  Comparator #(.width(32), .mode("twosComplement")) comparator_13 (
    .a(CUR4), .b(PC), .eq(comparator_13_eq));  // open: gt, lt
  Comparator #(.width(32), .mode("twosComplement")) comparator_14 (
    .a(CUR5), .b(PC), .eq(comparator_14_eq));  // open: gt, lt
  Comparator #(.width(32), .mode("twosComplement")) comparator_15 (
    .a(CUR6), .b(PC), .eq(comparator_15_eq));  // open: gt, lt
  Comparator #(.width(32), .mode("twosComplement")) comparator_16 (
    .a(CUR7), .b(PC), .eq(comparator_16_eq));  // open: gt, lt
  and and_25 (and_25_out, comparator_9_eq, V0);
  and and_26 (and_26_out, comparator_10_eq, V1);
  and and_27 (and_27_out, comparator_11_eq, V2);
  and and_28 (and_28_out, comparator_12_eq, V3);
  and and_29 (and_29_out, comparator_13_eq, V4);
  and and_30 (and_30_out, comparator_14_eq, V5);
  and and_31 (and_31_out, comparator_15_eq, V6);
  and and_32 (and_32_out, comparator_16_eq, V7);
  assign {PREDICTJUMP, controlled_buffer_1_out[0]} = and_25_out ? P0 : 2'bz;  // Controlled_Buffer controlled_buffer_1
  assign {PREDICTJUMP, controlled_buffer_1_out[0]} = and_26_out ? P1 : 2'bz;  // Controlled_Buffer controlled_buffer_2
  assign {PREDICTJUMP, controlled_buffer_1_out[0]} = and_27_out ? P2 : 2'bz;  // Controlled_Buffer controlled_buffer_3
  assign {PREDICTJUMP, controlled_buffer_1_out[0]} = and_28_out ? P3 : 2'bz;  // Controlled_Buffer controlled_buffer_4
  assign {PREDICTJUMP, controlled_buffer_1_out[0]} = and_29_out ? P4 : 2'bz;  // Controlled_Buffer controlled_buffer_5
  assign {PREDICTJUMP, controlled_buffer_1_out[0]} = and_30_out ? P5 : 2'bz;  // Controlled_Buffer controlled_buffer_6
  assign {PREDICTJUMP, controlled_buffer_1_out[0]} = and_31_out ? P6 : 2'bz;  // Controlled_Buffer controlled_buffer_7
  assign {PREDICTJUMP, controlled_buffer_1_out[0]} = and_32_out ? P7 : 2'bz;  // Controlled_Buffer controlled_buffer_8
  Pull_Resistor #(.pull(0)) pull_resistor_1 (.node({PREDICTJUMP, controlled_buffer_1_out[0]}));
  assign PREDICTADDR = and_25_out ? NEXT0 : 32'bz;  // Controlled_Buffer controlled_buffer_9
  assign PREDICTADDR = and_26_out ? NEXT1 : 32'bz;  // Controlled_Buffer controlled_buffer_10
  assign PREDICTADDR = and_27_out ? NEXT2 : 32'bz;  // Controlled_Buffer controlled_buffer_11
  assign PREDICTADDR = and_28_out ? NEXT3 : 32'bz;  // Controlled_Buffer controlled_buffer_12
  assign PREDICTADDR = and_29_out ? NEXT4 : 32'bz;  // Controlled_Buffer controlled_buffer_13
  assign PREDICTADDR = and_30_out ? NEXT5 : 32'bz;  // Controlled_Buffer controlled_buffer_14
  assign PREDICTADDR = and_31_out ? NEXT6 : 32'bz;  // Controlled_Buffer controlled_buffer_15
  assign PREDICTADDR = and_32_out ? NEXT7 : 32'bz;  // Controlled_Buffer controlled_buffer_16
  Pull_Resistor #(.pull(0)) pull_resistor_2 (.node(PREDICTADDR));

  // Other names for the same wires on the sheet: Branch = EX_BRANCHTAKEN; B_Instruction = EX_BRANCH;
  //   PREDICTADDRl[31:0] = PREDICTADDR

  // Notes on the sheet:
  //   VALID
  //   分支指令地址
  //   分支目标地址
  //   状态机
  //   计时器
  //   状态机更新
  //   选择一个位置写入该分支信息
  //   IF段预测逻辑
  //   预测结果
endmodule

module compare (
  input  [31:0] X,
  input  [31:0] Y,
  input  [2:0] X_PLACE,
  input  [2:0] Y_PLACE,
  output [31:0] MAX,
  output [2:0] MAX_PLACE
);

  wire comparator_1_lt;

  Comparator #(.width(32), .mode("twosComplement")) comparator_1 (.a(X), .b(Y), .lt(comparator_1_lt));  // open: gt, eq
  Multiplexer #(.select(1), .width(32), .disabled("Z"), .enable("false")) multiplexer_1 (
    .in0(X), .in1(Y), .out(MAX), .sel(comparator_1_lt));
  Multiplexer #(.select(1), .width(3), .disabled("Z"), .enable("false")) multiplexer_2 (
    .in0(X_PLACE), .in1(Y_PLACE), .out(MAX_PLACE), .sel(comparator_1_lt));
endmodule
